// Logisim project Computer8Bit.circ as structural Verilog: 18 circuits, main circuit main
module main (
);

  wire C1, C2, C3, C4, CSPC_DIR, FLAGS_MODE_SEL0, FLAGS_MODE_SEL1, flagscontroller_1_flags_in_sel,
       flagscontroller_1_not_czn_in, flagscontroller_1_not_i_in, I_VAL, J, JA, JC, JN, JZ, keyboard_1_avail,
       keyboardadapter_1_k_clear, keyboardadapter_1_k_clk, keyboardadapter_1_k_read_en, not_1_out, not_2_out,
       not_3_out, not_4_out, not_5_out, not_6_out, not_7_out, not_8_out, not_9_out, not_10_out, not_11_out,
       not_12_out, not_13_out, not_14_out, NOT_ABH_IN, NOT_ABL_IN, NOT_CS_IN, NOT_CS_OUT, NOT_DATA_LATCH_OUT,
       NOT_DEVICE_IN, NOT_DEVICE_OUT, NOT_DEVICE_SEL_0, NOT_DEVICE_SEL_1, NOT_DEVICE_SEL_2, NOT_DEVICE_SEL_3,
       NOT_DEVICE_SEL_4, NOT_DEVICE_SEL_5, NOT_DEVICE_SEL_RAM, NOT_DEVICE_SEL_ROM, NOT_FETCH, NOT_FLAGS_OUT,
       NOT_HLT, NOT_IRQ, NOT_IVH_OUT, NOT_IVL_OUT, NOT_PASS, NOT_PC_IN, NOT_PC_INC, NOT_PC_OUT, NOT_POP,
       NOT_PUSH, NOT_RA_OUT, NOT_RB_IN, NOT_RB_OUT, NOT_RC_IN, NOT_RC_OUT, NOT_RD_IN, NOT_RD_OUT, NOT_RT_IN,
       NOT_RT_OUT, NOT_SP_CT, NOT_SP_IN, NOT_SP_OUT, NOT_SS_IN, NOT_SS_OUT, OP_SEL0, OP_SEL1, OP_SEL2,
       or_1_out, or_2_out, or_3_out, or_4_out, or_5_out, or_6_out, or_7_out, or_8_out, or_9_out, PAGE_0,
       RA_S0, RA_S1, RESET, SP_DIR, switch_1_p2, ttyadapter_1_tty_we, X_SEL0, X_SEL1, Y_SEL0, Y_SEL1, Y_SEL2;
  wire [2:0] alu_1_flags;
  wire [3:0] FLAGS_VAL;
  wire [6:0] bit_extender_1_out, keyboard_1_data;
  wire [7:0] ABH_q, ABL_q, aluoperandselector_1_o1, aluoperandselector_1_o2, aluoperatorselector_1_op_out,
       bufferedregister_1_async_out, controlunit_1_ir_out, DBUS, DL_VAL, FBUS, keyboardadapter_1_async_out,
       multiplexer_1_out, RA_VAL, RB_VAL, RC_VAL, RD_VAL, SP_VAL, SS_VAL, undriven, undriven_2, undriven_3;
  wire [15:0] ABUS, CS_PC;

  // Probe on controlunit_1_ir_out
  // Probe on CS_PC
  // Probe on ABUS
  // Probe on DBUS
  // Probe on RA_VAL
  // Probe on RB_VAL
  // Probe on RC_VAL
  // Probe on RD_VAL
  // Probe on DL_VAL
  // Probe on SS_VAL
  // Probe on SP_VAL
  // Probe on FLAGS_VAL
  // DipSwitch dipswitch_1: pin names not known
  assign DBUS = switch_1_p2 ? undriven : 8'bz;  // Controlled_Buffer controlled_buffer_1
  // Switch switch_1: pin names not known; wires that end beside it: 1'b1, switch_1_p2
  Pull_Resistor pull_resistor_1 (.node(switch_1_p2));
  Hex_Digit_Display hex_digit_display_1 (.value(DBUS[7:4]));  // open: dp
  Hex_Digit_Display hex_digit_display_2 (.value(DBUS[3:0]));  // open: dp
  ControlUnit controlunit_1 (
    .DATA_LATCH(DL_VAL), .NOT_IRQ(NOT_IRQ), .CLK90(C1), .RESET(RESET), .I(FLAGS_VAL[3]),
    .IR_OUT(controlunit_1_ir_out), .RA_S0(RA_S0), .RA_S1(RA_S1), .NOT_RA_OUT(NOT_RA_OUT),
    .NOT_RB_IN(NOT_RB_IN), .NOT_RB_OUT(NOT_RB_OUT), .NOT_RC_IN(NOT_RC_IN), .NOT_RC_OUT(NOT_RC_OUT),
    .NOT_RD_IN(NOT_RD_IN), .NOT_RD_OUT(NOT_RD_OUT), .NOT_DEVICE_IN(NOT_DEVICE_IN),
    .NOT_DEVICE_OUT(NOT_DEVICE_OUT), .NOT_SS_IN(NOT_SS_IN), .NOT_SS_OUT(NOT_SS_OUT), .NOT_SP_IN(NOT_SP_IN),
    .NOT_SP_OUT(NOT_SP_OUT), .NOT_SP_CT(NOT_SP_CT), .SP_DIR(SP_DIR), .NOT_ABH_IN(NOT_ABH_IN),
    .NOT_ABL_IN(NOT_ABL_IN), .NOT_RT_IN(NOT_RT_IN), .NOT_RT_OUT(NOT_RT_OUT), .X_SEL0(X_SEL0),
    .X_SEL1(X_SEL1), .Y_SEL0(Y_SEL0), .Y_SEL1(Y_SEL1), .Y_SEL2(Y_SEL2), .OP_SEL0(OP_SEL0), .OP_SEL1(OP_SEL1),
    .OP_SEL2(OP_SEL2), .NOT_CS_IN(NOT_CS_IN), .NOT_PC_IN(NOT_PC_IN), .NOT_PC_INC(NOT_PC_INC),
    .NOT_CS_OUT(NOT_CS_OUT), .NOT_PC_OUT(NOT_PC_OUT), .NOT_FETCH(NOT_FETCH), .J(J), .JC(JC), .JZ(JZ),
    .JN(JN), .JA(JA), .NOT_PASS(NOT_PASS), .NOT_HLT(NOT_HLT), .PAGE_0(PAGE_0), .NOT_PUSH(NOT_PUSH),
    .NOT_POP(NOT_POP), .NOT_DATA_LATCH_OUT(NOT_DATA_LATCH_OUT), .NOT_IVH_OUT(NOT_IVH_OUT),
    .NOT_IVL_OUT(NOT_IVL_OUT), .I_VAL(I_VAL), .FLAGS_MODE_SEL0(FLAGS_MODE_SEL0),
    .FLAGS_MODE_SEL1(FLAGS_MODE_SEL1), .NOT_FLAGS_OUT(NOT_FLAGS_OUT), .CSPC_DIR(CSPC_DIR));
  LED led_1 (.in(RA_S0));
  LED led_2 (.in(RA_S1));
  LED led_3 (.in(NOT_RA_OUT));
  LED led_4 (.in(NOT_RB_IN));
  LED led_5 (.in(NOT_RB_OUT));
  LED led_6 (.in(NOT_RC_IN));
  LED led_7 (.in(NOT_RC_OUT));
  LED led_8 (.in(NOT_RD_IN));
  LED led_9 (.in(NOT_RD_OUT));
  LED led_10 (.in(NOT_DEVICE_IN));
  LED led_11 (.in(NOT_DEVICE_OUT));
  LED led_12 (.in(NOT_SS_IN));
  LED led_13 (.in(NOT_SS_OUT));
  LED led_14 (.in(NOT_SP_IN));
  LED led_15 (.in(NOT_SP_OUT));
  LED led_16 (.in(NOT_SP_CT));
  LED led_17 (.in(SP_DIR));
  LED led_18 (.in(NOT_ABH_IN));
  LED led_19 (.in(NOT_ABL_IN));
  LED led_20 (.in(NOT_RT_IN));
  LED led_21 (.in(NOT_RT_OUT));
  LED led_22 (.in(X_SEL0));
  LED led_23 (.in(X_SEL1));
  LED led_24 (.in(Y_SEL0));
  LED led_25 (.in(Y_SEL1));
  LED led_26 (.in(Y_SEL2));
  LED led_27 (.in(OP_SEL0));
  LED led_28 (.in(OP_SEL1));
  LED led_29 (.in(OP_SEL2));
  LED led_30 (.in(NOT_CS_IN));
  LED led_31 (.in(NOT_PC_IN));
  LED led_32 (.in(NOT_PC_INC));
  LED led_33 (.in(NOT_CS_OUT));
  LED led_34 (.in(NOT_PC_OUT));
  LED led_35 (.in(NOT_FETCH));
  LED led_36 (.in(J));
  LED led_37 (.in(JC));
  LED led_38 (.in(JZ));
  LED led_39 (.in(JN));
  LED led_40 (.in(JA));
  LED led_41 (.in(NOT_PASS));
  LED led_42 (.in(NOT_HLT));
  LED led_43 (.in(PAGE_0));
  LED led_44 (.in(NOT_PUSH));
  LED led_45 (.in(NOT_POP));
  LED led_46 (.in(NOT_DATA_LATCH_OUT));
  LED led_47 (.in(NOT_IVH_OUT));
  LED led_48 (.in(NOT_IVL_OUT));
  LED led_49 (.in(I_VAL));
  LED led_50 (.in(FLAGS_MODE_SEL0));
  LED led_51 (.in(FLAGS_MODE_SEL1));
  LED led_52 (.in(NOT_FLAGS_OUT));
  LED led_53 (.in(CSPC_DIR));
  Pull_Resistor #(.pull(1)) pull_resistor_2 (.node(NOT_IRQ));
  or or_1 (or_1_out, NOT_DEVICE_SEL_0, NOT_DEVICE_IN);
  or or_2 (or_2_out, NOT_DEVICE_SEL_0, NOT_DEVICE_OUT);
  Keyboard keyboard_1 (
    .clk(keyboardadapter_1_k_clk), .re(keyboardadapter_1_k_read_en), .clr(keyboardadapter_1_k_clear),
    .avail(keyboard_1_avail), .data(keyboard_1_data));
  Hex_Digit_Display hex_digit_display_3 (.value(ABUS[15:12]));  // open: dp
  Hex_Digit_Display hex_digit_display_4 (.value(ABUS[11:8]));  // open: dp
  or or_3 (or_3_out, NOT_FETCH, NOT_DEVICE_SEL_0);
  Hex_Digit_Display hex_digit_display_5 (.value(ABUS[7:4]));  // open: dp
  Hex_Digit_Display hex_digit_display_6 (.value(ABUS[3:0]));  // open: dp
  KeyboardAdapter keyboardadapter_1 (
    .K_AVAIL(keyboard_1_avail), .K_DATA(keyboard_1_data), .BUS_IN(DBUS), .ABUS(ABUS),
    .NOT_DEVICE_IN(or_1_out), .NOT_DEVICE_OUT(or_2_out), .CLK(C4), .NOT_IRQ(NOT_IRQ),
    .ASYNC_OUT(keyboardadapter_1_async_out), .K_READ_EN(keyboardadapter_1_k_read_en),
    .K_CLEAR(keyboardadapter_1_k_clear), .K_CLK(keyboardadapter_1_k_clk));
  not not_1 (not_1_out, or_3_out);
  assign FBUS = not_1_out ? keyboardadapter_1_async_out : 8'bz;  // Controlled_Buffer controlled_buffer_2
  assign DBUS = not_2_out ? keyboardadapter_1_async_out : 8'bz;  // Controlled_Buffer controlled_buffer_3
  not not_2 (not_2_out, or_2_out);
  Pull_Resistor pull_resistor_3 (.node(RESET));
  // Switch RESET: pin names not known; wires that end beside it: 1'b1, RESET
  not not_3 (not_3_out, NOT_ABH_IN);
  Register ABH (.D(DBUS), .en(not_3_out), .clk(C4), .Q(ABH_q));  // open: clr
  Register ABL (.D(DBUS), .en(not_4_out), .clk(C4), .Q(ABL_q));  // open: clr
  not not_4 (not_4_out, NOT_ABL_IN);
  Multiplexer #(.width(8)) multiplexer_1 (.in0(ABH_q), .in1(8'h20), .out(multiplexer_1_out), .sel(PAGE_0));
  or or_4 (or_4_out, NOT_DEVICE_SEL_1, NOT_DEVICE_IN);
  or or_5 (or_5_out, NOT_DEVICE_SEL_1, NOT_DEVICE_OUT);
  Bit_Extender #(.out_width(7)) bit_extender_1 (.in(DBUS), .out(bit_extender_1_out));
  TTY #(.cols(56)) tty_1 (.data(bit_extender_1_out), .clk(C4), .we(ttyadapter_1_tty_we));  // open: clr
  Register SS (.D(DBUS), .en(not_5_out), .clk(C4), .Q(SS_VAL), .clr(1'b0));
  not not_5 (not_5_out, NOT_SS_IN);
  or or_6 (or_6_out, NOT_FETCH, NOT_DEVICE_SEL_1);
  AddrDecoder addrdecoder_1 (
    .ABUS(ABUS), .NOT_DEVICE_SEL_ROM(NOT_DEVICE_SEL_ROM), .NOT_DEVICE_SEL_RAM(NOT_DEVICE_SEL_RAM),
    .NOT_DEVICE_SEL_0(NOT_DEVICE_SEL_0), .NOT_DEVICE_SEL_1(NOT_DEVICE_SEL_1),
    .NOT_DEVICE_SEL_2(NOT_DEVICE_SEL_2), .NOT_DEVICE_SEL_3(NOT_DEVICE_SEL_3),
    .NOT_DEVICE_SEL_4(NOT_DEVICE_SEL_4), .NOT_DEVICE_SEL_5(NOT_DEVICE_SEL_5));
  StackPointer SP (.NOT_SP_IN(NOT_SP_IN), .SP_DIR(SP_DIR), .NOT_SP_CT(NOT_SP_CT), .CLK(C3), .SP_OUT(SP_VAL));
  Multiplexer #(.width(16)) multiplexer_2 (.in0({multiplexer_1_out, ABL_q}), .in1(CS_PC), .out(ABUS), .sel(C1));
  CodeSegment_ProgramCounter codesegment_programcounter_1 (
    .FLAGS(FLAGS_VAL), .J(J), .JC(JC), .JZ(JZ), .JN(JN), .JA(JA), .NOT_PC_IN(NOT_PC_IN),
    .NOT_CS_IN(NOT_CS_IN), .NOT_PC_INC(NOT_PC_INC), .RESET(RESET), .ABUS({multiplexer_1_out, ABL_q}),
    .CLK(C3), .NOT_PC_OUT(NOT_PC_OUT), .NOT_CS_OUT(NOT_CS_OUT), .CSPC_DIR(CSPC_DIR), .CS_PC(CS_PC),
    .BUS_OUT(DBUS));
  TTYAdapter ttyadapter_1 (
    .DBUS_IN(DBUS), .ABUS(ABUS), .NOT_DEVICE_IN(or_4_out), .NOT_DEVICE_OUT(or_5_out), .CLK(C4),
    .TTY_WE(ttyadapter_1_tty_we));  // open: TTY_DATA, TTY_CLR
  not not_6 (not_6_out, or_6_out);
  assign FBUS = not_6_out ? undriven_2 : 8'bz;  // Controlled_Buffer controlled_buffer_4
  assign DBUS = not_7_out ? undriven_2 : 8'bz;  // Controlled_Buffer controlled_buffer_5
  not not_7 (not_7_out, or_5_out);
  Register DATA_LATCH (.D(FBUS), .en(not_8_out), .clk(C2), .Q(DL_VAL), .clr(RESET));
  not not_8 (not_8_out, NOT_FETCH);
  not not_9 (not_9_out, NOT_DATA_LATCH_OUT);
  assign DBUS = not_9_out ? DL_VAL : 8'bz;  // Controlled_Buffer controlled_buffer_6
  BufferedRegister bufferedregister_1 (
    .BUS_IN(DBUS), .CLK(C4), .NOT_R_IN(NOT_RT_IN), .NOT_R_OUT(NOT_RT_OUT),
    .ASYNC_OUT(bufferedregister_1_async_out), .BUS_OUT(DBUS));
  or or_7 (or_7_out, NOT_DEVICE_SEL_2, NOT_DEVICE_IN);
  or or_8 (or_8_out, NOT_DEVICE_SEL_2, NOT_DEVICE_OUT);
  ClockModule clockmodule_1 (.NOT_HLT(NOT_HLT), .C2(C2), .C1(C1), .C4(C4), .C3(C3));
  RAMModule rammodule_1 (
    .NOT_PUSH(NOT_PUSH), .NOT_DEVICE_IN(NOT_DEVICE_IN), .NOT_DEVICE_SEL_RAM(NOT_DEVICE_SEL_RAM), .SP(SP_VAL),
    .NOT_DEVICE_OUT(NOT_DEVICE_OUT), .NOT_POP(NOT_POP), .CLK(C4), .SS(SS_VAL), .ABUS(ABUS), .BUS_IN(DBUS),
    .NOT_FETCH(NOT_FETCH), .DBUS_OUT(DBUS), .FBUS_OUT(FBUS));
  ROMModule rommodule_1 (
    .ABUS(ABUS), .NOT_DEVICE_SEL_ROM(NOT_DEVICE_SEL_ROM), .NOT_DEVICE_OUT(NOT_DEVICE_OUT),
    .NOT_FETCH(NOT_FETCH), .DBUS_OUT(DBUS), .FBUS_OUT(FBUS));
  not not_10 (not_10_out, NOT_IVL_OUT);
  assign DBUS = not_10_out ? {8{1'b0}} : 8'bz;  // Controlled_Buffer controlled_buffer_7
  assign DBUS = not_11_out ? 8'h1f : 8'bz;  // Controlled_Buffer controlled_buffer_8
  not not_11 (not_11_out, NOT_IVH_OUT);
  or or_9 (or_9_out, NOT_FETCH, NOT_DEVICE_SEL_2);
  not not_12 (not_12_out, or_9_out);
  assign FBUS = not_12_out ? undriven_3 : 8'bz;  // Controlled_Buffer controlled_buffer_9
  assign DBUS = not_13_out ? undriven_3 : 8'bz;  // Controlled_Buffer controlled_buffer_10
  not not_13 (not_13_out, or_8_out);
  BufferedRegister RC (
    .BUS_IN(DBUS), .CLK(C4), .NOT_R_IN(NOT_RC_IN), .NOT_R_OUT(NOT_RC_OUT), .ASYNC_OUT(RC_VAL), .BUS_OUT(DBUS));
  Hex_Digit_Display hex_digit_display_7 (.value(RC_VAL[7:4]));  // open: dp
  ShiftRegister RA (
    .S0(RA_S0), .S1(RA_S1), .CLK(C4), .BUS_IN(DBUS), .NOT_OE(NOT_RA_OUT), .ASYNC_OUT(RA_VAL), .BUS_OUT(DBUS));
  Hex_Digit_Display hex_digit_display_8 (.value(RA_VAL[7:4]));  // open: dp
  Hex_Digit_Display hex_digit_display_9 (.value(RC_VAL[3:0]));  // open: dp
  Hex_Digit_Display hex_digit_display_10 (.value(RA_VAL[3:0]));  // open: dp
  ALUOperandSelector aluoperandselector_1 (
    .X_SEL0(X_SEL0), .X_SEL1(X_SEL1), .Y_SEL0(Y_SEL0), .Y_SEL1(Y_SEL1), .Y_SEL2(Y_SEL2), .A_ASYNC(RA_VAL),
    .B_ASYNC(RB_VAL), .C_ASYNC(RC_VAL), .D_ASYNC(RD_VAL), .E_ASYNC(bufferedregister_1_async_out),
    .F_ASYNC(8'h1), .O1(aluoperandselector_1_o1), .O2(aluoperandselector_1_o2));
  FLAGSController flagscontroller_1 (
    .FLAGS_MODE_SEL0(FLAGS_MODE_SEL0), .FLAGS_MODE_SEL1(FLAGS_MODE_SEL1),
    .NOT_CZN_IN(flagscontroller_1_not_czn_in), .NOT_I_IN(flagscontroller_1_not_i_in),
    .FLAGS_IN_SEL(flagscontroller_1_flags_in_sel));
  BufferedRegister RB (
    .BUS_IN(DBUS), .CLK(C4), .NOT_R_IN(NOT_RB_IN), .NOT_R_OUT(NOT_RB_OUT), .ASYNC_OUT(RB_VAL), .BUS_OUT(DBUS));
  BufferedRegister RD (
    .BUS_IN(DBUS), .CLK(C4), .NOT_R_IN(NOT_RD_IN), .NOT_R_OUT(NOT_RD_OUT), .ASYNC_OUT(RD_VAL), .BUS_OUT(DBUS));
  Hex_Digit_Display hex_digit_display_11 (.value(RD_VAL[7:4]));  // open: dp
  Hex_Digit_Display hex_digit_display_12 (.value(RD_VAL[3:0]));  // open: dp
  Hex_Digit_Display hex_digit_display_13 (.value(RB_VAL[7:4]));  // open: dp
  Hex_Digit_Display hex_digit_display_14 (.value(RB_VAL[3:0]));  // open: dp
  ALUOperatorSelector aluoperatorselector_1 (
    .OP_SEL0(OP_SEL0), .OP_SEL1(OP_SEL1), .OP_SEL2(OP_SEL2), .OP_OUT(aluoperatorselector_1_op_out));
  ALU alu_1 (
    .OPERATORS(aluoperatorselector_1_op_out), .O1(aluoperandselector_1_o1), .O2(aluoperandselector_1_o2),
    .BUS_OUT(DBUS), .FLAGS(alu_1_flags));
  FLAGSRegister flagsregister_1 (
    .BUS_IN(DBUS), .I_VAL(I_VAL), .ALU_FLAGS(alu_1_flags), .NOT_CZN_IN(flagscontroller_1_not_czn_in),
    .NOT_I_IN(flagscontroller_1_not_i_in), .FLAGS_IN_SEL(flagscontroller_1_flags_in_sel), .CLK(C4),
    .FLAGS_OUT(FLAGS_VAL));
  LED led_54 (.in(FLAGS_VAL[3]));
  LED led_55 (.in(FLAGS_VAL[2]));
  LED led_56 (.in(FLAGS_VAL[1]));
  LED led_57 (.in(FLAGS_VAL[0]));
  not not_14 (not_14_out, NOT_FLAGS_OUT);
  assign DBUS = not_14_out ? {4'b0000, FLAGS_VAL} : 8'bz;  // Controlled_Buffer controlled_buffer_11

  // Notes on the sheet:
  //   IR
  //   CS_PC
  //   ABUS
  //   DBUS
  //   RA
  //   RB
  //   RC
  //   RD
  //   DL
  //   SS
  //   SP
  //   INZC
  //   Write to bus
  //   Data bus
  //   Address bus
  //   1. control 2. fetch 3. PC increment 4. data
  //   ROM
  //   Clock
  //   RAM
  //   DATA_LATCH
  //   RT
  //   RC
  //   RA
  //   ALU_OPERAND_SELECTOR
  //   RD
  //   RB
  //   ALU_OPERATOR_SELECTOR
  //   I
  //   N
  //   Z
  //   C
endmodule

module ShiftRegister (
  input  S0,
  input  S1,
  input  CLK,
  input  [7:0] BUS_IN,
  input  NOT_OE,
  output [7:0] ASYNC_OUT,
  output [7:0] BUS_OUT
);

  wire not_1_out;

  not not_1 (not_1_out, NOT_OE);
  L_4_bit_bidir_univ_shift_register_sn74194 l_4_bit_bidir_univ_shift_register_sn74194_1 (
    .SL_SERIAL(ASYNC_OUT[3]), .DATA_IN(BUS_IN[7:4]), .SR_SERIAL(1'b0), .CLK(CLK), .NOT_CLR(1'b1), .S0(S0),
    .S1(S1), .DATA_OUT(ASYNC_OUT[7:4]));
  L_4_bit_bidir_univ_shift_register_sn74194 l_4_bit_bidir_univ_shift_register_sn74194_2 (
    .SL_SERIAL(1'b0), .DATA_IN(BUS_IN[3:0]), .SR_SERIAL(ASYNC_OUT[4]), .CLK(CLK), .NOT_CLR(1'b1), .S0(S0),
    .S1(S1), .DATA_OUT(ASYNC_OUT[3:0]));
  assign BUS_OUT = not_1_out ? ASYNC_OUT : 8'bz;  // Controlled_Buffer controlled_buffer_1
endmodule

module BufferedRegister (
  input  [7:0] BUS_IN,
  input  CLK,
  input  NOT_R_IN,
  input  NOT_R_OUT,
  output [7:0] ASYNC_OUT,
  output [7:0] BUS_OUT
);

  wire not_1_out, not_2_out;

  not not_1 (not_1_out, NOT_R_IN);
  not not_2 (not_2_out, NOT_R_OUT);
  Register register_1 (.D(BUS_IN), .en(not_1_out), .clk(CLK), .Q(ASYNC_OUT), .clr(1'b0));
  assign BUS_OUT = not_2_out ? ASYNC_OUT : 8'bz;  // Controlled_Buffer controlled_buffer_1
endmodule

module ALUOperandSelector (
  input  X_SEL0,
  input  X_SEL1,
  input  Y_SEL0,
  input  Y_SEL1,
  input  Y_SEL2,
  input  [7:0] A_ASYNC,
  input  [7:0] B_ASYNC,
  input  [7:0] C_ASYNC,
  input  [7:0] D_ASYNC,
  input  [7:0] E_ASYNC,
  input  [7:0] F_ASYNC,
  output [7:0] O1,
  output [7:0] O2
);

  wire decoder_1_out0, decoder_1_out1, decoder_1_out2, decoder_1_out3, decoder_2_out0, decoder_2_out1,
       decoder_2_out2, decoder_2_out3, decoder_2_out4, decoder_2_out5;

  Decoder #(.select(2)) decoder_1 (
    .out0(decoder_1_out0), .out1(decoder_1_out1), .out2(decoder_1_out2), .out3(decoder_1_out3),
    .sel({X_SEL1, X_SEL0}), .en(1'b1));
  Decoder #(.select(3)) decoder_2 (
    .out0(decoder_2_out0), .out1(decoder_2_out1), .out2(decoder_2_out2), .out3(decoder_2_out3),
    .out4(decoder_2_out4), .out5(decoder_2_out5), .sel({Y_SEL2, Y_SEL1, Y_SEL0}), .en(1'b1));  // open: out6, out7
  assign O1 = decoder_1_out0 ? A_ASYNC : 8'bz;  // Controlled_Buffer controlled_buffer_1
  assign O1 = decoder_1_out1 ? B_ASYNC : 8'bz;  // Controlled_Buffer controlled_buffer_2
  assign O1 = decoder_1_out2 ? C_ASYNC : 8'bz;  // Controlled_Buffer controlled_buffer_3
  assign O1 = decoder_1_out3 ? D_ASYNC : 8'bz;  // Controlled_Buffer controlled_buffer_4
  assign O2 = decoder_2_out4 ? E_ASYNC : 8'bz;  // Controlled_Buffer controlled_buffer_5
  assign O2 = decoder_2_out5 ? F_ASYNC : 8'bz;  // Controlled_Buffer controlled_buffer_6
  assign O2 = decoder_2_out0 ? A_ASYNC : 8'bz;  // Controlled_Buffer controlled_buffer_7
  assign O2 = decoder_2_out1 ? B_ASYNC : 8'bz;  // Controlled_Buffer controlled_buffer_8
  assign O2 = decoder_2_out2 ? C_ASYNC : 8'bz;  // Controlled_Buffer controlled_buffer_9
  assign O2 = decoder_2_out3 ? D_ASYNC : 8'bz;  // Controlled_Buffer controlled_buffer_10
endmodule

module ALUOperatorSelector (
  input  OP_SEL0,
  input  OP_SEL1,
  input  OP_SEL2,
  output [7:0] OP_OUT
);

  Decoder #(.select(3)) decoder_1 (
    .out0(OP_OUT[0]), .out1(OP_OUT[1]), .out2(OP_OUT[2]), .out3(OP_OUT[3]), .out4(OP_OUT[4]),
    .out5(OP_OUT[5]), .out6(OP_OUT[6]), .out7(OP_OUT[7]), .sel({OP_SEL2, OP_SEL1, OP_SEL0}), .en(1'b1));
endmodule

module FLAGSRegister (
  input  [7:0] BUS_IN,
  input  I_VAL,
  input  [2:0] ALU_FLAGS,
  input  NOT_CZN_IN,
  input  NOT_I_IN,
  input  FLAGS_IN_SEL,
  input  CLK,
  output [3:0] FLAGS_OUT
);

  wire not_1_out, not_2_out;
  wire [3:0] multiplexer_1_out;

  Multiplexer #(.width(4)) multiplexer_1 (
    .in0(BUS_IN[3:0]), .in1({I_VAL, ALU_FLAGS}), .out(multiplexer_1_out), .sel(FLAGS_IN_SEL));
  Register #(.width(3)) CZN (.D(multiplexer_1_out[2:0]), .en(not_1_out), .clk(CLK), .Q(FLAGS_OUT[2:0]));  // open: clr
  not not_1 (not_1_out, NOT_CZN_IN);
  Register #(.width(1)) I (.D(multiplexer_1_out[3]), .en(not_2_out), .clk(CLK), .Q(FLAGS_OUT[3]));  // open: clr
  not not_2 (not_2_out, NOT_I_IN);
endmodule

module ALU (
  input  [7:0] OPERATORS,
  input  [7:0] O1,
  input  [7:0] O2,
  output [7:0] BUS_OUT,
  output [2:0] FLAGS
);

  wire adder_1_cout, and_2_out, and_3_out, nor_1_out, nor_2_out, nor_3_out, nor_4_out, or_2_out;
  wire [6:0] buffer_1_out;
  wire [7:0] adder_1_out, and_1_out, bit_extender_1_out, not_1_out, or_1_out, xor_1_out, xor_2_out;

  assign not_1_out = ~O1;  // NOT_Gate not_1, 8 bits wide
  assign xor_1_out = O1 ^ O2;  // XOR_Gate xor_1, 8 bits wide
  assign BUS_OUT = OPERATORS[6] ? not_1_out : 8'bz;  // Controlled_Buffer controlled_buffer_1
  assign BUS_OUT = OPERATORS[5] ? xor_1_out : 8'bz;  // Controlled_Buffer controlled_buffer_2
  assign and_1_out = O1 & O2;  // AND_Gate and_1, 8 bits wide
  assign BUS_OUT = OPERATORS[4] ? and_1_out : 8'bz;  // Controlled_Buffer controlled_buffer_3
  // NoConnect on OPERATORS[7]
  assign or_1_out = O1 | O2;  // OR_Gate or_1, 8 bits wide
  assign BUS_OUT = OPERATORS[3] ? or_1_out : 8'bz;  // Controlled_Buffer controlled_buffer_4
  nor nor_1 (nor_1_out, FLAGS[2], buffer_1_out[6]);
  assign bit_extender_1_out = {{7{OPERATORS[2]}}, OPERATORS[2]};  // Bit_Extender bit_extender_1
  assign {FLAGS[2], buffer_1_out} = BUS_OUT;  // Buffer buffer_1, 8 bits wide
  Pull_Resistor pull_resistor_1 (.node({FLAGS[2], buffer_1_out}));
  nor nor_2 (nor_2_out, buffer_1_out[5], buffer_1_out[4]);
  nor nor_3 (nor_3_out, buffer_1_out[3], buffer_1_out[2]);
  and and_2 (and_2_out, nor_1_out, nor_2_out);
  and and_3 (and_3_out, nor_3_out, nor_4_out);
  and and_4 (FLAGS[1], and_2_out, and_3_out);
  Adder adder_1 (.a(O1), .b(xor_2_out), .out(adder_1_out), .cin(OPERATORS[2]), .cout(adder_1_cout));
  assign xor_2_out = O2 ^ bit_extender_1_out;  // XOR_Gate xor_2, 8 bits wide
  assign BUS_OUT = or_2_out ? adder_1_out : 8'bz;  // Controlled_Buffer controlled_buffer_5
  xor xor_3 (FLAGS[0], OPERATORS[2], adder_1_cout);
  nor nor_4 (nor_4_out, buffer_1_out[1], buffer_1_out[0]);
  or or_2 (or_2_out, OPERATORS[2], OPERATORS[1]);

  // Notes on the sheet:
  //   we invert the carry when subtracting, so that the carry flag in a sub operation means "borrow"
endmodule

module ClockModule (
  input  NOT_HLT,
  output C2,
  output C1,
  output C4,
  output C3
);

  wire CLK_GEN_out, sysclk_out;

  Clock #(.highDuration(2), .lowDuration(2), .phaseOffset(3)) CLK_GEN (.out(CLK_GEN_out));
  Clock #(.highDuration(2), .lowDuration(2)) sysclk (.out(sysclk_out));
  and and_1 (C2, CLK_GEN_out, NOT_HLT);
  and and_2 (C1, NOT_HLT, sysclk_out);
  not not_1 (C4, C2);
  not not_2 (C3, C1);
endmodule

module InstructionRegister (
);

  Counter counter_1 ();  // open: clr, load, up, count, clk, D, carry, Q
endmodule

module RAMModule (
  input  NOT_PUSH,
  input  NOT_DEVICE_IN,
  input  NOT_DEVICE_SEL_RAM,
  input  [7:0] SP,
  input  NOT_DEVICE_OUT,
  input  NOT_POP,
  input  CLK,
  input  [7:0] SS,
  input  [15:0] ABUS,
  input  [7:0] BUS_IN,
  input  NOT_FETCH,
  output [7:0] DBUS_OUT,
  output [7:0] FBUS_OUT
);

  wire nand_1_out, nand_2_out, nand_3_out, nand_4_out, nand_5_out, nand_6_out, nand_7_out, not_1_out,
       not_2_out, not_3_out, or_1_out;
  wire [7:0] multiplexer_1_out, multiplexer_2_out, ram_1_dout;

  Multiplexer #(.width(8)) multiplexer_1 (.in0(ABUS[7:0]), .in1(SP), .out(multiplexer_1_out), .sel(nand_1_out));
  Multiplexer #(.width(8)) multiplexer_2 (
    .in0({3'b000, ABUS[12:8]}), .in1(SS), .out(multiplexer_2_out), .sel(nand_1_out));
  RAM #(.addrWidth(13), .asyncread("true")) ram_1 (
    .addr({multiplexer_2_out[4:0], multiplexer_1_out}), .we(not_1_out), .oe(1'b1), .clk(CLK), .din(BUS_IN),
    .dout(ram_1_dout));
  nand nand_1 (nand_1_out, NOT_PUSH, NOT_POP);
  not not_1 (not_1_out, nand_2_out);
  nand nand_2 (nand_2_out, nand_4_out, nand_5_out);
  not not_2 (not_2_out, nand_3_out);
  nand nand_3 (nand_3_out, nand_6_out, nand_7_out);
  assign DBUS_OUT = not_2_out ? ram_1_dout : 8'bz;  // Controlled_Buffer controlled_buffer_1
  assign FBUS_OUT = not_3_out ? ram_1_dout : 8'bz;  // Controlled_Buffer controlled_buffer_2
  not not_3 (not_3_out, or_1_out);
  or or_1 (or_1_out, NOT_DEVICE_SEL_RAM, NOT_FETCH);
  nand nand_4 (nand_4_out, NOT_PUSH, NOT_DEVICE_IN);
  nand nand_5 (nand_5_out, NOT_DEVICE_SEL_RAM, NOT_PUSH);
  nand nand_6 (nand_6_out, NOT_DEVICE_SEL_RAM, NOT_POP);
  nand nand_7 (nand_7_out, NOT_DEVICE_OUT, NOT_POP);
endmodule

module StackPointer (
  input  NOT_SP_IN,
  input  SP_DIR,
  input  NOT_SP_CT,
  input  CLK,
  output [7:0] SP_OUT
);

  wire not_1_out, not_2_out;

  not not_1 (not_1_out, NOT_SP_IN);
  Counter counter_1 (
    .clr(1'b0), .load(not_1_out), .up(SP_DIR), .count(not_2_out), .clk(CLK), .D({8{1'b0}}), .Q(SP_OUT));  // open: carry
  not not_2 (not_2_out, NOT_SP_CT);
endmodule

module ROMModule (
  input  [15:0] ABUS,
  input  NOT_DEVICE_SEL_ROM,
  input  NOT_DEVICE_OUT,
  input  NOT_FETCH,
  output [7:0] DBUS_OUT,
  output [7:0] FBUS_OUT
);

  wire not_1_out, not_2_out, or_1_out, or_2_out;
  wire [7:0] STORAGE_ROM_data;
  wire [12:0] bit_extender_1_out;

  Bit_Extender #(.in_width(16), .out_width(13), .\type ("zero")) bit_extender_1 (.in(ABUS), .out(bit_extender_1_out));
  ROM #(.addrWidth(13)) STORAGE_ROM (.addr(bit_extender_1_out), .data(STORAGE_ROM_data));
  not not_1 (not_1_out, or_1_out);
  or or_1 (or_1_out, NOT_DEVICE_SEL_ROM, NOT_DEVICE_OUT);
  assign DBUS_OUT = not_1_out ? STORAGE_ROM_data : 8'bz;  // Controlled_Buffer controlled_buffer_1
  assign FBUS_OUT = not_2_out ? STORAGE_ROM_data : 8'bz;  // Controlled_Buffer controlled_buffer_2
  not not_2 (not_2_out, or_2_out);
  or or_2 (or_2_out, NOT_FETCH, NOT_DEVICE_SEL_ROM);

  // Notes on the sheet:
  //   contents of STORAGE_ROM (hex, n*v repeats v):
  //   0 0 8 21 7 0 45 60 0 c 21 2 0 21 3 0 21 4 0 21 5 0 f3 21 0 0 21 1 0 45 60 0 3e 45 60 0 20 f2 1d 1 91
  //   0 e7 26 f3 5 22 cc 1e 0 92 1 e7 58 92 4 e5 92 ee 1e 5d 91 1 e7 92 1d 6 19 2 1d 7 19 3 8e e7 8d 38 d8
  //   91 2e e7 73 91 3a e7 6a e8 92 38 91 72 e7 63 91 52 e7 63 e8 92 1f 2 20 3 ef e8 96 ee 1 0 91 1 e7 92
  //   e8 96 92 9 e7 79 e8 92 ee 1e 5d 91 1 e7 92 1d 6 19 4 1d 7 19 5 ee 0 a5 e8 96 ee 0 9d e8 96 45 60 0
  //   3f 45 60 0 a f2 e8 16 1d 2 19 4 1d 3 19 5 1d 4 1e 5 1f 2 20 3 46 e8 c2 83 e5 e7 e7 b7 e8 ba 88 e5 e7
  //   46 14 b9 7 e7 c2 e8 d6 45 60 0 a 11 ee 1e 48 14 ee 1e 48 45 60 0 3a 45 60 0 20 38 ee 1e 48 45 60 0
  //   20 50 d8 e5 e4 e8 b0 d7 e8 b0 f0 24*0 47 51 47 74 e7 41 e5 3d 38 91 20 e7 f e8 3d d8 38 ee 1e 16 91
  //   ff e7 3d 4*dd b d8 38 ee 1e 16 91 ff e7 3d 5a 48 49 1f 2 20 3 34 d8 1c 3 e5 38 53 52 d8 e8 1 d7 1b 2
  //   e8 33 3 1 51 f0 bd 51 f0 7356*0 46 48 49 38 a9 e7 12 3d 60 0 d8 e5 f e8 3 d7 e8 3 53 52 50 f0 7d 30
  //   e6 34 91 9 e6 39 e7 39 7d 11 e6 34 91 5 e6 37 e7 37 7d 20 e6 34 91 5 e6 37 e7 37 3 ff f0 69 a f0 b9
  //   f 91 a e6 45 7d a 69 41 f0 69 30 f0 46 46 4*de ee 1e 3a 3d 60 0 50 ee 1e 3a 3d 60 0 50 f0 47 38 ee
  //   1e 16 91 ff e7 9b 4*dd 19 6 d8 38 ee 1e 16 91 ff e7 9b 1e 6 5a 19 6 d8 38 ee 1e 16 91 ff e7 9b 4*dd
  //   19 7 d8 38 ee 1e 16 91 ff e7 9b 1e 7 5a 19 7 d8 51 bd f0 51 3 1 f0 97*0 46 41 40 0 a9 e7 26 48 49 41
  //   40 1 3d 60 0 5 22 20 0 91 8 e7 21 91 a e7 28 34 d8 1c 0 e8 24 dc 1c 0 53 52 50 f1 21 1 1 e8 24
endmodule

module CodeSegment_ProgramCounter (
  input  [3:0] FLAGS,
  input  J,
  input  JC,
  input  JZ,
  input  JN,
  input  JA,
  input  NOT_PC_IN,
  input  NOT_CS_IN,
  input  NOT_PC_INC,
  input  RESET,
  input  [15:0] ABUS,
  input  CLK,
  input  NOT_PC_OUT,
  input  NOT_CS_OUT,
  input  CSPC_DIR,
  output [15:0] CS_PC,
  output [7:0] BUS_OUT
);

  wire and_1_out, and_2_out, and_3_out, and_4_out, and_5_out, nor_1_out, nor_2_out, nor_3_out, not_1_out,
       not_2_out, not_3_out, or_1_out, or_2_out, or_3_out, PC_carry;

  and and_1 (and_1_out, JC, FLAGS[0]);
  or or_1 (or_1_out, and_1_out, and_2_out);
  and and_2 (and_2_out, JZ, FLAGS[1]);
  and and_3 (and_3_out, JN, FLAGS[2]);
  or or_2 (or_2_out, and_3_out, and_4_out);
  or or_3 (or_3_out, or_1_out, or_2_out);
  nor nor_1 (nor_1_out, J, or_3_out);
  and and_4 (and_4_out, JA, FLAGS[3]);
  nor nor_2 (nor_2_out, NOT_CS_IN, nor_1_out);
  and and_5 (and_5_out, CLK, RESET);
  not not_1 (not_1_out, NOT_PC_OUT);
  not not_2 (not_2_out, NOT_CS_OUT);
  Counter CS (
    .clr(and_5_out), .load(nor_2_out), .up(CSPC_DIR), .count(PC_carry), .clk(CLK), .D(ABUS[15:8]),
    .Q(CS_PC[15:8]));  // open: carry
  not not_3 (not_3_out, NOT_PC_INC);
  nor nor_3 (nor_3_out, nor_1_out, NOT_PC_IN);
  Counter PC (
    .clr(and_5_out), .load(nor_3_out), .up(CSPC_DIR), .count(not_3_out), .clk(CLK), .D(ABUS[7:0]),
    .carry(PC_carry), .Q(CS_PC[7:0]));
  assign BUS_OUT = not_2_out ? CS_PC[15:8] : 8'bz;  // Controlled_Buffer controlled_buffer_1
  assign BUS_OUT = not_1_out ? CS_PC[7:0] : 8'bz;  // Controlled_Buffer controlled_buffer_2
endmodule

module LCD_emulator (
  input  RS,
  input  R_NW,
  input  LCD_EN,
  input  [7:0] BUS_IN
);
endmodule

module Interface_emulator (
  input  POLL,
  input  TRANSMIT,
  input  CLK,
  input  [7:0] BUS_IN,
  output [7:0] BUS_OUT,
  output A_OUT
);

  wire [7:0] register_1_q;

  Register register_1 (.D(BUS_IN), .en(TRANSMIT), .clk(CLK), .Q(register_1_q));  // open: clr
  assign BUS_OUT = POLL ? register_1_q : 8'bz;  // Controlled_Buffer controlled_buffer_1

  assign A_OUT = POLL;
endmodule

module ControlUnit (
  input  [7:0] DATA_LATCH,
  input  NOT_IRQ,
  input  CLK90,
  input  RESET,
  input  I,
  output [7:0] IR_OUT,
  output RA_S0,
  output RA_S1,
  output NOT_RA_OUT,
  output NOT_RB_IN,
  output NOT_RB_OUT,
  output NOT_RC_IN,
  output NOT_RC_OUT,
  output NOT_RD_IN,
  output NOT_RD_OUT,
  output NOT_DEVICE_IN,
  output NOT_DEVICE_OUT,
  output NOT_SS_IN,
  output NOT_SS_OUT,
  output NOT_SP_IN,
  output NOT_SP_OUT,
  output NOT_SP_CT,
  output SP_DIR,
  output NOT_ABH_IN,
  output NOT_ABL_IN,
  output NOT_RT_IN,
  output NOT_RT_OUT,
  output X_SEL0,
  output X_SEL1,
  output Y_SEL0,
  output Y_SEL1,
  output Y_SEL2,
  output OP_SEL0,
  output OP_SEL1,
  output OP_SEL2,
  output NOT_CS_IN,
  output NOT_PC_IN,
  output NOT_PC_INC,
  output NOT_CS_OUT,
  output NOT_PC_OUT,
  output NOT_FETCH,
  output J,
  output JC,
  output JZ,
  output JN,
  output JA,
  output NOT_PASS,
  output NOT_HLT,
  output PAGE_0,
  output NOT_PUSH,
  output NOT_POP,
  output NOT_DATA_LATCH_OUT,
  output NOT_IVH_OUT,
  output NOT_IVL_OUT,
  output I_VAL,
  output FLAGS_MODE_SEL0,
  output FLAGS_MODE_SEL1,
  output NOT_FLAGS_OUT,
  output CSPC_DIR
);

  wire and_1_out, edgedetector_1_pulse, not_1_out, or_1_out, or_2_out;
  wire [3:0] counter_1_q;
  wire [7:0] multiplexer_1_out;
  wire [7:5] EEPROM6_data;

  not not_1 (not_1_out, NOT_PASS);
  Multiplexer #(.width(8)) multiplexer_1 (.in0(8'h2), .in1(DATA_LATCH), .out(multiplexer_1_out), .sel(or_1_out));
  or or_1 (or_1_out, NOT_IRQ, I);
  or or_2 (or_2_out, not_1_out, RESET);
  EdgeDetector edgedetector_1 (.D(CLK90), .PULSE(edgedetector_1_pulse));
  Register IR (.D(multiplexer_1_out), .en(or_2_out), .clk(CLK90), .Q(IR_OUT), .clr(RESET));
  Counter #(.max('hf), .width(4)) counter_1 (
    .clr(and_1_out), .load(1'b0), .up(1'b1), .count(1'b1), .clk(CLK90), .D(4'b1111), .Q(counter_1_q));  // open: carry
  and and_1 (and_1_out, or_2_out, edgedetector_1_pulse);
  ROM #(.addrWidth(13)) EEPROM0 (
    .addr({1'b0, IR_OUT, counter_1_q}),
    .data({NOT_RD_IN, NOT_RC_OUT, NOT_RC_IN, NOT_RB_OUT, NOT_RB_IN, NOT_RA_OUT, RA_S1, RA_S0}));
  ROM #(.addrWidth(13)) EEPROM1 (
    .addr({1'b0, IR_OUT, counter_1_q}),
    .data({NOT_SP_CT, NOT_SP_OUT, NOT_SP_IN, NOT_SS_OUT, NOT_SS_IN, NOT_DEVICE_OUT, NOT_DEVICE_IN, NOT_RD_OUT}));
  ROM #(.addrWidth(13)) EEPROM2 (
    .addr({1'b0, IR_OUT, counter_1_q}),
    .data({Y_SEL0, X_SEL1, X_SEL0, NOT_RT_OUT, NOT_RT_IN, NOT_ABL_IN, NOT_ABH_IN, SP_DIR}));
  ROM #(.addrWidth(13)) EEPROM3 (
    .addr({1'b0, IR_OUT, counter_1_q}),
    .data({NOT_PC_INC, NOT_PC_IN, NOT_CS_IN, OP_SEL2, OP_SEL1, OP_SEL0, Y_SEL2, Y_SEL1}));
  ROM #(.addrWidth(13)) EEPROM4 (
    .addr({1'b0, IR_OUT, counter_1_q}), .data({JA, JN, JZ, JC, J, NOT_FETCH, NOT_PC_OUT, NOT_CS_OUT}));
  ROM #(.addrWidth(13)) EEPROM5 (
    .addr({1'b0, IR_OUT, counter_1_q}),
    .data({NOT_IVL_OUT, NOT_IVH_OUT, NOT_DATA_LATCH_OUT, NOT_POP, NOT_PUSH, PAGE_0, NOT_HLT, NOT_PASS}));
  ROM #(.addrWidth(13)) EEPROM6 (
    .addr({1'b0, IR_OUT, counter_1_q}),
    .data({EEPROM6_data, CSPC_DIR, NOT_FLAGS_OUT, FLAGS_MODE_SEL1, FLAGS_MODE_SEL0, I_VAL}));

  // Notes on the sheet:
  //   Get the 163! Synchronous reset
  //   contents of EEPROM0 (hex, n*v repeats v):
  //   48*fc ff 15*fc f4 15*fc dc 15*fc 7c 47*fc 7c 15*fc 7c 15*fc f0 15*fc d8 15*fc 78 15*fc ef 15*fc cc
  //   15*fc 6c 15*fc bf 15*fc b4 15*fc 3c 15*fc ff 15*fc f4 15*fc dc 48*fc f8 15*fc ec 15*fc bc 31*fc ff
  //   15*fc f4 15*fc dc 15*fc 7c 31*fc f8 15*fc ec 15*fc bc 31*fc ff 15*fc f4 15*fc dc 15*fc 7c 32*fc f8
  //   15*fc ec 15*fc bc 31*fc ff 15*fc f4 15*fc dc 15*fc 7c 29*fc bc fc f8 13*fc bc fc ec 13*fc bc fc bc
  //   13*fc bc 15*fc bc fc ff 13*fc bc fc f4 13*fc bc fc dc 13*fc bc fc 7c 13*fc bc 17*fc f8 15*fc ec
  //   15*fc bc 31*fc ff 15*fc f4 15*fc dc 15*fc 7c 29*fc f8 15*fc ec 15*fc bc 79*fc bc 47*fc ff 15*fc f4
  //   15*fc dc 15*fc 7c 64*fc bc 30*fc ff 15*fc ff 15*fc ff 15*fc ff 15*fc f4 15*fc f4 15*fc f4 15*fc f4
  //   15*fc dc 15*fc dc 15*fc dc 15*fc dc 15*fc 7c 15*fc 7c 15*fc 7c 15*fc 7c 16*fc ff 15*fc f4 15*fc f4
  //   15*fc f4 14*fc ff 15*fc ff 15*fc ff 15*fc ff 15*fc f4 15*fc f4 15*fc f4 15*fc f4 15*fc dc 15*fc dc
  //   15*fc dc 15*fc dc 15*fc 7c 15*fc 7c 15*fc 7c 15*fc 7c 16*fc ff 15*fc f4 15*fc f4 15*fc f4 334*fc ff
  //   15*fc ff 15*fc ff 15*fc ff 15*fc f4 15*fc f4 15*fc f4 15*fc f4 15*fc dc 15*fc dc 15*fc dc 15*fc dc
  //   15*fc 7c 15*fc 7c 15*fc 7c 15*fc 7c 16*fc ff 15*fc f4 15*fc f4 15*fc f4 14*fc ff 15*fc ff 15*fc ff
  //   15*fc ff 15*fc f4 15*fc f4 15*fc f4 15*fc f4 15*fc dc 15*fc dc 15*fc dc 15*fc dc 15*fc 7c 15*fc 7c
  //   15*fc 7c 15*fc 7c 16*fc ff 15*fc f4 15*fc f4 15*fc f4 14*fc ff 15*fc ff 15*fc ff 15*fc ff 15*fc f4
  //   15*fc f4 15*fc f4 15*fc f4 15*fc dc 15*fc dc 15*fc dc 15*fc dc 15*fc 7c 15*fc 7c 15*fc 7c 15*fc 7c
  //   16*fc ff 15*fc f4 15*fc f4 15*fc f4 14*fc ff 15*fc f4 15*fc dc 15*fc 7c 15*fc ff 15*fc f4 15*fc dc
  //   15*fc 7c 15*fc ff 15*fc f4 15*fc dc 15*fc 7c 15*fc fe 15*fc fd 15*fc f8 ef f4 13*fc f8 bf dc 13*fc
  //   f8 ff 7c 13*fc ec b4 dc 13*fc ec f4 7c 13*fc bc dc 7c 141*fc bc 31*fc bc 79*fc
  //   contents of EEPROM1 (hex, n*v repeats v):
  //   35*ff 7f 7f 7f 74*ff df 15*ff f7 15*ff ef 15*ff bf 159*ff fe 15*ff fe 15*ff fe 15*ff f6 15*ff de
  //   16*ff fd 15*ff fd 15*ff fd 15*ff fc 15*ff fb 15*ff fb 15*ff fb 15*ff fb 15*ff fd 14*ff fe fd 14*ff
  //   fe fd 14*ff fe fd 14*ff fe fc 14*ff fe fb 14*ff fe fb 14*ff fe fb 14*ff fe fb 14*ff fe fd 15*ff fe
  //   fd 14*ff fe fd 14*ff fe fd 14*ff fe fc 14*ff fe fb 14*ff fe fb 14*ff fe fb 14*ff fe fb 14*ff fe fd
  //   14*ff fe fd 14*ff fe fd 14*ff fe fd 14*ff fe fc 14*ff fe fb 14*ff fe fb 14*ff fe fb 14*ff fe fb
  //   14*ff fe fd 15*ff fd 15*ff fd 15*ff fd 15*ff fc 15*ff fb 15*ff fb 15*ff fb 15*ff fb 15*ff fd 14*ff
  //   7f 15*ff 7f 15*ff 7f 14*ff fe 7f 15*ff fb ff 7f 12*ff fe fb ff 7f 13*ff fe fb ff 7f 12*ff fe fb ff
  //   7f 12*ff fe fb ff 7f 12*ff 7f 14*ff 7f 15*ff 7f 15*ff 7f 15*ff 7f 16*ff 7f fd 13*ff fe 7f fd 13*ff
  //   7f ff fe fd 12*ff 7f ff fe fd 12*ff 7f ff fe fd 2189*ff fe 31*ff fe 15*ff fe 143*ff fe 17*ff 7f 7f
  //   12*ff fe ff 7f 7f 11*ff 7f 7f 14*ff 7f 7f 7f 45*ff
  //   contents of EEPROM2 (hex, n*v repeats v):
  //   32*1e 1c 1a 1e 1f 1f 1f 362*1e 1a 15*1e 1a 15*1e 1a 15*1e 1a 15*1e 1a 15*1e 1a 15*1e 1a 15*1e 1a
  //   15*1e 1a 15*1e 1a 15*1e 1a 15*1e 1a 15*1e 1a 15*1e 1a 15*1e 1a 15*1e 1a 15*1e 1a 15*1e 1a 15*1e 1c
  //   1a 14*1e 1c 1a 14*1e 1c 1a 14*1e 1c 1a 14*1e 1c 1a 14*1e 1c 1a 14*1e 1c 1a 14*1e 1c 1a 14*1e 1c 1a
  //   14*1e 1c 1a 14*1e 1c 1a 14*1e 1c 1a 14*1e 1c 1a 14*1e 1c 1a 14*1e 1c 1a 14*1e 1c 1a 14*1e 1c 1a
  //   14*1e 1c 1a 14*1e 1c 1a 14*1e 1c 1a 14*1e 1c 1a 14*1e 1c 1a 14*1e 1c 1a 14*1e 1c 1a 14*1e 1c 1a
  //   14*1e 1c 1a 14*1e 1c 1a 15*1e 1f 15*1e 1f 15*1e 1f 15*1e 1f 14*1e 1a 16 e 1f 12*1e 1a 16 e 1f 12*1e
  //   1c 1a 16 e 1f 11*1e 1c 1a 16 e 1f 11*1e 1c 1a 16 e 1f 12*1e 1f 78*1e 1a 16 e 13*1e 1a 16 e 13*1e 16
  //   1c 1a e 12*1e 16 1c 1a e 12*1e 16 1c 1a e 28*1e 9e 31*1e 9e 15*1e 3e 15*1e be 15*1e 3e 15*1e be
  //   15*1e 5e 15*1e de 15*1e 5e 15*1e de 15*1e 7e 15*1e fe 15*1e 7e 15*1e fe 15*1e 16 15*1e 16 3e 14*1e
  //   16 5e 14*1e 16 7e 30*1e 9e 31*1e 9e 15*1e 3e 15*1e be 15*1e 3e 15*1e be 15*1e 5e 15*1e de 15*1e 5e
  //   15*1e de 15*1e 7e 15*1e fe 15*1e 7e 15*1e fe 15*1e 16 15*1e 16 3e 14*1e 16 5e 14*1e 16 7e 30*1e 9e
  //   31*1e 9e 15*1e 3e 15*1e be 15*1e 3e 15*1e be 15*1e 5e 15*1e de 15*1e 5e 15*1e de 15*1e 7e 15*1e fe
  //   15*1e 7e 15*1e fe 15*1e 16 15*1e 16 3e 14*1e 16 5e 14*1e 16 7e 30*1e 9e 31*1e 9e 15*1e 3e 15*1e be
  //   15*1e 3e 15*1e be 15*1e 5e 15*1e de 15*1e 5e 15*1e de 15*1e 7e 15*1e fe 15*1e 7e 15*1e fe 15*1e 16
  //   15*1e 16 3e 14*1e 16 5e 14*1e 16 7e 30*1e 9e 31*1e 9e 15*1e 3e 15*1e be 15*1e 3e 15*1e be 15*1e 5e
  //   15*1e de 15*1e 5e 15*1e de 15*1e 7e 15*1e fe 15*1e 7e 15*1e fe 15*1e 16 15*1e 16 3e 14*1e 16 5e
  //   14*1e 16 7e 30*1e 9e 31*1e 9e 15*1e 3e 15*1e be 15*1e 3e 15*1e be 15*1e 5e 15*1e de 15*1e 5e 15*1e
  //   de 15*1e 7e 15*1e fe 15*1e 7e 15*1e fe 15*1e 16 15*1e 16 3e 14*1e 16 5e 14*1e 16 7e 30*1e 3e 15*1e
  //   5e 15*1e 7e 15*1e 9e 15*1e be 15*1e de 15*1e fe 15*1e 9e 15*1e be 15*1e de 15*1e fe 47*1e 16 1e e
  //   13*1e 16 1e e 13*1e 16 1e e 13*1e 16 1e e 13*1e 16 1e e 13*1e 16 1e e 13*1e 1a 15*1e 1a 15*1e 1a
  //   15*1e 1a 15*1e 1c 1a 14*1e 1c 1a 14*1e 1c 1a 14*1e 1c 1a 14*1e 1c 1a 14*1e 1c 1a 1e 1f 1f 11*1e 1c
  //   1a 1e 1f 1f 11*1e 1a 1c 15*1e 1a 1c 45*1e
  //   contents of EEPROM3 (hex, n*v repeats v):
  //   60 15*e0 60 15*e0 60 4*e0 80 60 9*e0 60 60 14*e0 60 60 14*e0 60 60 14*e0 60 60 14*e0 60 60 14*e0 60
  //   60 14*e0 60 15*e0 60 15*e0 60 15*e0 60 15*e0 60 15*e0 60 15*e0 60 15*e0 60 15*e0 60 15*e0 60 15*e0
  //   60 15*e0 60 15*e0 60 15*e0 60 15*e0 60 15*e0 60 15*e0 60 60 14*e0 60 60 14*e0 60 60 14*e0 60 60
  //   14*e0 60 60 14*e0 60 60 14*e0 60 60 14*e0 60 60 14*e0 60 60 60 14*e0 60 15*e0 60 15*e0 60 15*e0 60
  //   15*e0 60 15*e0 60 15*e0 60 15*e0 60 15*e0 60 60 13*e0 60 e0 60 13*e0 60 e0 60 13*e0 60 e0 60 13*e0
  //   60 e0 60 13*e0 60 e0 60 13*e0 60 e0 60 13*e0 60 e0 60 13*e0 60 e0 60 13*e0 60 e0 60 60 14*e0 60
  //   15*e0 60 15*e0 60 15*e0 60 15*e0 60 15*e0 60 15*e0 60 15*e0 60 15*e0 60 60 12*e0 60 60 60 13*e0 60
  //   60 60 13*e0 60 60 60 13*e0 60 60 60 13*e0 60 60 60 13*e0 60 60 60 13*e0 60 60 60 13*e0 60 60 60
  //   13*e0 4*60 13*e0 60 15*e0 60 15*e0 60 15*e0 60 14*e0 60 e0 e0 60 15*e0 60 12*e0 60 e0 e0 e0 60 15*e0
  //   60 11*e0 60 e0 e0 e0 60 11*e0 60 60 14*e0 60 15*e0 60 15*e0 60 15*e0 60 15*e0 60 e0 60 15*e0 60
  //   14*e0 60 e0 60 15*e0 60 13*e0 60 e0 60 12*e0 64 15*e0 64 15*e0 65 15*e0 65 15*e0 64 15*e0 64 15*e0
  //   65 15*e0 65 15*e0 64 15*e0 64 15*e0 65 15*e0 65 15*e0 64 15*e0 64 15*e0 65 15*e0 65 15*e0 60 66
  //   14*e0 60 66 14*e0 60 66 14*e0 60 66 14*e0 68 15*e0 68 15*e0 69 15*e0 69 15*e0 68 15*e0 68 15*e0 69
  //   15*e0 69 15*e0 68 15*e0 68 15*e0 69 15*e0 69 15*e0 68 15*e0 68 15*e0 69 15*e0 69 15*e0 60 6a 14*e0
  //   60 6a 14*e0 60 6a 14*e0 60 6a 14*e0 68 15*e0 68 15*e0 69 15*e0 69 15*e0 68 15*e0 68 15*e0 69 15*e0
  //   69 15*e0 68 15*e0 68 15*e0 69 15*e0 69 15*e0 68 15*e0 68 15*e0 69 15*e0 69 15*e0 60 6a 14*e0 60 6a
  //   14*e0 60 6a 14*e0 60 6a 14*e0 6c 15*e0 6c 15*e0 6d 15*e0 6d 15*e0 6c 15*e0 6c 15*e0 6d 15*e0 6d
  //   15*e0 6c 15*e0 6c 15*e0 6d 15*e0 6d 15*e0 6c 15*e0 6c 15*e0 6d 15*e0 6d 15*e0 60 6e 14*e0 60 6e
  //   14*e0 60 6e 14*e0 60 6e 14*e0 70 15*e0 70 15*e0 71 15*e0 71 15*e0 70 15*e0 70 15*e0 71 15*e0 71
  //   15*e0 70 15*e0 70 15*e0 71 15*e0 71 15*e0 70 15*e0 70 15*e0 71 15*e0 71 15*e0 60 72 14*e0 60 72
  //   14*e0 60 72 14*e0 60 72 14*e0 74 15*e0 74 15*e0 75 15*e0 75 15*e0 74 15*e0 74 15*e0 75 15*e0 75
  //   15*e0 74 15*e0 74 15*e0 75 15*e0 75 15*e0 74 15*e0 74 15*e0 75 15*e0 75 15*e0 60 76 14*e0 60 76
  //   14*e0 60 76 14*e0 60 76 14*e0 78 15*e0 78 15*e0 78 15*e0 78 15*e0 66 15*e0 66 15*e0 66 15*e0 66
  //   15*e0 6a 15*e0 6a 15*e0 6a 15*e0 6a 15*e0 60 15*e0 60 17*e0 60 15*e0 60 15*e0 60 15*e0 60 15*e0 60
  //   15*e0 60 13*e0 60 a0 60 13*e0 60 a0 60 13*e0 60 a0 60 13*e0 60 a0 60 13*e0 60 60 80 60 12*e0 60 60
  //   80 60 12*e0 60 60 80 60 12*e0 60 60 80 60 14*e0 80 60 12*e0 60 60 e0 e0 80 60 14*e0 80 60 12*e0 80
  //   60 15*e0 80 60 11*e0 60 15*e0 60 15*e0
  //   contents of EEPROM4 (hex, n*v repeats v):
  //   3 15*7 3 17*7 6 5 7 f 3 9*7 3 3 14*7 3 3 14*7 3 3 14*7 3 3 14*7 3 3 14*7 3 3 14*7 3 15*7 3 15*7 3
  //   15*7 3 15*7 3 15*7 3 15*7 3 15*7 3 15*7 3 15*7 3 15*7 3 15*7 3 15*7 3 15*7 3 15*7 3 15*7 3 15*7 3 3
  //   14*7 3 3 14*7 3 3 14*7 3 3 14*7 3 3 14*7 3 3 14*7 3 3 14*7 3 3 14*7 3 3 3 14*7 3 15*7 3 15*7 3 15*7
  //   3 15*7 3 15*7 3 15*7 3 15*7 3 15*7 3 3 13*7 3 7 3 13*7 3 7 3 13*7 3 7 3 13*7 3 7 3 13*7 3 7 3 13*7 3
  //   7 3 13*7 3 7 3 13*7 3 7 3 13*7 3 7 3 3 14*7 3 15*7 3 15*7 3 15*7 3 15*7 3 15*7 3 15*7 3 15*7 3 15*7
  //   3 3 12*7 3 3 3 13*7 3 3 3 13*7 3 3 3 13*7 3 3 3 13*7 3 3 3 13*7 3 3 3 13*7 3 3 3 13*7 3 3 3 13*7 4*3
  //   13*7 3 15*7 3 15*7 3 15*7 3 14*7 3 7 7 3 15*7 3 12*7 3 7 7 7 3 15*7 3 11*7 3 7 7 7 3 11*7 3 3 14*7 3
  //   15*7 3 15*7 3 15*7 3 15*7 3 7 3 15*7 3 14*7 3 7 3 15*7 3 13*7 3 7 3 12*7 3 15*7 3 15*7 3 15*7 3 15*7
  //   3 15*7 3 15*7 3 15*7 3 15*7 3 15*7 3 15*7 3 15*7 3 15*7 3 15*7 3 15*7 3 15*7 3 15*7 3 3 14*7 3 3
  //   14*7 3 3 14*7 3 3 14*7 3 15*7 3 15*7 3 15*7 3 15*7 3 15*7 3 15*7 3 15*7 3 15*7 3 15*7 3 15*7 3 15*7
  //   3 15*7 3 15*7 3 15*7 3 15*7 3 15*7 3 3 14*7 3 3 14*7 3 3 14*7 3 3 14*7 3 15*7 3 15*7 3 15*7 3 15*7 3
  //   15*7 3 15*7 3 15*7 3 15*7 3 15*7 3 15*7 3 15*7 3 15*7 3 15*7 3 15*7 3 15*7 3 15*7 3 3 14*7 3 3 14*7
  //   3 3 14*7 3 3 14*7 3 15*7 3 15*7 3 15*7 3 15*7 3 15*7 3 15*7 3 15*7 3 15*7 3 15*7 3 15*7 3 15*7 3
  //   15*7 3 15*7 3 15*7 3 15*7 3 15*7 3 3 14*7 3 3 14*7 3 3 14*7 3 3 14*7 3 15*7 3 15*7 3 15*7 3 15*7 3
  //   15*7 3 15*7 3 15*7 3 15*7 3 15*7 3 15*7 3 15*7 3 15*7 3 15*7 3 15*7 3 15*7 3 15*7 3 3 14*7 3 3 14*7
  //   3 3 14*7 3 3 14*7 3 15*7 3 15*7 3 15*7 3 15*7 3 15*7 3 15*7 3 15*7 3 15*7 3 15*7 3 15*7 3 15*7 3
  //   15*7 3 15*7 3 15*7 3 15*7 3 15*7 3 3 14*7 3 3 14*7 3 3 14*7 3 3 14*7 3 15*7 3 15*7 3 15*7 3 15*7 3
  //   15*7 3 15*7 3 15*7 3 15*7 3 15*7 3 15*7 3 15*7 3 15*7 3 15*7 3 17*7 3 15*7 3 15*7 3 15*7 3 15*7 3
  //   15*7 3 13*7 3 17 3 13*7 3 47 3 13*7 3 27 3 13*7 3 f 3 13*7 3 3 17 3 12*7 3 3 47 3 12*7 3 3 27 3 12*7
  //   3 3 f 3 14*7 f 3 12*7 3 3 6 5 f 3 12*7 6 5 f 3 12*7 f 3 15*7 f 3 11*7 3 15*7 3 15*7
  //   contents of EEPROM5 (hex, n*v repeats v):
  //   fa 15*fb f8 15*fb bb 7b f3 f3 f3 fb fa 9*fb db fa 14*fb db fa 14*fb db fa 14*fb db fa 14*fb db fa
  //   14*fb db fa 14*fb fa 15*fb fa 15*fb fa 15*fb fa 15*fb fa 15*fb fa 15*fb fa 15*fb fa 15*fb fa 15*fb
  //   fa 15*fb fa 15*fb fa 15*fb fa 15*fb fa 15*fb fa 15*fb fa 15*fb db fe 14*fb db fe 14*fb db fe 14*fb
  //   db fe 14*fb db fe 14*fb db fe 14*fb db fe 14*fb db fe 14*fb db df fa 14*fb fe 15*fb fe 15*fb fe
  //   15*fb fe 15*fb fe 15*fb fe 15*fb fe 15*fb fe 15*fb df fa 13*fb db fb fa 13*fb db fb fa 13*fb db fb
  //   fa 13*fb db fb fa 13*fb db fb fa 13*fb db fb fa 13*fb db fb fa 13*fb db fb fa 13*fb db fb db fa
  //   14*fb fa 15*fb fa 15*fb fa 15*fb fa 15*fb fa 15*fb fa 15*fb fa 15*fb fa 15*fb db fa 12*fb db db fa
  //   13*fb db db fa 13*fb db db fa 13*fb db db fa 13*fb db db fa 13*fb db db fa 13*fb db db fa 13*fb db
  //   db fa 13*fb db db db fa 12*fb f3 fa 14*fb f3 fa 14*fb f3 fa 14*fb f3 fa 14*fb db ff f3 fa 13*fb ff
  //   f3 fa 12*fb db fb fb f3 fa 14*fb f3 fa 11*fb db fb fb f3 fa 11*fb d3 fa 14*fb ea 15*fb ea 15*fb ea
  //   15*fb ea 15*fb db eb fe 14*fb eb fe 13*fb eb db fb fa 12*fb eb fb fb fa 12*fb eb db fb fa 12*fb fa
  //   15*fb fa 15*fb fa 15*fb fa 15*fb fa 15*fb fa 15*fb fa 15*fb fa 15*fb fa 15*fb fa 15*fb fa 15*fb fa
  //   15*fb fa 15*fb fa 15*fb fa 15*fb fa 15*fb db fa 14*fb db fa 14*fb db fa 14*fb db fa 14*fb fa 15*fb
  //   fa 15*fb fa 15*fb fa 15*fb fa 15*fb fa 15*fb fa 15*fb fa 15*fb fa 15*fb fa 15*fb fa 15*fb fa 15*fb
  //   fa 15*fb fa 15*fb fa 15*fb fa 15*fb db fa 14*fb db fa 14*fb db fa 14*fb db fa 14*fb fa 15*fb fa
  //   15*fb fa 15*fb fa 15*fb fa 15*fb fa 15*fb fa 15*fb fa 15*fb fa 15*fb fa 15*fb fa 15*fb fa 15*fb fa
  //   15*fb fa 15*fb fa 15*fb fa 15*fb db fa 14*fb db fa 14*fb db fa 14*fb db fa 14*fb fa 15*fb fa 15*fb
  //   fa 15*fb fa 15*fb fa 15*fb fa 15*fb fa 15*fb fa 15*fb fa 15*fb fa 15*fb fa 15*fb fa 15*fb fa 15*fb
  //   fa 15*fb fa 15*fb fa 15*fb db fa 14*fb db fa 14*fb db fa 14*fb db fa 14*fb fa 15*fb fa 15*fb fa
  //   15*fb fa 15*fb fa 15*fb fa 15*fb fa 15*fb fa 15*fb fa 15*fb fa 15*fb fa 15*fb fa 15*fb fa 15*fb fa
  //   15*fb fa 15*fb fa 15*fb db fa 14*fb db fa 14*fb db fa 14*fb db fa 14*fb fa 15*fb fa 15*fb fa 15*fb
  //   fa 15*fb fa 15*fb fa 15*fb fa 15*fb fa 15*fb fa 15*fb fa 15*fb fa 15*fb fa 15*fb fa 15*fb fa 15*fb
  //   fa 15*fb fa 15*fb db fa 14*fb db fa 14*fb db fa 14*fb db fa 14*fb fa 15*fb fa 15*fb fa 15*fb fa
  //   15*fb fa 15*fb fa 15*fb fa 15*fb fa 15*fb fa 15*fb fa 15*fb fa 15*fb fa 15*fb fa 15*fb fa 17*fb fa
  //   15*fb fa 15*fb fa 15*fb fa 15*fb fa 15*fb fa 13*fb db fb fa 13*fb db fb fa 13*fb db fb fa 13*fb db
  //   fb fa 13*fb db db fb fa 12*fb db db fb fa 12*fb db db fb fa 12*fb db db fb fa 15*fb fa 12*fb db db
  //   f3 f3 fb fa 12*fb f3 f3 fb fa 10*fb eb eb fb fa 12*fb eb eb eb fb fa 11*fb fa 15*fb fa 15*fb
  //   contents of EEPROM6 (hex, n*v repeats v):
  //   32*1e e 1e 1e 1e 16 1b 1386*1e 1c 15*1e 1c 15*1e 1c 15*1e 1c 15*1e 1c 15*1e 1c 15*1e 1c 15*1e 1c
  //   15*1e 1c 15*1e 1c 15*1e 1c 15*1e 1c 15*1e 1c 15*1e 1c 15*1e 1c 15*1e 1c 16*1e 1c 15*1e 1c 15*1e 1c
  //   15*1e 1c 14*1e 1c 15*1e 1c 15*1e 1c 15*1e 1c 15*1e 1c 15*1e 1c 15*1e 1c 15*1e 1c 15*1e 1c 15*1e 1c
  //   15*1e 1c 15*1e 1c 15*1e 1c 15*1e 1c 15*1e 1c 15*1e 1c 16*1e 1c 15*1e 1c 15*1e 1c 15*1e 1c 14*1e 1c
  //   15*1e 1c 15*1e 1c 15*1e 1c 15*1e 1c 15*1e 1c 15*1e 1c 15*1e 1c 15*1e 1c 15*1e 1c 15*1e 1c 15*1e 1c
  //   15*1e 1c 15*1e 1c 15*1e 1c 15*1e 1c 16*1e 1c 15*1e 1c 15*1e 1c 15*1e 1c 14*1e 1c 15*1e 1c 15*1e 1c
  //   15*1e 1c 15*1e 1c 15*1e 1c 15*1e 1c 15*1e 1c 15*1e 1c 15*1e 1c 15*1e 1c 15*1e 1c 15*1e 1c 15*1e 1c
  //   15*1e 1c 15*1e 1c 16*1e 1c 15*1e 1c 15*1e 1c 15*1e 1c 14*1e 1c 15*1e 1c 15*1e 1c 15*1e 1c 15*1e 1c
  //   15*1e 1c 15*1e 1c 15*1e 1c 15*1e 1c 15*1e 1c 15*1e 1c 15*1e 1c 15*1e 1c 15*1e 1c 15*1e 1c 15*1e 1c
  //   16*1e 1c 15*1e 1c 15*1e 1c 15*1e 1c 14*1e 1c 15*1e 1c 15*1e 1c 15*1e 1c 15*1e 1c 15*1e 1c 15*1e 1c
  //   15*1e 1c 15*1e 1c 15*1e 1c 15*1e 1c 15*1e 1c 15*1e 1c 15*1e 1c 15*1e 1c 15*1e 1c 16*1e 1c 15*1e 1c
  //   15*1e 1c 15*1e 1c 14*1e 1c 15*1e 1c 15*1e 1c 15*1e 1c 15*1e 1c 15*1e 1c 15*1e 1c 15*1e 1c 15*1e 1c
  //   15*1e 1c 15*1e 1c 15*1e 1c 335*1e 18 15*1e 1a 15*1e 1b 15*1e
endmodule

module AddrDecoder (
  input  [15:0] ABUS,
  output NOT_DEVICE_SEL_ROM,
  output NOT_DEVICE_SEL_RAM,
  output NOT_DEVICE_SEL_0,
  output NOT_DEVICE_SEL_1,
  output NOT_DEVICE_SEL_2,
  output NOT_DEVICE_SEL_3,
  output NOT_DEVICE_SEL_4,
  output NOT_DEVICE_SEL_5
);

  wire decoder_1_out0, decoder_1_out1, decoder_1_out2, decoder_1_out3, decoder_1_out4, decoder_1_out5,
       decoder_1_out6, decoder_1_out7;

  Decoder #(.select(3)) decoder_1 (
    .out0(decoder_1_out0), .out1(decoder_1_out1), .out2(decoder_1_out2), .out3(decoder_1_out3),
    .out4(decoder_1_out4), .out5(decoder_1_out5), .out6(decoder_1_out6), .out7(decoder_1_out7),
    .sel(ABUS[15:13]), .en(1'b1));
  not not_1 (NOT_DEVICE_SEL_ROM, decoder_1_out0);
  not not_2 (NOT_DEVICE_SEL_RAM, decoder_1_out1);
  not not_3 (NOT_DEVICE_SEL_0, decoder_1_out2);
  not not_4 (NOT_DEVICE_SEL_1, decoder_1_out3);
  not not_5 (NOT_DEVICE_SEL_2, decoder_1_out4);
  not not_6 (NOT_DEVICE_SEL_3, decoder_1_out5);
  not not_7 (NOT_DEVICE_SEL_4, decoder_1_out6);
  not not_8 (NOT_DEVICE_SEL_5, decoder_1_out7);
endmodule

module FLAGSController (
  input  FLAGS_MODE_SEL0,
  input  FLAGS_MODE_SEL1,
  output NOT_CZN_IN,
  output NOT_I_IN,
  output FLAGS_IN_SEL
);

  or or_1 (FLAGS_IN_SEL, FLAGS_MODE_SEL0, FLAGS_MODE_SEL1);

  assign NOT_CZN_IN = FLAGS_MODE_SEL0;
  assign NOT_I_IN = FLAGS_MODE_SEL1;

  // Notes on the sheet:
  //   0
  //   0
  //   0
  //   1
  //   1
  //   0
  //   1
  //   1
  //   SEL0 SEL1 MODE
  //   load from bus
  //   load from ALU
  //   load I
  //   nothing
endmodule
