// Logisim project Devices.circ as structural Verilog: 4 circuits, main circuit ButtonAdapter
module ButtonAdapter (
  input  BUTTON_IN,
  input  [7:0] DBUS_IN,
  input  [15:0] ABUS,
  input  NOT_DEVICE_IN,
  input  CLK,
  output NOT_IRQ,
  output [7:0] D_BUS_OUT
);

  wire not_1_out, s_r_ff_1_q;

  S_R_Flip_Flop s_r_ff_1 (.S(BUTTON_IN), .R(not_1_out), .clk(CLK), .Q(s_r_ff_1_q));  // open: reset, Qn, preset
  not not_1 (not_1_out, NOT_DEVICE_IN);
  assign NOT_IRQ = s_r_ff_1_q ? 1'b0 : 1'bz;  // Controlled_Buffer controlled_buffer_1
  assign D_BUS_OUT = {{7{1'b0}}, s_r_ff_1_q};  // Bit_Extender bit_extender_1
endmodule

module HexDisplayAdapter (
  input  [7:0] DBUS_IN,
  input  [15:0] ABUS,
  input  NOT_DEVICE_IN,
  input  NOT_DEVICE_OUT,
  input  CLK,
  output [3:0] LSB,
  output [3:0] MSB
);

  wire not_1_out;

  Register register_1 (.D(DBUS_IN), .en(not_1_out), .clk(CLK), .Q({MSB, LSB}));  // open: clr
  not not_1 (not_1_out, NOT_DEVICE_IN);
endmodule

module KeyboardAdapter (
  input  K_AVAIL,
  input  [6:0] K_DATA,
  input  [7:0] BUS_IN,
  input  [15:0] ABUS,
  input  NOT_DEVICE_IN,
  input  NOT_DEVICE_OUT,
  input  CLK,
  output NOT_IRQ,
  output [7:0] ASYNC_OUT,
  output K_READ_EN,
  output K_CLEAR,
  output K_CLK
);

  wire bit_extender_3_out, not_2_out;
  wire [7:0] bit_extender_1_out, bit_extender_2_out;

  assign bit_extender_1_out = {{1{1'b0}}, K_DATA};  // Bit_Extender bit_extender_1
  not not_1 (K_CLEAR, NOT_DEVICE_IN);
  and and_1 (K_READ_EN, not_2_out, bit_extender_3_out);
  not not_2 (not_2_out, NOT_DEVICE_OUT);
  assign bit_extender_2_out = {{7{1'b0}}, K_AVAIL};  // Bit_Extender bit_extender_2
  Transistor #(.\type ("n")) transistor_1 (.in(1'b0), .out(NOT_IRQ), .gate(K_AVAIL));
  Bit_Extender #(.in_width(16), .out_width(1)) bit_extender_3 (.in(ABUS), .out(bit_extender_3_out));
  Multiplexer #(.width(8)) multiplexer_1 (
    .in0(bit_extender_2_out), .in1(bit_extender_1_out), .out(ASYNC_OUT), .sel(bit_extender_3_out));

  assign K_CLK = CLK;
endmodule

module TTYAdapter (
  input  [7:0] DBUS_IN,
  input  [15:0] ABUS,
  input  NOT_DEVICE_IN,
  input  NOT_DEVICE_OUT,
  input  CLK,
  output [6:0] TTY_DATA,
  output TTY_WE,
  output TTY_CLR
);

  wire bit_extender_1_out, not_1_out, not_2_out;
  wire [7:0] register_1_q;

  Bit_Extender #(.in_width(16), .out_width(1)) bit_extender_1 (.in(ABUS), .out(bit_extender_1_out));
  Register register_1 (.D(DBUS_IN), .en(not_1_out), .clk(CLK), .Q(register_1_q));  // open: clr
  not not_1 (not_1_out, NOT_DEVICE_IN);
  Bit_Extender #(.out_width(7)) bit_extender_2 (.in(register_1_q), .out(TTY_DATA));
  and and_1 (TTY_WE, not_1_out, not_2_out);
  not not_2 (not_2_out, bit_extender_1_out);
  and and_2 (TTY_CLR, bit_extender_1_out, not_1_out);
endmodule
