// Digital circuit BufferedRegister.dig as structural Verilog
module BufferedRegister (
  input  [7:0] BUS_IN,
  input  C,
  input  nR_in,
  input  nR_out,
  output [7:0] BUS_out,
  output [7:0] OUT
);

  _74173 _74173_1 (
    .pin1(1'b0), .pin2(1'b0), .pin3(OUT[0]), .pin4(OUT[1]), .pin5(OUT[2]), .pin6(OUT[3]), .pin7(C),
    .pin8(1'b0), .pin9(nR_in), .pin10(nR_in), .pin11(BUS_IN[3]), .pin12(BUS_IN[2]), .pin13(BUS_IN[1]),
    .pin14(BUS_IN[0]), .pin15(1'b0), .pin16(1'b1));
  _74173 _74173_2 (
    .pin1(1'b0), .pin2(1'b0), .pin3(OUT[4]), .pin4(OUT[5]), .pin5(OUT[6]), .pin6(OUT[7]), .pin7(C),
    .pin8(1'b0), .pin9(nR_in), .pin10(nR_in), .pin11(BUS_IN[7]), .pin12(BUS_IN[6]), .pin13(BUS_IN[5]),
    .pin14(BUS_IN[4]), .pin15(1'b0), .pin16(1'b1));
  _74244 _74244_1 (
    .pin1(nR_out), .pin2(OUT[0]), .pin3(BUS_out[7]), .pin4(OUT[1]), .pin5(BUS_out[6]), .pin6(OUT[2]),
    .pin7(BUS_out[5]), .pin8(OUT[3]), .pin9(BUS_out[4]), .pin10(1'b0), .pin11(OUT[4]), .pin12(BUS_out[3]),
    .pin13(OUT[5]), .pin14(BUS_out[2]), .pin15(OUT[6]), .pin16(BUS_out[1]), .pin17(OUT[7]),
    .pin18(BUS_out[0]), .pin19(nR_out), .pin20(1'b1));
endmodule
