// Digital circuit Clock.dig as structural Verilog
module Clock (
  input  nHLT,
  input  C_IN,
  output C1,
  output C2,
  output C3,
  output C4
);

  wire and_1_out;

  and and_1 (and_1_out, nHLT, C_IN);
  D_FF_AS d_ff_as_1 (.Set(1'b0), .D(C4), .C(and_1_out), .Clr(1'b0), .Q(C1), .nQ(C3));
  D_FF_AS d_ff_as_2 (.Set(1'b0), .D(C3), .C(and_1_out), .Clr(1'b0), .Q(C4), .nQ(C2));

  // Notes on the sheet:
  //   https://www.theremin.us/Circuit_Library/four_phase_clock.html
endmodule
