// Digital circuit ShiftRegister.dig as structural Verilog
module ShiftRegister (
  input  [7:0] BUS_IN,
  input  S0,
  input  CLK,
  input  S1,
  input  nOE,
  output [7:0] BUS_out,
  output [7:0] OUT
);

  _74194 _74194_1 (
    .pin1(1'b1), .pin2(1'b0), .pin3(BUS_IN[7]), .pin4(BUS_IN[6]), .pin5(BUS_IN[5]), .pin6(BUS_IN[4]),
    .pin7(OUT[3]), .pin8(1'b0), .pin9(S0), .pin10(S1), .pin11(CLK), .pin12(OUT[4]), .pin13(OUT[5]),
    .pin14(OUT[6]), .pin15(OUT[7]), .pin16(1'b1));
  _74194 _74194_2 (
    .pin1(1'b1), .pin2(OUT[4]), .pin3(BUS_IN[3]), .pin4(BUS_IN[2]), .pin5(BUS_IN[1]), .pin6(BUS_IN[0]),
    .pin7(1'b0), .pin8(1'b0), .pin9(S0), .pin10(S1), .pin11(CLK), .pin12(OUT[0]), .pin13(OUT[1]),
    .pin14(OUT[2]), .pin15(OUT[3]), .pin16(1'b1));
  _74244 _74244_1 (
    .pin1(nOE), .pin2(OUT[0]), .pin3(BUS_out[7]), .pin4(OUT[1]), .pin5(BUS_out[6]), .pin6(OUT[2]),
    .pin7(BUS_out[5]), .pin8(OUT[3]), .pin9(BUS_out[4]), .pin10(1'b0), .pin11(OUT[4]), .pin12(BUS_out[3]),
    .pin13(OUT[5]), .pin14(BUS_out[2]), .pin15(OUT[6]), .pin16(BUS_out[1]), .pin17(OUT[7]),
    .pin18(BUS_out[0]), .pin19(nOE), .pin20(1'b1));
endmodule
