// Digital circuit ALU.dig as structural Verilog
module ALU (
  input  OP_sel0,
  input  OP_sel1,
  input  OP_sel2,
  input  [7:0] X,
  input  [7:0] Y,
  output [7:0] BUS_out,
  output [2:0] FLAGS
);

  wire _7402_1_pin1, _7402_1_pin4, _7402_1_pin10, _7402_1_pin13, _7408_1_pin3, _7408_1_pin6, _7408_2_pin3,
       _7408_2_pin6, _7486_1_pin3, _7486_1_pin6, _7486_1_pin8, _7486_1_pin11, _7486_2_pin3, _7486_2_pin6,
       _7486_2_pin8, _7486_2_pin11, _74283_1_pin7, ADD0, ADD1, ADD2, ADD3, ADD4, ADD5, ADD6, ADD7, AND0,
       AND1, AND2, AND3, AND4, AND5, AND6, AND7, nOP_sel0, nOP_sel1, nOP_sel2, NOT0, NOT1, NOT2, NOT3, NOT4,
       NOT5, NOT6, NOT7, OR0, OR1, OR2, OR3, OR4, OR5, OR6, OR7, XOR0, XOR1, XOR2, XOR3, XOR4, XOR5, XOR6,
       XOR7;
  wire [2:0] _7402_1_pin9;
  wire [3:0] _7402_1_pin3;

  _74151 _74151_1 (
    .pin1(OR0), .pin2(ADD0), .pin3(ADD0), .pin4(1'b0), .pin5(_7402_1_pin3[0]), .pin7(1'b0), .pin8(1'b0),
    .pin9(OP_sel2), .pin10(OP_sel1), .pin11(OP_sel0), .pin12(1'b0), .pin13(NOT0), .pin14(XOR0), .pin15(AND0),
    .pin16(1'b1));  // open: pin6
  _7486 _7486_1 (
    .pin1(Y[4]), .pin2(OP_sel1), .pin3(_7486_1_pin3), .pin4(Y[5]), .pin5(OP_sel1), .pin6(_7486_1_pin6),
    .pin7(1'b0), .pin8(_7486_1_pin8), .pin9(Y[6]), .pin10(OP_sel1), .pin11(_7486_1_pin11), .pin12(Y[7]),
    .pin13(OP_sel1), .pin14(1'b1));
  _74283 _74283_1 (
    .pin1(ADD5), .pin2(_7486_1_pin6), .pin3(X[5]), .pin4(ADD4), .pin5(X[4]), .pin6(_7486_1_pin3),
    .pin7(_74283_1_pin7), .pin8(1'b0), .pin9(FLAGS[0]), .pin10(ADD7), .pin11(_7486_1_pin11), .pin12(X[7]),
    .pin13(ADD6), .pin14(X[6]), .pin15(_7486_1_pin8), .pin16(1'b1));
  _7402 _7402_1 (
    .pin1(_7402_1_pin1), .pin2(_7402_1_pin3[0]), .pin3(_7402_1_pin3[1]), .pin4(_7402_1_pin4),
    .pin5(_7402_1_pin3[2]), .pin6(_7402_1_pin3[3]), .pin7(1'b0), .pin8(_7402_1_pin9[1]),
    .pin9(_7402_1_pin9[0]), .pin10(_7402_1_pin10), .pin11(_7402_1_pin9[2]), .pin12(FLAGS[2]),
    .pin13(_7402_1_pin13), .pin14(1'b1));
  _74151 _74151_2 (
    .pin1(OR1), .pin2(ADD1), .pin3(ADD1), .pin4(1'b0), .pin5(_7402_1_pin3[1]), .pin7(1'b0), .pin8(1'b0),
    .pin9(OP_sel2), .pin10(OP_sel1), .pin11(OP_sel0), .pin12(1'b0), .pin13(NOT1), .pin14(XOR1), .pin15(AND1),
    .pin16(1'b1));  // open: pin6
  _7486 _7486_2 (
    .pin1(Y[0]), .pin2(OP_sel1), .pin3(_7486_2_pin3), .pin4(Y[1]), .pin5(OP_sel1), .pin6(_7486_2_pin6),
    .pin7(1'b0), .pin8(_7486_2_pin8), .pin9(Y[2]), .pin10(OP_sel1), .pin11(_7486_2_pin11), .pin12(Y[3]),
    .pin13(OP_sel1), .pin14(1'b1));
  _74283 _74283_2 (
    .pin1(ADD1), .pin2(_7486_2_pin6), .pin3(X[1]), .pin4(ADD0), .pin5(X[0]), .pin6(_7486_2_pin3),
    .pin7(OP_sel1), .pin8(1'b0), .pin9(_74283_1_pin7), .pin10(ADD3), .pin11(_7486_2_pin11), .pin12(X[3]),
    .pin13(ADD2), .pin14(X[2]), .pin15(_7486_2_pin8), .pin16(1'b1));
  _74151 _74151_3 (
    .pin1(OR2), .pin2(ADD2), .pin3(ADD2), .pin4(1'b0), .pin5(_7402_1_pin3[2]), .pin7(1'b0), .pin8(1'b0),
    .pin9(OP_sel2), .pin10(OP_sel1), .pin11(OP_sel0), .pin12(1'b0), .pin13(NOT2), .pin14(XOR2), .pin15(AND2),
    .pin16(1'b1));  // open: pin6
  _7408 _7408_1 (
    .pin1(_7402_1_pin1), .pin2(_7402_1_pin4), .pin3(_7408_1_pin3), .pin4(_7402_1_pin10),
    .pin5(_7402_1_pin13), .pin6(_7408_1_pin6), .pin7(1'b0), .pin8(FLAGS[1]), .pin9(_7408_1_pin3),
    .pin10(_7408_1_pin6), .pin12(1'b0), .pin13(1'b0), .pin14(1'b1));  // open: pin11
  _74151 _74151_4 (
    .pin1(OR3), .pin2(ADD3), .pin3(ADD3), .pin4(1'b0), .pin5(_7402_1_pin3[3]), .pin7(1'b0), .pin8(1'b0),
    .pin9(OP_sel2), .pin10(OP_sel1), .pin11(OP_sel0), .pin12(1'b0), .pin13(NOT3), .pin14(XOR3), .pin15(AND3),
    .pin16(1'b1));  // open: pin6
  _7408 _7408_2 (
    .pin1(nOP_sel0), .pin2(nOP_sel1), .pin3(_7408_2_pin3), .pin4(_7408_2_pin3), .pin5(nOP_sel2),
    .pin6(_7408_2_pin6), .pin7(1'b0), .pin9(1'b0), .pin10(1'b0), .pin12(1'b0), .pin13(1'b0), .pin14(1'b1));  // open: pin8, pin11
  _7432 _7432_1 (
    .pin1(X[0]), .pin2(Y[0]), .pin3(OR0), .pin4(X[1]), .pin5(Y[1]), .pin6(OR1), .pin7(1'b0), .pin8(OR2),
    .pin9(X[2]), .pin10(Y[2]), .pin11(OR3), .pin12(X[3]), .pin13(Y[3]), .pin14(1'b1));
  _7408 _7408_3 (
    .pin1(X[0]), .pin2(Y[0]), .pin3(AND0), .pin4(X[1]), .pin5(Y[1]), .pin6(AND1), .pin7(1'b0), .pin8(AND2),
    .pin9(X[2]), .pin10(Y[2]), .pin11(AND3), .pin12(X[3]), .pin13(Y[3]), .pin14(1'b1));
  _74151 _74151_5 (
    .pin1(OR4), .pin2(ADD4), .pin3(ADD4), .pin4(1'b0), .pin5(_7402_1_pin9[0]), .pin7(1'b0), .pin8(1'b0),
    .pin9(OP_sel2), .pin10(OP_sel1), .pin11(OP_sel0), .pin12(1'b0), .pin13(NOT4), .pin14(XOR4), .pin15(AND4),
    .pin16(1'b1));  // open: pin6
  _7432 _7432_2 (
    .pin1(X[4]), .pin2(Y[4]), .pin3(OR4), .pin4(X[5]), .pin5(Y[5]), .pin6(OR5), .pin7(1'b0), .pin8(OR6),
    .pin9(X[6]), .pin10(Y[6]), .pin11(OR7), .pin12(X[7]), .pin13(Y[7]), .pin14(1'b1));
  _7408 _7408_4 (
    .pin1(X[4]), .pin2(Y[4]), .pin3(AND4), .pin4(X[5]), .pin5(Y[5]), .pin6(AND5), .pin7(1'b0), .pin8(AND6),
    .pin9(X[6]), .pin10(Y[6]), .pin11(AND7), .pin12(X[7]), .pin13(Y[7]), .pin14(1'b1));
  _74151 _74151_6 (
    .pin1(OR5), .pin2(ADD5), .pin3(ADD5), .pin4(1'b0), .pin5(_7402_1_pin9[1]), .pin7(1'b0), .pin8(1'b0),
    .pin9(OP_sel2), .pin10(OP_sel1), .pin11(OP_sel0), .pin12(1'b0), .pin13(NOT5), .pin14(XOR5), .pin15(AND5),
    .pin16(1'b1));  // open: pin6
  _74244 _74244_1 (
    .pin1(_7408_2_pin6), .pin2(_7402_1_pin3[0]), .pin3(BUS_out[7]), .pin4(_7402_1_pin3[1]),
    .pin5(BUS_out[6]), .pin6(_7402_1_pin3[2]), .pin7(BUS_out[5]), .pin8(_7402_1_pin3[3]), .pin9(BUS_out[4]),
    .pin10(1'b0), .pin11(_7402_1_pin9[0]), .pin12(BUS_out[3]), .pin13(_7402_1_pin9[1]), .pin14(BUS_out[2]),
    .pin15(_7402_1_pin9[2]), .pin16(BUS_out[1]), .pin17(FLAGS[2]), .pin18(BUS_out[0]), .pin19(_7408_2_pin6),
    .pin20(1'b1));
  _7486 _7486_3 (
    .pin1(X[0]), .pin2(Y[0]), .pin3(XOR0), .pin4(X[1]), .pin5(Y[1]), .pin6(XOR1), .pin7(1'b0), .pin8(XOR2),
    .pin9(X[2]), .pin10(Y[2]), .pin11(XOR3), .pin12(X[3]), .pin13(Y[3]), .pin14(1'b1));
  _7404 _7404_1 (
    .pin1(X[0]), .pin2(NOT0), .pin3(X[1]), .pin4(NOT1), .pin5(X[2]), .pin6(NOT2), .pin7(1'b0), .pin8(NOT3),
    .pin9(X[3]), .pin10(NOT4), .pin11(X[4]), .pin12(NOT5), .pin13(X[5]), .pin14(1'b1));
  _74151 _74151_7 (
    .pin1(OR6), .pin2(ADD6), .pin3(ADD6), .pin4(1'b0), .pin5(_7402_1_pin9[2]), .pin7(1'b0), .pin8(1'b0),
    .pin9(OP_sel2), .pin10(OP_sel1), .pin11(OP_sel0), .pin12(1'b0), .pin13(NOT6), .pin14(XOR6), .pin15(AND6),
    .pin16(1'b1));  // open: pin6
  _7486 _7486_4 (
    .pin1(X[4]), .pin2(Y[4]), .pin3(XOR4), .pin4(X[5]), .pin5(Y[5]), .pin6(XOR5), .pin7(1'b0), .pin8(XOR6),
    .pin9(X[6]), .pin10(Y[6]), .pin11(XOR7), .pin12(X[7]), .pin13(Y[7]), .pin14(1'b1));
  _7404 _7404_2 (
    .pin1(X[6]), .pin2(NOT6), .pin3(X[7]), .pin4(NOT7), .pin5(OP_sel0), .pin6(nOP_sel0), .pin7(1'b0),
    .pin8(nOP_sel1), .pin9(OP_sel1), .pin10(nOP_sel2), .pin11(OP_sel2), .pin13(1'b0), .pin14(1'b1));  // open: pin12
  _74151 _74151_8 (
    .pin1(OR7), .pin2(ADD7), .pin3(ADD7), .pin4(1'b0), .pin5(FLAGS[2]), .pin7(1'b0), .pin8(1'b0),
    .pin9(OP_sel2), .pin10(OP_sel1), .pin11(OP_sel0), .pin12(1'b0), .pin13(NOT7), .pin14(XOR7), .pin15(AND7),
    .pin16(1'b1));  // open: pin6

  // Other names for the same wires on the sheet: C_out = FLAGS[0]
endmodule

/* Test case:
		OP_sel0		OP_sel1		OP_sel2		X		Y		BUS_out		FLAGS
loop(i,128)
  let x = random(256);
  let y = random(256);
  		0		0		0		(x)		(y)		Z		X
		1		0		0		(x)		(y)		(x+y)		((((x+y) >> 8) & 1) + (ite((x+y) & 0xFF, 0, 1) << 1) + ((((x+y) >> 7) & 1) << 2))
		0		1		0		(x)		(y)		(x+(y^0xFF)+1)	((((x+(y^0xFF)+1) >> 8) & 1) + (ite((x+(y^0xFF)+1) & 0xFF, 0, 1) << 1) + ((((x+(y^0xFF)+1) >> 7) & 1) << 2))
		1		1		0		(x)		(y)		(x|y)		((((x+(y^0xFF)+1) >> 8) & 1) + (ite((x|y) & 0xFF, 0, 1) << 1) + ((((x|y) >> 7) & 1) << 2))
		0		0		1		(x)		(y)		(x&y)		((((x+y) >> 8) & 1) + (ite((x&y) & 0xFF, 0, 1) << 1) + ((((x&y) >> 7) & 1) << 2))
		1		0		1		(x)		(y)		(x^y)		((((x+y) >> 8) & 1) + (ite((x^y) & 0xFF, 0, 1) << 1) + ((((x^y) >> 7) & 1) << 2))
		0		1		1		(x)		(y)		(~x)		((((x+(y^0xFF)+1) >> 8) & 1) + (ite((~x) & 0xFF, 0, 1) << 1) + ((((~x) >> 7) & 1) << 2))
		1		1		1		(x)		(y)		0		((((x+(y^0xFF)+1) >> 8) & 1) + 2)
end loop
*/
