// Digital circuit ALUOperandSelector.dig as structural Verilog
module ALUOperandSelector (
  input  X_sel0,
  input  X_sel1,
  input  Y_sel0,
  input  Y_sel1,
  input  Y_sel2,
  input  [7:0] A,
  input  [7:0] B,
  input  [7:0] C,
  input  [7:0] D,
  input  [7:0] E,
  input  [7:0] F,
  output [7:0] X,
  output [7:0] Y
);

  _74151 _74151_1 (
    .pin1(D[0]), .pin2(C[0]), .pin3(B[0]), .pin4(A[0]), .pin5(X[0]), .pin7(1'b0), .pin8(1'b0), .pin9(1'b0),
    .pin10(X_sel1), .pin11(X_sel0), .pin16(1'b1));  // open: pin6, pin12, pin13, pin14, pin15
  _74151 _74151_2 (
    .pin1(D[0]), .pin2(C[0]), .pin3(B[0]), .pin4(A[0]), .pin5(Y[0]), .pin7(1'b0), .pin8(1'b0), .pin9(Y_sel2),
    .pin10(Y_sel1), .pin11(Y_sel0), .pin14(E[0]), .pin15(F[0]), .pin16(1'b1));  // open: pin6, pin12, pin13
  _74151 _74151_3 (
    .pin1(D[1]), .pin2(C[1]), .pin3(B[1]), .pin4(A[1]), .pin5(X[1]), .pin7(1'b0), .pin8(1'b0), .pin9(1'b0),
    .pin10(X_sel1), .pin11(X_sel0), .pin16(1'b1));  // open: pin6, pin12, pin13, pin14, pin15
  _74151 _74151_4 (
    .pin1(D[1]), .pin2(C[1]), .pin3(B[1]), .pin4(A[1]), .pin5(Y[1]), .pin7(1'b0), .pin8(1'b0), .pin9(Y_sel2),
    .pin10(Y_sel1), .pin11(Y_sel0), .pin14(E[1]), .pin15(F[1]), .pin16(1'b1));  // open: pin6, pin12, pin13
  _74151 _74151_5 (
    .pin1(D[2]), .pin2(C[2]), .pin3(B[2]), .pin4(A[2]), .pin5(X[2]), .pin7(1'b0), .pin8(1'b0), .pin9(1'b0),
    .pin10(X_sel1), .pin11(X_sel0), .pin16(1'b1));  // open: pin6, pin12, pin13, pin14, pin15
  _74151 _74151_6 (
    .pin1(D[2]), .pin2(C[2]), .pin3(B[2]), .pin4(A[2]), .pin5(Y[2]), .pin7(1'b0), .pin8(1'b0), .pin9(Y_sel2),
    .pin10(Y_sel1), .pin11(Y_sel0), .pin14(E[2]), .pin15(F[2]), .pin16(1'b1));  // open: pin6, pin12, pin13
  _74151 _74151_7 (
    .pin1(D[3]), .pin2(C[3]), .pin3(B[3]), .pin4(A[3]), .pin5(X[3]), .pin7(1'b0), .pin8(1'b0), .pin9(1'b0),
    .pin10(X_sel1), .pin11(X_sel0), .pin16(1'b1));  // open: pin6, pin12, pin13, pin14, pin15
  _74151 _74151_8 (
    .pin1(D[3]), .pin2(C[3]), .pin3(B[3]), .pin4(A[3]), .pin5(Y[3]), .pin7(1'b0), .pin8(1'b0), .pin9(Y_sel2),
    .pin10(Y_sel1), .pin11(Y_sel0), .pin14(E[3]), .pin15(F[3]), .pin16(1'b1));  // open: pin6, pin12, pin13
  _74151 _74151_9 (
    .pin1(D[4]), .pin2(C[4]), .pin3(B[4]), .pin4(A[4]), .pin5(X[4]), .pin7(1'b0), .pin8(1'b0), .pin9(1'b0),
    .pin10(X_sel1), .pin11(X_sel0), .pin16(1'b1));  // open: pin6, pin12, pin13, pin14, pin15
  _74151 _74151_10 (
    .pin1(D[4]), .pin2(C[4]), .pin3(B[4]), .pin4(A[4]), .pin5(Y[4]), .pin7(1'b0), .pin8(1'b0), .pin9(Y_sel2),
    .pin10(Y_sel1), .pin11(Y_sel0), .pin14(E[4]), .pin15(F[4]), .pin16(1'b1));  // open: pin6, pin12, pin13
  _74151 _74151_11 (
    .pin1(D[5]), .pin2(C[5]), .pin3(B[5]), .pin4(A[5]), .pin5(X[5]), .pin7(1'b0), .pin8(1'b0), .pin9(1'b0),
    .pin10(X_sel1), .pin11(X_sel0), .pin16(1'b1));  // open: pin6, pin12, pin13, pin14, pin15
  _74151 _74151_12 (
    .pin1(D[5]), .pin2(C[5]), .pin3(B[5]), .pin4(A[5]), .pin5(Y[5]), .pin7(1'b0), .pin8(1'b0), .pin9(Y_sel2),
    .pin10(Y_sel1), .pin11(Y_sel0), .pin14(E[5]), .pin15(F[5]), .pin16(1'b1));  // open: pin6, pin12, pin13
  _74151 _74151_13 (
    .pin1(D[6]), .pin2(C[6]), .pin3(B[6]), .pin4(A[6]), .pin5(X[6]), .pin7(1'b0), .pin8(1'b0), .pin9(1'b0),
    .pin10(X_sel1), .pin11(X_sel0), .pin16(1'b1));  // open: pin6, pin12, pin13, pin14, pin15
  _74151 _74151_14 (
    .pin1(D[6]), .pin2(C[6]), .pin3(B[6]), .pin4(A[6]), .pin5(Y[6]), .pin7(1'b0), .pin8(1'b0), .pin9(Y_sel2),
    .pin10(Y_sel1), .pin11(Y_sel0), .pin14(E[6]), .pin15(F[6]), .pin16(1'b1));  // open: pin6, pin12, pin13
  _74151 _74151_15 (
    .pin1(D[7]), .pin2(C[7]), .pin3(B[7]), .pin4(A[7]), .pin5(X[7]), .pin7(1'b0), .pin8(1'b0), .pin9(1'b0),
    .pin10(X_sel1), .pin11(X_sel0), .pin16(1'b1));  // open: pin6, pin12, pin13, pin14, pin15
  _74151 _74151_16 (
    .pin1(D[7]), .pin2(C[7]), .pin3(B[7]), .pin4(A[7]), .pin5(Y[7]), .pin7(1'b0), .pin8(1'b0), .pin9(Y_sel2),
    .pin10(Y_sel1), .pin11(Y_sel0), .pin14(E[7]), .pin15(F[7]), .pin16(1'b1));  // open: pin6, pin12, pin13
endmodule
