// Digital circuit FLAGSController.dig as structural Verilog
module FLAGSController (
  input  FLAGSMode_sel0,
  input  FLAGSMode_sel1,
  output FLAGSIn_sel,
  output nCZN_in,
  output nI_in
);

  _7432 _7432_1 (
    .pin1(FLAGSMode_sel0), .pin2(FLAGSMode_sel1), .pin3(FLAGSIn_sel), .pin4(1'b0), .pin5(1'b0), .pin7(1'b0),
    .pin9(1'b0), .pin10(1'b0), .pin12(1'b0), .pin13(1'b0), .pin14(1'b1));  // open: pin6, pin8, pin11

  assign nCZN_in = FLAGSMode_sel0;
  assign nI_in = FLAGSMode_sel1;
endmodule
