// Digital circuit Computer8bit_digital.dig as structural Verilog
module Computer8bit_digital (
  input  nHLT,
  input  CLK
);

  wire ADDR_sel0, ADDR_sel1, C1, C2, C3, C4, flagscontroller_1_flagsin_sel, flagscontroller_1_nczn_in,
       flagscontroller_1_ni_in, FLAGSMode_sel0, FLAGSMode_sel1, I_val, nABH_in, nABL_in, nDEin, nDEout,
       nDSEL_D0, nDSEL_D1, nDSEL_D2, nDSEL_D3, nDSEL_D4, nDSEL_D5, nDSEL_RAM, nDSEL_ROM, nFETCH, nFLAGS_out,
       notconnected_1_out, notconnected_2_out, notconnected_3_out, notconnected_4_out, notconnected_5_out,
       notconnected_6_out, notconnected_7_out, notconnected_8_out, notconnected_9_out, notconnected_10_out,
       notconnected_11_out, notconnected_12_out, notconnected_13_out, notconnected_14_out,
       notconnected_15_out, notconnected_16_out, nRA_out, nRB_in, nRB_out, nRC_in, nRC_out, nRD_in, nRD_out,
       nRT_in, nRT_out, nSP_down, nSP_out, nSS_in, nSS_out, OP_sel0, OP_sel1, OP_sel2, RA_S0, RA_S1, SP_down,
       SP_in;
  wire [2:0] alu_1_flags;
  wire [3:0] FLAGS_p10, RA_out, RA_out_2, RB_out, RD_p7, RT_out, RT_out_2, undriven, undriven_2;
  wire [7:0] ABH_out, ABL_out, aluoperandselector_1_x, aluoperandselector_1_y, DBUS, FBUS, RC_out, SS_out,
       stackpointer_1_out;
  wire [7:4] RB_out_2, RD_p7_2;
  wire [15:0] ABUS;

  AddrDecoder addrdecoder_1 (
    .ABUS_in(ABUS), .nDSEL_ROM(nDSEL_ROM), .nDSEL_RAM(nDSEL_RAM), .nDSEL_D0(nDSEL_D0), .nDSEL_D1(nDSEL_D1),
    .nDSEL_D2(nDSEL_D2), .nDSEL_D3(nDSEL_D3), .nDSEL_D4(nDSEL_D4), .nDSEL_D5(nDSEL_D5));
  BufferedRegister SS (.BUS_IN(DBUS), .C(C4), .nR_in(nSS_in), .nR_out(nSS_out), .BUS_out(DBUS), .OUT(SS_out));
  BufferedRegister ABH (.BUS_IN(DBUS), .C(C4), .nR_in(nABH_in), .nR_out(1'b1), .OUT(ABH_out));  // open: BUS_out
  BufferedRegister ABL (.BUS_IN(DBUS), .C(C4), .nR_in(nABL_in), .nR_out(1'b1), .OUT(ABL_out));  // open: BUS_out
  StackPointer stackpointer_1 (
    .DBUS_in(DBUS), .CLK(C3), .SP_down(SP_down), .nSP_count(nSP_down), .SP_in(SP_in), .nSPout(nSP_out),
    .OUT(stackpointer_1_out), .DBUS_out(DBUS));
  AddrSelector addrselector_1 (
    .ABH_in(ABH_out), .ABL_in(ABL_out), .SS_in(SS_out), .SP_in(stackpointer_1_out), .ADDR_sel0(ADDR_sel0),
    .ADDR_sel1(ADDR_sel1), .OUT(ABUS));
  Seven_Seg_Hex seven_seg_hex_1 (.d(DBUS[7:4]), .dp(notconnected_1_out));
  Seven_Seg_Hex seven_seg_hex_2 (.d(DBUS[3:0]), .dp(notconnected_2_out));
  // NotConnected on notconnected_1_out
  // NotConnected on notconnected_2_out
  Clock clock_1 (.nHLT(nHLT), .C_IN(CLK), .C1(C1), .C2(C2), .C3(C3), .C4(C4));
  RAM ram_1 (
    .nDE_in(nDEin), .nDSEL_RAM(nDSEL_RAM), .ABUS_in(ABUS), .nCLK(C2), .DBUS_in(DBUS), .nDout_fbus(nDEout),
    .nDout_dbus(nFETCH), .DBUS_out(DBUS), .FBUS_out(FBUS));
  Seven_Seg_Hex seven_seg_hex_3 (.d(ABUS[15:12]), .dp(notconnected_3_out));
  Seven_Seg_Hex seven_seg_hex_4 (.d(ABUS[11:8]), .dp(notconnected_4_out));
  // NotConnected on notconnected_3_out
  LED led_1 ();  // open: in
  LED led_2 ();  // open: in
  LED led_3 ();  // open: in
  LED led_4 ();  // open: in
  Seven_Seg_Hex seven_seg_hex_5 (.d(ABUS[7:4]), .dp(notconnected_5_out));
  // NotConnected on notconnected_4_out
  Seven_Seg_Hex seven_seg_hex_6 (.d(ABUS[3:0]), .dp(notconnected_6_out));
  // NotConnected on notconnected_5_out
  // NotConnected on notconnected_6_out
  BufferedRegister RC (.BUS_IN(DBUS), .C(C4), .nR_in(nRC_in), .nR_out(nRC_out), .BUS_out(DBUS), .OUT(RC_out));
  ShiftRegister RA (
    .BUS_out(DBUS), .OUT({RA_out_2, RA_out}), .BUS_IN(DBUS), .CLK(C4), .S0(RA_S0), .S1(RA_S1), .nOE(nRA_out));
  BufferedRegister RT (
    .BUS_IN(DBUS), .C(C4), .nR_in(nRT_in), .nR_out(nRT_out), .BUS_out(DBUS), .OUT({RT_out_2, RT_out}));
  FLAGSController flagscontroller_1 (
    .FLAGSMode_sel0(FLAGSMode_sel0), .FLAGSMode_sel1(FLAGSMode_sel1), .nI_in(flagscontroller_1_ni_in),
    .nCZN_in(flagscontroller_1_nczn_in), .FLAGSIn_sel(flagscontroller_1_flagsin_sel));
  Seven_Seg_Hex seven_seg_hex_7 (.d(undriven_2), .dp(notconnected_8_out));
  Seven_Seg_Hex seven_seg_hex_8 (.d(undriven), .dp(notconnected_7_out));
  Seven_Seg_Hex seven_seg_hex_9 (.d(RA_out), .dp(notconnected_10_out));
  Seven_Seg_Hex seven_seg_hex_10 (.d(RA_out_2), .dp(notconnected_9_out));
  Seven_Seg_Hex seven_seg_hex_11 (.d(RT_out), .dp(notconnected_12_out));
  Seven_Seg_Hex seven_seg_hex_12 (.d(RT_out_2), .dp(notconnected_11_out));
  // NotConnected on notconnected_7_out
  // NotConnected on notconnected_8_out
  // NotConnected on notconnected_9_out
  // NotConnected on notconnected_10_out
  // NotConnected on notconnected_11_out
  // NotConnected on notconnected_12_out
  ALUOperandSelector aluoperandselector_1 (
    .A({RA_out_2, RA_out}), .B({RB_out_2, RB_out}), .C(RC_out), .D({RD_p7_2, RD_p7}), .E({RT_out_2, RT_out}),
    .X(aluoperandselector_1_x), .Y(aluoperandselector_1_y));  // open: X_sel0, X_sel1, Y_sel0, Y_sel1, Y_sel2, F
  // BufferedRegister RD: pin names not known; wires that end beside it: DBUS, C4, nRD_in, nRD_out, DBUS, DBUS, {RD_p7_2, RD_p7}
  BufferedRegister RB (
    .BUS_IN(DBUS), .C(C4), .nR_in(nRB_in), .nR_out(nRB_out), .BUS_out(DBUS), .OUT({RB_out_2, RB_out}));
  ALU alu_1 (
    .OP_sel0(OP_sel0), .OP_sel1(OP_sel1), .OP_sel2(OP_sel2), .X(aluoperandselector_1_x),
    .Y(aluoperandselector_1_y), .BUS_out(DBUS), .FLAGS(alu_1_flags));
  // FLAGSRegister FLAGS: pin names not known; wires that end beside it: alu_1_flags, DBUS, C4, flagscontroller_1_nczn_in, flagscontroller_1_flagsin_sel, flagscontroller_1_ni_in, nFLAGS_out, I_val, DBUS, FLAGS_p10
  Seven_Seg_Hex seven_seg_hex_13 (.d(RD_p7), .dp(notconnected_13_out));
  Seven_Seg_Hex seven_seg_hex_14 (.d(RD_p7_2), .dp(notconnected_15_out));
  // NotConnected on notconnected_13_out
  Seven_Seg_Hex seven_seg_hex_15 (.d(RB_out), .dp(notconnected_14_out));
  Seven_Seg_Hex seven_seg_hex_16 (.d(RB_out_2), .dp(notconnected_16_out));
  // NotConnected on notconnected_14_out
  // NotConnected on notconnected_15_out
  // NotConnected on notconnected_16_out
  LED C (.in(FLAGS_p10[0]));
  LED Z (.in(FLAGS_p10[1]));
  LED N (.in(FLAGS_p10[2]));
  LED I (.in(FLAGS_p10[3]));
  // also tied to GND on the sheet: {ABUS[1], ABUS[2], ABUS[3], ABUS[4], ABUS[5], ABUS[6], ABUS[7], ABUS[8], ABUS[9], ABUS[10], ABUS[11], ABUS[12], ABUS[13], ABUS[14], ABUS[15], DBUS[1], DBUS[2], DBUS[3], DBUS[4], DBUS[5], DBUS[6], DBUS[7]}
  // also tied to VCC on the sheet: {ABUS[0], DBUS[0]}

  // Notes on the sheet:
  //   DATA BUS
  //   ADDRESS BUS
endmodule
