// Digital circuit AddrDecoder.dig as structural Verilog
module AddrDecoder (
  input  [15:0] ABUS_in,
  output nDSEL_ROM,
  output nDSEL_RAM,
  output nDSEL_D0,
  output nDSEL_D1,
  output nDSEL_D2,
  output nDSEL_D3,
  output nDSEL_D4,
  output nDSEL_D5
);

  _74138 _74138_1 (
    .pin1(ABUS_in[13]), .pin2(ABUS_in[14]), .pin3(ABUS_in[15]), .pin4(1'b0), .pin5(1'b0), .pin6(1'b1),
    .pin7(nDSEL_D5), .pin8(1'b0), .pin9(nDSEL_D4), .pin10(nDSEL_D3), .pin11(nDSEL_D2), .pin12(nDSEL_D1),
    .pin13(nDSEL_D0), .pin14(nDSEL_RAM), .pin15(nDSEL_ROM), .pin16(1'b1));
endmodule
