// Digital circuit AddrSelector.dig as structural Verilog
module AddrSelector (
  input  ADDR_sel0,
  input  ADDR_sel1,
  input  [7:0] ABH_in,
  input  [7:0] SS_in,
  input  [7:0] ABL_in,
  input  [7:0] SP_in,
  output [15:0] OUT
);

  wire _7408_1_pin11;
  wire [7:0] _74153_1_pin4;

  _74153 _74153_1 (
    .pin1(1'b0), .pin2(ADDR_sel1), .pin3(SS_in[0]), .pin4(_74153_1_pin4[0]), .pin5(_74153_1_pin4[0]),
    .pin6(ABH_in[0]), .pin7(OUT[8]), .pin8(1'b0), .pin9(OUT[9]), .pin10(ABH_in[1]), .pin11(_74153_1_pin4[1]),
    .pin12(_74153_1_pin4[1]), .pin13(SS_in[1]), .pin14(ADDR_sel0), .pin15(1'b0), .pin16(1'b1));
  _74153 _74153_2 (
    .pin1(1'b0), .pin2(ADDR_sel1), .pin3(SS_in[2]), .pin4(_74153_1_pin4[2]), .pin5(_74153_1_pin4[2]),
    .pin6(ABH_in[2]), .pin7(OUT[10]), .pin8(1'b0), .pin9(OUT[11]), .pin10(ABH_in[3]),
    .pin11(_74153_1_pin4[3]), .pin12(_74153_1_pin4[3]), .pin13(SS_in[3]), .pin14(ADDR_sel0), .pin15(1'b0),
    .pin16(1'b1));
  _74153 _74153_3 (
    .pin1(1'b0), .pin2(ADDR_sel1), .pin3(SS_in[4]), .pin4(_74153_1_pin4[4]), .pin5(_74153_1_pin4[4]),
    .pin6(ABH_in[4]), .pin7(OUT[12]), .pin8(1'b0), .pin9(OUT[13]), .pin10(ABH_in[5]),
    .pin11(_74153_1_pin4[5]), .pin12(_74153_1_pin4[5]), .pin13(SS_in[5]), .pin14(ADDR_sel0), .pin15(1'b0),
    .pin16(1'b1));
  _74153 _74153_4 (
    .pin1(1'b0), .pin2(ADDR_sel1), .pin3(SS_in[6]), .pin4(_74153_1_pin4[6]), .pin5(_74153_1_pin4[6]),
    .pin6(ABH_in[6]), .pin7(OUT[14]), .pin8(1'b0), .pin9(OUT[15]), .pin10(ABH_in[7]),
    .pin11(_74153_1_pin4[7]), .pin12(_74153_1_pin4[7]), .pin13(SS_in[7]), .pin14(ADDR_sel0), .pin15(1'b0),
    .pin16(1'b1));
  _7408 _7408_1 (
    .pin1(1'b0), .pin2(1'b0), .pin4(1'b0), .pin5(1'b0), .pin7(1'b0), .pin9(1'b0), .pin10(1'b0),
    .pin11(_7408_1_pin11), .pin12(ADDR_sel0), .pin13(ADDR_sel1), .pin14(1'b1));  // open: pin3, pin6, pin8
  _74157 _74157_1 (
    .pin1(_7408_1_pin11), .pin2(ABL_in[0]), .pin3(SP_in[0]), .pin4(OUT[0]), .pin5(ABL_in[1]),
    .pin6(SP_in[1]), .pin7(OUT[1]), .pin8(1'b0), .pin9(OUT[3]), .pin10(SP_in[2]), .pin11(ABL_in[2]),
    .pin12(OUT[2]), .pin13(SP_in[3]), .pin14(ABL_in[3]), .pin15(1'b0), .pin16(1'b1));
  _74157 _74157_2 (
    .pin1(_7408_1_pin11), .pin2(ABL_in[4]), .pin3(SP_in[4]), .pin4(OUT[4]), .pin5(ABL_in[5]),
    .pin6(SP_in[5]), .pin7(OUT[5]), .pin8(1'b0), .pin9(OUT[6]), .pin10(SP_in[6]), .pin11(ABL_in[6]),
    .pin12(OUT[7]), .pin13(SP_in[7]), .pin14(ABL_in[7]), .pin15(1'b0), .pin16(1'b1));
  // also tied to GND on the sheet: {_74153_1_pin4[0], _74153_1_pin4[1], _74153_1_pin4[2], _74153_1_pin4[3], _74153_1_pin4[4], _74153_1_pin4[6], _74153_1_pin4[7]}
  // also tied to VCC on the sheet: _74153_1_pin4[5]
endmodule
