// Digital circuit FLAGSRegister.dig as structural Verilog
module FLAGSRegister (
  input  [7:0] BUS_IN,
  input  C,
  input  nCZN_in,
  input  nR_out,
  input  [2:0] FLAGS_ALU,
  input  I_val,
  input  nI_in,
  input  FLAGSIn_sel,
  output [7:0] BUS_out,
  output [7:0] OUT
);

  wire _74157_1_pin12;
  wire [2:0] _74157_1_pin7;

  _74157 _74157_1 (
    .pin1(FLAGSIn_sel), .pin2(BUS_IN[0]), .pin3(FLAGS_ALU[0]), .pin4(_74157_1_pin7[0]), .pin5(BUS_IN[1]),
    .pin6(FLAGS_ALU[1]), .pin7(_74157_1_pin7[1]), .pin8(1'b0), .pin9(_74157_1_pin7[2]), .pin10(FLAGS_ALU[2]),
    .pin11(BUS_IN[2]), .pin12(_74157_1_pin12), .pin13(I_val), .pin14(BUS_IN[3]), .pin15(1'b0), .pin16(1'b1));
  _74173 _74173_1 (
    .pin1(1'b0), .pin2(1'b0), .pin3(OUT[0]), .pin4(OUT[1]), .pin5(OUT[2]), .pin7(C), .pin8(1'b0),
    .pin9(nCZN_in), .pin10(nCZN_in), .pin11(1'b0), .pin12(_74157_1_pin7[2]), .pin13(_74157_1_pin7[1]),
    .pin14(_74157_1_pin7[0]), .pin15(1'b0), .pin16(1'b1));  // open: pin6
  _74173 _74173_2 (
    .pin1(1'b0), .pin2(1'b0), .pin3(OUT[3]), .pin7(C), .pin8(1'b0), .pin9(nI_in), .pin10(nI_in),
    .pin11(1'b0), .pin12(1'b0), .pin13(1'b0), .pin14(_74157_1_pin12), .pin15(1'b0), .pin16(1'b1));  // open: pin4, pin5, pin6
  _74244 _74244_1 (
    .pin1(nR_out), .pin2(OUT[0]), .pin3(BUS_out[7]), .pin4(OUT[1]), .pin5(BUS_out[6]), .pin6(OUT[2]),
    .pin7(BUS_out[5]), .pin8(OUT[3]), .pin9(BUS_out[4]), .pin10(1'b0), .pin11(OUT[4]), .pin12(BUS_out[3]),
    .pin13(OUT[5]), .pin14(BUS_out[2]), .pin15(OUT[6]), .pin16(BUS_out[1]), .pin17(OUT[7]),
    .pin18(BUS_out[0]), .pin19(nR_out), .pin20(1'b1));
  // also tied to GND on the sheet: {OUT[4], OUT[5], OUT[6], OUT[7]}
endmodule
