// Digital circuit RAM.dig as structural Verilog
module RAM (
  input  [15:0] ABUS_in,
  input  nDout_fbus,
  input  nDout_dbus,
  input  nCLK,
  input  nDE_in,
  input  nDSEL_RAM,
  input  [7:0] DBUS_in,
  output [7:0] FBUS_out,
  output [7:0] DBUS_out
);

  wire _7432_1_pin8, _7432_1_pin11, _74244_1_pin1, a623308a_1_p7, a623308a_1_p11;
  wire [7:0] _74244_1_pin3;

  _74244 _74244_1 (
    .pin1(_74244_1_pin1), .pin2(DBUS_in[0]), .pin3(_74244_1_pin3[7]), .pin4(DBUS_in[1]),
    .pin5(_74244_1_pin3[6]), .pin6(DBUS_in[2]), .pin7(_74244_1_pin3[5]), .pin8(DBUS_in[3]),
    .pin9(_74244_1_pin3[4]), .pin10(1'b0), .pin11(DBUS_in[4]), .pin12(_74244_1_pin3[3]), .pin13(DBUS_in[5]),
    .pin14(_74244_1_pin3[2]), .pin15(DBUS_in[6]), .pin16(_74244_1_pin3[1]), .pin17(DBUS_in[7]),
    .pin18(_74244_1_pin3[0]), .pin19(_74244_1_pin1), .pin20(1'b1));
  // A623308A a623308a_1: pin names not known; wires that end beside it: ABUS_in[12], _74244_1_pin3[0], _74244_1_pin3[1], _74244_1_pin3[2], 1'b0, 1'b1, a623308a_1_p7, ABUS_in[8], ABUS_in[9], ABUS_in[10], a623308a_1_p11, ABUS_in[11], 1'b0, _74244_1_pin3[7]
  _7432 _7432_1 (
    .pin1(nDE_in), .pin2(nDSEL_RAM), .pin3(_74244_1_pin1), .pin4(nCLK), .pin5(_74244_1_pin1),
    .pin6(a623308a_1_p7), .pin7(1'b0), .pin8(_7432_1_pin8), .pin9(nDSEL_RAM), .pin10(nDout_dbus),
    .pin11(_7432_1_pin11), .pin12(nDSEL_RAM), .pin13(nDout_fbus), .pin14(1'b1));
  _7408 _7408_1 (
    .pin1(1'b0), .pin2(1'b0), .pin4(1'b0), .pin5(1'b0), .pin7(1'b0), .pin9(1'b0), .pin10(1'b0),
    .pin11(a623308a_1_p11), .pin12(nDout_fbus), .pin13(nDout_dbus), .pin14(1'b1));  // open: pin3, pin6, pin8
  _74244 _74244_2 (
    .pin1(_7432_1_pin8), .pin2(_74244_1_pin3[0]), .pin3(DBUS_out[7]), .pin4(_74244_1_pin3[1]),
    .pin5(DBUS_out[6]), .pin6(_74244_1_pin3[2]), .pin7(DBUS_out[5]), .pin8(_74244_1_pin3[3]),
    .pin9(DBUS_out[4]), .pin10(1'b0), .pin11(_74244_1_pin3[4]), .pin12(DBUS_out[3]),
    .pin13(_74244_1_pin3[5]), .pin14(DBUS_out[2]), .pin15(_74244_1_pin3[6]), .pin16(DBUS_out[1]),
    .pin17(_74244_1_pin3[7]), .pin18(DBUS_out[0]), .pin19(_7432_1_pin8), .pin20(1'b1));
  _74244 _74244_3 (
    .pin1(_7432_1_pin11), .pin2(_74244_1_pin3[0]), .pin3(FBUS_out[7]), .pin4(_74244_1_pin3[1]),
    .pin5(FBUS_out[6]), .pin6(_74244_1_pin3[2]), .pin7(FBUS_out[5]), .pin8(_74244_1_pin3[3]),
    .pin9(FBUS_out[4]), .pin10(1'b0), .pin11(_74244_1_pin3[4]), .pin12(FBUS_out[3]),
    .pin13(_74244_1_pin3[5]), .pin14(FBUS_out[2]), .pin15(_74244_1_pin3[6]), .pin16(FBUS_out[1]),
    .pin17(_74244_1_pin3[7]), .pin18(FBUS_out[0]), .pin19(_7432_1_pin11), .pin20(1'b1));
endmodule
