// Digital circuit StackPointer.dig as structural Verilog
module StackPointer (
  input  nSP_count,
  input  SP_in,
  input  [7:0] DBUS_in,
  input  SP_down,
  input  CLK,
  input  nSPout,
  output [7:0] OUT,
  output [7:0] DBUS_out
);

  wire _7400_1_pin8, _74191_1_pin13;

  _7400 _7400_1 (
    .pin1(1'b0), .pin2(1'b0), .pin4(1'b0), .pin5(1'b0), .pin7(1'b0), .pin8(_7400_1_pin8), .pin9(SP_in),
    .pin10(CLK), .pin12(1'b0), .pin13(1'b0), .pin14(1'b1));  // open: pin3, pin6, pin11
  _74191 _74191_1 (
    .pin1(DBUS_in[1]), .pin2(OUT[1]), .pin3(OUT[0]), .pin4(nSP_count), .pin5(SP_down), .pin6(OUT[2]),
    .pin7(OUT[3]), .pin8(1'b0), .pin9(DBUS_in[3]), .pin10(DBUS_in[2]), .pin11(_7400_1_pin8),
    .pin13(_74191_1_pin13), .pin14(CLK), .pin15(DBUS_in[0]), .pin16(1'b1));  // open: pin12
  _74191 _74191_2 (
    .pin1(DBUS_in[5]), .pin2(OUT[5]), .pin3(OUT[4]), .pin4(_74191_1_pin13), .pin5(SP_down), .pin6(OUT[6]),
    .pin7(OUT[7]), .pin8(1'b0), .pin9(DBUS_in[7]), .pin10(DBUS_in[6]), .pin11(_7400_1_pin8), .pin14(CLK),
    .pin15(DBUS_in[4]), .pin16(1'b1));  // open: pin12, pin13
  _74244 _74244_1 (
    .pin1(nSPout), .pin2(OUT[0]), .pin3(DBUS_out[7]), .pin4(OUT[1]), .pin5(DBUS_out[6]), .pin6(OUT[2]),
    .pin7(DBUS_out[5]), .pin8(OUT[3]), .pin9(DBUS_out[4]), .pin10(1'b0), .pin11(OUT[4]), .pin12(DBUS_out[3]),
    .pin13(OUT[5]), .pin14(DBUS_out[2]), .pin15(OUT[6]), .pin16(DBUS_out[1]), .pin17(OUT[7]),
    .pin18(DBUS_out[0]), .pin19(nSPout), .pin20(1'b1));
endmodule
