// Logisim project C8BComponents.circ as structural Verilog: 4 circuits, main circuit L_3_state_octal_D_flip_flop_74HC574AP_57ace3e5
module L_3_state_octal_D_flip_flop_74HC574AP_57ace3e5 (
  input  [7:0] D,
  input  CLK,
  input  NOT_OE,
  output [7:0] Q
);

  wire not_1_out;
  wire [7:0] d_ff_8_q;

  not not_1 (not_1_out, NOT_OE);
  D_Flip_Flop d_ff_1 (.D(D[7]), .clk(CLK), .Q(d_ff_8_q[7]));  // open: Qn, preset, reset
  assign Q = not_1_out ? d_ff_8_q : 8'bz;  // Controlled_Buffer controlled_buffer_1
  D_Flip_Flop d_ff_2 (.D(D[6]), .clk(CLK), .Q(d_ff_8_q[6]));  // open: Qn, preset, reset
  D_Flip_Flop d_ff_3 (.D(D[5]), .clk(CLK), .Q(d_ff_8_q[5]));  // open: Qn, preset, reset
  D_Flip_Flop d_ff_4 (.D(D[4]), .clk(CLK), .Q(d_ff_8_q[4]));  // open: Qn, preset, reset
  D_Flip_Flop d_ff_5 (.D(D[3]), .clk(CLK), .Q(d_ff_8_q[3]));  // open: Qn, preset, reset
  D_Flip_Flop d_ff_6 (.D(D[2]), .clk(CLK), .Q(d_ff_8_q[2]));  // open: Qn, preset, reset
  D_Flip_Flop d_ff_7 (.D(D[1]), .clk(CLK), .Q(d_ff_8_q[1]));  // open: Qn, preset, reset
  D_Flip_Flop d_ff_8 (.D(D[0]), .clk(CLK), .Q(d_ff_8_q[0]));  // open: Qn, preset, reset
endmodule

module L_8_bit_universal_shift_storage_register_with_3_state_outputs_SN74ALS299_87cfe9f2 (
  input  S0,
  input  S1,
  input  SL,
  input  SR,
  input  CLK,
  input  NOT_CLR,
  input  NOT_OE1,
  input  NOT_OE2,
  input  [7:0] BUS_IN,
  output QA1,
  output QH1,
  output [7:0] BUS_OUT
);

  wire and_1_out, and_2_out, and_3_out, and_4_out, and_5_out, and_6_out, and_7_out, and_8_out, and_9_out,
       and_10_out, and_11_out, and_12_out, and_13_out, and_14_out, and_15_out, and_16_out, and_17_out,
       and_18_out, and_19_out, and_20_out, and_21_out, and_22_out, and_23_out, and_24_out, and_25_out,
       and_26_out, and_27_out, and_28_out, and_29_out, and_30_out, and_31_out, and_32_out, and_33_out,
       d_ff_2_q, d_ff_3_q, d_ff_4_q, d_ff_5_q, d_ff_6_q, d_ff_7_q, not_1_out, not_2_out, not_3_out,
       not_4_out, not_5_out, not_6_out, not_7_out, or_1_out, or_2_out, or_3_out, or_4_out, or_5_out,
       or_6_out, or_7_out, or_8_out, or_9_out;

  not not_1 (not_1_out, S0);
  not not_2 (not_2_out, S1);
  not not_3 (not_3_out, NOT_CLR);
  not not_4 (not_4_out, not_1_out);
  not not_5 (not_5_out, not_2_out);
  or or_1 (or_1_out, not_2_out, not_1_out);
  and and_1 (and_1_out, SR, not_4_out, not_2_out);
  not not_6 (not_6_out, NOT_OE1);
  and and_2 (and_2_out, or_1_out, not_6_out, not_7_out);
  not not_7 (not_7_out, NOT_OE2);
  and and_3 (and_3_out, not_5_out, not_1_out, d_ff_2_q);
  and and_4 (and_4_out, not_5_out, not_4_out, BUS_IN[7]);
  or or_2 (or_2_out, and_1_out, and_3_out, and_4_out, and_5_out);
  assign BUS_OUT[7] = and_2_out ? QA1 : 1'bz;  // Controlled_Buffer controlled_buffer_1
  and and_5 (and_5_out, not_2_out, not_1_out, QA1);
  D_Flip_Flop d_ff_1 (.D(or_2_out), .clk(CLK), .Q(QA1), .reset(not_3_out));  // open: Qn, preset
  and and_6 (and_6_out, QA1, not_4_out, not_2_out);
  and and_7 (and_7_out, not_5_out, not_1_out, d_ff_3_q);
  and and_8 (and_8_out, not_5_out, not_4_out, BUS_IN[6]);
  or or_3 (or_3_out, and_6_out, and_7_out, and_8_out, and_9_out);
  D_Flip_Flop d_ff_2 (.D(or_3_out), .clk(CLK), .Q(d_ff_2_q), .reset(not_3_out));  // open: Qn, preset
  assign BUS_OUT[6] = and_2_out ? d_ff_2_q : 1'bz;  // Controlled_Buffer controlled_buffer_2
  and and_9 (and_9_out, not_2_out, not_1_out, d_ff_2_q);
  and and_10 (and_10_out, d_ff_2_q, not_4_out, not_2_out);
  assign BUS_OUT[5] = and_2_out ? d_ff_3_q : 1'bz;  // Controlled_Buffer controlled_buffer_3
  and and_11 (and_11_out, not_5_out, not_1_out, d_ff_4_q);
  and and_12 (and_12_out, not_5_out, not_4_out, BUS_IN[5]);
  or or_4 (or_4_out, and_10_out, and_11_out, and_12_out, and_13_out);
  D_Flip_Flop d_ff_3 (.D(or_4_out), .clk(CLK), .Q(d_ff_3_q), .reset(not_3_out));  // open: Qn, preset
  and and_13 (and_13_out, not_2_out, not_1_out, d_ff_3_q);
  and and_14 (and_14_out, not_5_out, not_1_out, d_ff_5_q);
  and and_15 (and_15_out, d_ff_3_q, not_4_out, not_2_out);
  assign BUS_OUT[4] = and_2_out ? d_ff_4_q : 1'bz;  // Controlled_Buffer controlled_buffer_4
  and and_16 (and_16_out, not_5_out, not_4_out, BUS_IN[4]);
  and and_17 (and_17_out, not_2_out, not_1_out, d_ff_4_q);
  or or_5 (or_5_out, and_15_out, and_14_out, and_16_out, and_17_out);
  D_Flip_Flop d_ff_4 (.D(or_5_out), .clk(CLK), .Q(d_ff_4_q), .reset(not_3_out));  // open: Qn, preset
  and and_18 (and_18_out, d_ff_4_q, not_4_out, not_2_out);
  and and_19 (and_19_out, not_5_out, not_1_out, d_ff_6_q);
  assign BUS_OUT[3] = and_2_out ? d_ff_5_q : 1'bz;  // Controlled_Buffer controlled_buffer_5
  and and_20 (and_20_out, not_5_out, not_4_out, BUS_IN[3]);
  and and_21 (and_21_out, not_2_out, not_1_out, d_ff_5_q);
  or or_6 (or_6_out, and_18_out, and_19_out, and_20_out, and_21_out);
  D_Flip_Flop d_ff_5 (.D(or_6_out), .clk(CLK), .Q(d_ff_5_q), .reset(not_3_out));  // open: Qn, preset
  and and_22 (and_22_out, d_ff_5_q, not_4_out, not_2_out);
  and and_23 (and_23_out, not_5_out, not_1_out, d_ff_7_q);
  or or_7 (or_7_out, and_22_out, and_23_out, and_24_out, and_25_out);
  assign BUS_OUT[2] = and_2_out ? d_ff_6_q : 1'bz;  // Controlled_Buffer controlled_buffer_6
  and and_24 (and_24_out, not_5_out, not_4_out, BUS_IN[2]);
  and and_25 (and_25_out, not_2_out, not_1_out, d_ff_6_q);
  D_Flip_Flop d_ff_6 (.D(or_7_out), .clk(CLK), .Q(d_ff_6_q), .reset(not_3_out));  // open: Qn, preset
  and and_26 (and_26_out, d_ff_6_q, not_4_out, not_2_out);
  and and_27 (and_27_out, not_5_out, not_1_out, QH1);
  or or_8 (or_8_out, and_26_out, and_27_out, and_28_out, and_29_out);
  assign BUS_OUT[1] = and_2_out ? d_ff_7_q : 1'bz;  // Controlled_Buffer controlled_buffer_7
  and and_28 (and_28_out, not_5_out, not_4_out, BUS_IN[1]);
  and and_29 (and_29_out, not_2_out, not_1_out, d_ff_7_q);
  D_Flip_Flop d_ff_7 (.D(or_8_out), .clk(CLK), .Q(d_ff_7_q), .reset(not_3_out));  // open: Qn, preset
  and and_30 (and_30_out, d_ff_7_q, not_4_out, not_2_out);
  and and_31 (and_31_out, not_5_out, not_1_out, SL);
  and and_32 (and_32_out, not_5_out, not_4_out, BUS_IN[0]);
  or or_9 (or_9_out, and_30_out, and_31_out, and_32_out, and_33_out);
  D_Flip_Flop d_ff_8 (.D(or_9_out), .clk(CLK), .Q(QH1), .reset(not_3_out));  // open: Qn, preset
  assign BUS_OUT[0] = and_2_out ? QH1 : 1'bz;  // Controlled_Buffer controlled_buffer_8
  and and_33 (and_33_out, not_2_out, not_1_out, QH1);

  // Notes on the sheet:
  //   CLK: pull=down
  //   NOT_CLR: pull=down
  //   NOT_OE1: pull=down
  //   NOT_OE2: pull=down
  //   S1: pull=down
  //   SR: pull=down
  //   S0: pull=down
  //   SL: pull=down
  //   QH1: pull=down
endmodule

module EdgeDetector (
  input  D,
  output PULSE
);

  wire not_1_out, not_2_out, not_3_out;

  not not_1 (not_1_out, D);
  not not_2 (not_2_out, not_1_out);
  not not_3 (not_3_out, not_2_out);
  and and_1 (PULSE, not_3_out, D);
endmodule

module L_4_bit_bidir_univ_shift_register_sn74194 (
  input  SL_SERIAL,
  input  [3:0] DATA_IN,
  input  SR_SERIAL,
  input  CLK,
  input  NOT_CLR,
  input  S0,
  input  S1,
  output [3:0] DATA_OUT
);

  wire and_1_out, and_2_out, and_3_out, and_4_out, and_5_out, and_6_out, and_7_out, and_8_out, and_9_out,
       and_10_out, and_11_out, and_12_out, and_13_out, nor_1_out, nor_2_out, nor_3_out, nor_4_out, nor_5_out,
       nor_6_out, not_1_out, not_2_out, not_3_out, not_4_out, not_5_out, not_6_out, not_7_out, not_8_out;

  nor nor_1 (nor_1_out, not_1_out, not_2_out);
  not not_1 (not_1_out, S0);
  not not_2 (not_2_out, S1);
  and and_1 (and_1_out, SL_SERIAL, not_1_out);
  and and_2 (and_2_out, DATA_IN[0], nor_1_out);
  and and_3 (and_3_out, not_2_out, DATA_OUT[1]);
  and and_4 (and_4_out, DATA_OUT[0], not_1_out);
  and and_5 (and_5_out, DATA_IN[1], nor_1_out);
  and and_6 (and_6_out, not_2_out, DATA_OUT[2]);
  and and_7 (and_7_out, DATA_OUT[1], not_1_out);
  and and_8 (and_8_out, DATA_IN[2], nor_1_out);
  and and_9 (and_9_out, DATA_OUT[3], not_2_out);
  and and_10 (and_10_out, DATA_OUT[2], not_1_out);
  and and_11 (and_11_out, DATA_IN[3], nor_1_out);
  and and_12 (and_12_out, not_2_out, SR_SERIAL);
  S_R_Flip_Flop s_r_ff_1 (
    .S(not_3_out), .R(nor_2_out), .clk(not_7_out), .Q(DATA_OUT[0]), .reset(not_8_out));  // open: Qn, preset
  nor nor_2 (nor_2_out, and_1_out, and_2_out, and_3_out);
  not not_3 (not_3_out, nor_2_out);
  S_R_Flip_Flop s_r_ff_2 (
    .S(not_4_out), .R(nor_3_out), .clk(not_7_out), .Q(DATA_OUT[1]), .reset(not_8_out));  // open: Qn, preset
  nor nor_3 (nor_3_out, and_4_out, and_5_out, and_6_out);
  not not_4 (not_4_out, nor_3_out);
  S_R_Flip_Flop s_r_ff_3 (
    .S(not_5_out), .R(nor_4_out), .clk(not_7_out), .Q(DATA_OUT[2]), .reset(not_8_out));  // open: Qn, preset
  nor nor_4 (nor_4_out, and_7_out, and_8_out, and_9_out);
  not not_5 (not_5_out, nor_4_out);
  S_R_Flip_Flop s_r_ff_4 (
    .S(not_6_out), .R(nor_5_out), .clk(not_7_out), .Q(DATA_OUT[3]), .reset(not_8_out));  // open: Qn, preset
  nor nor_5 (nor_5_out, and_10_out, and_11_out, and_12_out);
  not not_6 (not_6_out, nor_5_out);
  not not_7 (not_7_out, nor_6_out);
  nor nor_6 (nor_6_out, and_13_out, CLK);
  and and_13 (and_13_out, not_1_out, not_2_out);
  not not_8 (not_8_out, NOT_CLR);
endmodule
