// Logisim project Computer8Bit.circ as structural Verilog
module main (
);

  wire ADDR_SEL0, ADDR_SEL1, BASE_CLK, C1, C2, C3, C4, CSPC_UP, FLAGS_MODE_SEL0, FLAGS_MODE_SEL1,
       FLAGS_MODE_SEL2, J, JC, JN, JZ, keyboard_1_avail, nor_1_out, nor_2_out, nor_3_out, nor_4_out,
       nor_5_out, nor_6_out, not_1_out, not_2_out, NOT_ABH_IN, NOT_ABL_IN, NOT_BP_IN, NOT_BP_OUT, NOT_CS_IN,
       NOT_CS_OUT, NOT_DATA_LATCH_OUT, NOT_DEVICE_IN, NOT_DEVICE_OE, NOT_DEVICE_OUT, NOT_DEVICE_SEL_0,
       NOT_DEVICE_SEL_1, NOT_DEVICE_SEL_2, NOT_DEVICE_SEL_3, NOT_DEVICE_SEL_4, NOT_DEVICE_SEL_5,
       NOT_DEVICE_SEL_RAM, NOT_DEVICE_SEL_ROM, NOT_DS_IN, NOT_DS_OUT, NOT_FETCH, NOT_FLAGS_OUT, NOT_HLT,
       NOT_IRQ, NOT_IVH_OUT, NOT_IVL_OUT, NOT_PASS, NOT_PC_IN, NOT_PC_INC, NOT_PC_OUT, NOT_RA_OUT, NOT_RB_IN,
       NOT_RB_OUT, NOT_RC_IN, NOT_RC_OUT, NOT_RD_IN, NOT_RD_OUT, NOT_RT_IN, NOT_RT_OUT, NOT_SP_OUT,
       NOT_SS_IN, NOT_SS_OUT, OP_SEL0, OP_SEL1, OP_SEL2, PHI1, PHI2, RA_S0, RA_S1, RESET, RESET_BTN_out,
       rgb_video_1_p1, rgb_video_1_p2, rgb_video_1_p3, rgb_video_1_p4, rgb_video_1_p5, rgb_video_1_p6,
       SP_MODE_SEL0, SP_MODE_SEL1, switch_1_p2, ttyadapter_1_k_clear, ttyadapter_1_k_clk,
       ttyadapter_1_k_read_en, ttyadapter_1_tty_clr, ttyadapter_1_tty_we, X_SEL0, X_SEL1, X_SEL2, Y_SEL0,
       Y_SEL1, Y_SEL2;
  wire [2:0] alu_1_flags;
  wire [3:0] controlunit_1_microinstr_ct_out, FLAGS_VAL, joystick_1_x, joystick_1_y;
  wire [6:0] keyboard_1_data, ttyadapter_1_tty_data;
  wire [7:0] ABH_q, ABL_VAL, aluoperandselector_1_out_async, aluoperandselector_2_out_async,
       aluoperatorselector_1_op_out, BP_VAL, bufferedregister_1_async_out, controlunit_1_ir_out, DBUS,
       DL_VAL, DS_async_out, joystickadapter_1_async_out, RA_VAL, RB_VAL, RC_VAL, RD_VAL,
       rgbscreenadapter_1_p7, RT_VAL, SP_VAL, SS_VAL, ttyadapter_1_async_out, undriven;
  wire [15:0] ABUS, CS_PC;

  // Digital_Oscilloscope #(.frontlines("no"), .showclock("false")) digital_oscilloscope_1: pin names not known; wires that end beside it: BASE_CLK, PHI1, C1, C3
  // Probe on controlunit_1_ir_out
  // Probe on controlunit_1_microinstr_ct_out
  // Probe on CS_PC
  // Probe on ABUS
  // Probe on DBUS
  // Probe on bufferedregister_1_async_out
  // Probe on RA_VAL
  // Probe on RB_VAL
  // Probe on RC_VAL
  // Probe on RD_VAL
  // Probe on RT_VAL
  // Probe on DL_VAL
  // Probe on SS_VAL
  // Probe on SP_VAL
  // Probe on FLAGS_VAL
  Pull_Resistor #(.pull(1)) pull_resistor_1 (.node(NOT_IRQ));
  // DipSwitch dipswitch_1: pin names not known
  assign DBUS = switch_1_p2 ? undriven : 8'bz;  // Controlled_Buffer controlled_buffer_1
  // Switch switch_1: pin names not known; wires that end beside it: 1'b1, switch_1_p2
  Pull_Resistor pull_resistor_2 (.node(switch_1_p2));
  Hex_Digit_Display hex_digit_display_1 (.value(DBUS[7:4]));  // open: dp
  Hex_Digit_Display hex_digit_display_2 (.value(DBUS[3:0]));  // open: dp
  ControlUnit controlunit_1 (
    .IR_IN(bufferedregister_1_async_out), .NOT_IRQ(NOT_IRQ), .RESET(RESET), .CLK(C1), .I(FLAGS_VAL[3]),
    .MICROINSTR_CT_OUT(controlunit_1_microinstr_ct_out), .IR_OUT(controlunit_1_ir_out), .RA_S0(RA_S0),
    .RA_S1(RA_S1), .NOT_RA_OUT(NOT_RA_OUT), .NOT_DEVICE_IN(NOT_DEVICE_IN), .NOT_DEVICE_OUT(NOT_DEVICE_OUT),
    .NOT_SS_IN(NOT_SS_IN), .NOT_SS_OUT(NOT_SS_OUT), .SP_MODE_SEL0(SP_MODE_SEL0), .NOT_RB_IN(NOT_RB_IN),
    .NOT_RC_IN(NOT_RC_IN), .NOT_RD_IN(NOT_RD_IN), .SP_MODE_SEL1(SP_MODE_SEL1), .NOT_SP_OUT(NOT_SP_OUT),
    .NOT_ABH_IN(NOT_ABH_IN), .NOT_ABL_IN(NOT_ABL_IN), .NOT_RB_OUT(NOT_RB_OUT), .NOT_RC_OUT(NOT_RC_OUT),
    .NOT_RD_OUT(NOT_RD_OUT), .NOT_RT_IN(NOT_RT_IN), .NOT_RT_OUT(NOT_RT_OUT), .X_SEL0(X_SEL0),
    .X_SEL1(X_SEL1), .X_SEL2(X_SEL2), .Y_SEL0(Y_SEL0), .Y_SEL1(Y_SEL1), .Y_SEL2(Y_SEL2), .OP_SEL0(OP_SEL0),
    .OP_SEL1(OP_SEL1), .OP_SEL2(OP_SEL2), .NOT_CS_IN(NOT_CS_IN), .NOT_PC_IN(NOT_PC_IN),
    .NOT_PC_INC(NOT_PC_INC), .NOT_CS_OUT(NOT_CS_OUT), .NOT_PC_OUT(NOT_PC_OUT), .NOT_BP_IN(NOT_BP_IN),
    .NOT_BP_OUT(NOT_BP_OUT), .J(J), .JC(JC), .JZ(JZ), .JN(JN), .NOT_PASS(NOT_PASS), .NOT_HLT(NOT_HLT),
    .ADDR_SEL0(ADDR_SEL0), .ADDR_SEL1(ADDR_SEL1), .NOT_FETCH(NOT_FETCH),
    .NOT_DATA_LATCH_OUT(NOT_DATA_LATCH_OUT), .NOT_IVH_OUT(NOT_IVH_OUT), .NOT_IVL_OUT(NOT_IVL_OUT),
    .FLAGS_MODE_SEL0(FLAGS_MODE_SEL0), .FLAGS_MODE_SEL1(FLAGS_MODE_SEL1), .FLAGS_MODE_SEL2(FLAGS_MODE_SEL2),
    .NOT_FLAGS_OUT(NOT_FLAGS_OUT), .CSPC_UP(CSPC_UP), .NOT_DS_IN(NOT_DS_IN), .NOT_DS_OUT(NOT_DS_OUT));
  LED led_1 (.in(RA_S0));
  LED led_2 (.in(RA_S1));
  LED led_3 (.in(NOT_RA_OUT));
  LED led_4 (.in(NOT_DEVICE_IN));
  LED led_5 (.in(NOT_DEVICE_OUT));
  LED led_6 (.in(NOT_SS_IN));
  LED led_7 (.in(NOT_SS_OUT));
  LED led_8 (.in(SP_MODE_SEL0));
  LED led_9 (.in(NOT_RB_IN));
  LED led_10 (.in(NOT_RC_IN));
  LED led_11 (.in(NOT_RD_IN));
  LED led_12 (.in(SP_MODE_SEL1));
  LED led_13 (.in(NOT_SP_OUT));
  LED led_14 (.in(NOT_ABH_IN));
  LED led_15 (.in(NOT_ABL_IN));
  LED led_16 (.in(NOT_RB_OUT));
  LED led_17 (.in(NOT_RC_OUT));
  LED led_18 (.in(NOT_RD_OUT));
  LED led_19 (.in(NOT_RT_IN));
  LED led_20 (.in(NOT_RT_OUT));
  LED led_21 (.in(X_SEL0));
  LED led_22 (.in(X_SEL1));
  LED led_23 (.in(X_SEL2));
  LED led_24 (.in(Y_SEL0));
  LED led_25 (.in(Y_SEL1));
  LED led_26 (.in(Y_SEL2));
  LED led_27 (.in(OP_SEL0));
  LED led_28 (.in(OP_SEL1));
  LED led_29 (.in(OP_SEL2));
  LED led_30 (.in(NOT_CS_IN));
  LED led_31 (.in(NOT_PC_IN));
  LED led_32 (.in(NOT_PC_INC));
  LED led_33 (.in(NOT_CS_OUT));
  LED led_34 (.in(NOT_PC_OUT));
  LED led_35 (.in(NOT_BP_IN));
  LED led_36 (.in(NOT_BP_OUT));
  LED led_37 (.in(J));
  LED led_38 (.in(JC));
  LED led_39 (.in(JZ));
  LED led_40 (.in(JN));
  LED led_41 (.in(NOT_PASS));
  LED led_42 (.in(NOT_HLT));
  LED led_43 (.in(ADDR_SEL0));
  LED led_44 (.in(ADDR_SEL1));
  LED led_45 (.in(NOT_FETCH));
  LED led_46 (.in(NOT_DATA_LATCH_OUT));
  LED led_47 (.in(NOT_IVH_OUT));
  LED led_48 (.in(NOT_IVL_OUT));
  LED led_49 (.in(FLAGS_MODE_SEL0));
  LED led_50 (.in(FLAGS_MODE_SEL1));
  LED led_51 (.in(FLAGS_MODE_SEL2));
  LED led_52 (.in(NOT_FLAGS_OUT));
  LED led_53 (.in(CSPC_UP));
  LED led_54 (.in(NOT_DS_IN));
  LED led_55 (.in(NOT_DS_OUT));
  nor nor_1 (nor_1_out, NOT_DEVICE_OE, NOT_DEVICE_SEL_0);
  TTY #(.cols(56), .rows(24)) tty_1 (
    .data(ttyadapter_1_tty_data), .clk(C4), .we(ttyadapter_1_tty_we), .clr(ttyadapter_1_tty_clr));
  Keyboard keyboard_1 (
    .clk(ttyadapter_1_k_clk), .re(ttyadapter_1_k_read_en), .clr(ttyadapter_1_k_clear),
    .avail(keyboard_1_avail), .data(keyboard_1_data));
  Hex_Digit_Display hex_digit_display_3 (.value(ABUS[11:8]));  // open: dp
  Hex_Digit_Display hex_digit_display_4 (.value(ABUS[15:12]));  // open: dp
  Button RESET_BTN (.out(RESET_BTN_out));
  TTYAdapter ttyadapter_1 (
    .K_AVAIL(keyboard_1_avail), .K_DATA(keyboard_1_data), .BUS_IN(DBUS), .ABUS(ABUS),
    .NOT_DEVICE_IN(NOT_DEVICE_IN), .NOT_DEVICE_OE(NOT_DEVICE_OE), .NOT_DEVICE_SEL(NOT_DEVICE_SEL_0),
    .CLK(C4), .NOT_IRQ(NOT_IRQ), .ASYNC_OUT(ttyadapter_1_async_out), .K_READ_EN(ttyadapter_1_k_read_en),
    .TTY_DATA(ttyadapter_1_tty_data), .K_CLEAR(ttyadapter_1_k_clear), .K_CLK(ttyadapter_1_k_clk),
    .TTY_WE(ttyadapter_1_tty_we), .TTY_CLR(ttyadapter_1_tty_clr));
  Hex_Digit_Display hex_digit_display_5 (.value(ABUS[7:4]));  // open: dp
  Hex_Digit_Display hex_digit_display_6 (.value(ABUS[3:0]));  // open: dp
  Register ABH (.D(DBUS), .en(not_1_out), .clk(C4), .Q(ABH_q));  // open: clr
  not not_1 (not_1_out, NOT_ABH_IN);
  Register ABL (.D(DBUS), .en(not_2_out), .clk(C4), .Q(ABL_VAL));  // open: clr
  not not_2 (not_2_out, NOT_ABL_IN);
  assign DBUS = nor_1_out ? ttyadapter_1_async_out : 8'bz;  // Controlled_Buffer controlled_buffer_2
  ResetCircuit resetcircuit_1 (.RESET_BTN(RESET_BTN_out), .PHASE(PHI1), .RESET_OUT(RESET));
  DeviceOEPhaseSelector deviceoephaseselector_1 (
    .NOT_DEVICE_OUT(NOT_DEVICE_OUT), .NOT_FETCH(NOT_FETCH), .PHI1(PHI1), .PHI2(PHI2),
    .NOT_DEVICE_OE(NOT_DEVICE_OE));
  BufferedRegister DS (
    .BUS_IN(DBUS), .CLK(C4), .NOT_R_IN(NOT_DS_IN), .NOT_R_OUT(NOT_DS_OUT), .NOT_ENABLE(PHI1),
    .ASYNC_OUT(DS_async_out), .BUS_OUT(DBUS));  // open: RESET
  BufferedRegister BP (
    .BUS_IN(DBUS), .CLK(C4), .NOT_R_IN(NOT_BP_IN), .NOT_R_OUT(NOT_BP_OUT), .NOT_ENABLE(PHI1),
    .ASYNC_OUT(BP_VAL), .BUS_OUT(DBUS));  // open: RESET
  AddressSelector addressselector_1 (
    .ABL_in(ABL_VAL), .ABH_in(ABH_q), .DS_IN(DS_async_out), .SS_SP_in({SS_VAL, SP_VAL}), .CS_PC_in(CS_PC),
    .ADDR_SEL0(ADDR_SEL0), .ADDR_SEL1(ADDR_SEL1), .CSPC_override(PHI1), .ADDR_OUT(ABUS));
  AddrDecoder addrdecoder_1 (
    .ABUS(ABUS), .NOT_DEVICE_SEL_ROM(NOT_DEVICE_SEL_ROM), .NOT_DEVICE_SEL_RAM(NOT_DEVICE_SEL_RAM),
    .NOT_DEVICE_SEL_0(NOT_DEVICE_SEL_0), .NOT_DEVICE_SEL_1(NOT_DEVICE_SEL_1),
    .NOT_DEVICE_SEL_2(NOT_DEVICE_SEL_2), .NOT_DEVICE_SEL_3(NOT_DEVICE_SEL_3),
    .NOT_DEVICE_SEL_4(NOT_DEVICE_SEL_4), .NOT_DEVICE_SEL_5(NOT_DEVICE_SEL_5));
  BufferedRegister SS (
    .BUS_IN(DBUS), .CLK(C3), .NOT_R_IN(NOT_SS_IN), .NOT_R_OUT(NOT_SS_OUT), .NOT_ENABLE(PHI1),
    .ASYNC_OUT(SS_VAL), .BUS_OUT(DBUS));  // open: RESET
  StackPointer SP (
    .SP_MODE_SEL0(SP_MODE_SEL0), .SP_MODE_SEL1(SP_MODE_SEL1), .NOT_OUT(NOT_SP_OUT), .NOT_OE(PHI1), .CLK(C3),
    .DBUS(DBUS), .ASYNC_OUT(SP_VAL), .BUS_OUT(DBUS));
  CodeSegment_ProgramCounter CSPC (
    .FLAGS(FLAGS_VAL), .J(J), .JC(JC), .JZ(JZ), .JN(JN), .NOT_PC_IN(NOT_PC_IN), .NOT_CS_IN(NOT_CS_IN),
    .NOT_PC_INC(NOT_PC_INC), .RESET(RESET), .ABUS(ABUS), .CLK(C3), .CSPC_UP(CSPC_UP),
    .NOT_PC_OUT(NOT_PC_OUT), .NOT_CS_OUT(NOT_CS_OUT), .NOT_OE(PHI1), .CS_PC(CS_PC), .BUS_OUT(DBUS));
  TwoPhaseClock twophaseclock_1 (
    .NOT_HLT(NOT_HLT), .BASE_CLK(BASE_CLK), .PHI1(PHI1), .PHI2(PHI2), .C1(C1), .C2(C2), .C3(C3), .C4(C4));
  RAMModule RAM (
    .ABUS(ABUS), .CLK(C4), .BUS_IN(DBUS), .NOT_DEVICE_IN(NOT_DEVICE_IN),
    .NOT_DEVICE_SEL_RAM(NOT_DEVICE_SEL_RAM), .NOT_RAM_OE(NOT_DEVICE_OE), .DBUS_OUT(DBUS));
  ROMModule ROM (.ABUS(ABUS), .NOT_DEVICE_SEL_ROM(NOT_DEVICE_SEL_ROM), .NOT_ROM_OE(NOT_DEVICE_OE), .DBUS(DBUS));
  BufferedRegister bufferedregister_1 (
    .BUS_IN(DBUS), .CLK(C2), .NOT_R_IN(NOT_FETCH), .NOT_R_OUT(NOT_DATA_LATCH_OUT), .NOT_ENABLE(PHI1),
    .RESET(RESET), .ASYNC_OUT(bufferedregister_1_async_out), .BUS_OUT(DBUS));
  BufferedRegister bufferedregister_2 (
    .BUS_IN(DBUS), .CLK(C4), .NOT_R_IN(NOT_RT_IN), .NOT_R_OUT(NOT_RT_OUT), .NOT_ENABLE(PHI1), .RESET(RESET),
    .ASYNC_OUT(RT_VAL), .BUS_OUT(DBUS));
  nor nor_2 (nor_2_out, NOT_DEVICE_SEL_2, NOT_DEVICE_OE);
  // RGB_Video #(.cursor("No Cursor"), .height(32), .reset("Synchronous"), .scale(8), .width(64)) rgb_video_1: pin names not known; wires that end beside it: rgb_video_1_p1, rgb_video_1_p2, rgb_video_1_p3, rgb_video_1_p4, rgb_video_1_p5, rgb_video_1_p6
  nor nor_3 (nor_3_out, PHI1, NOT_IVL_OUT);
  assign DBUS = nor_3_out ? {8{1'b0}} : 8'bz;  // Controlled_Buffer controlled_buffer_3
  assign DBUS = nor_4_out ? 8'h1f : 8'bz;  // Controlled_Buffer controlled_buffer_4
  nor nor_4 (nor_4_out, PHI1, NOT_IVH_OUT);
  // RGBScreenAdapter rgbscreenadapter_1: pin names not known; wires that end beside it: DBUS, ABUS, NOT_DEVICE_IN, NOT_DEVICE_OE, NOT_DEVICE_SEL_2, C3, rgbscreenadapter_1_p7, rgb_video_1_p1, rgb_video_1_p2, rgb_video_1_p3, rgb_video_1_p4, rgb_video_1_p5, rgb_video_1_p6
  assign DBUS = nor_2_out ? rgbscreenadapter_1_p7 : 8'bz;  // Controlled_Buffer controlled_buffer_5
  BufferedRegister RC (
    .BUS_IN(DBUS), .CLK(C4), .NOT_R_IN(NOT_RC_IN), .NOT_R_OUT(NOT_RC_OUT), .NOT_ENABLE(PHI1),
    .ASYNC_OUT(RC_VAL), .BUS_OUT(DBUS));  // open: RESET
  Hex_Digit_Display hex_digit_display_7 (.value(RC_VAL[7:4]));  // open: dp
  ShiftRegister RA (
    .S0(RA_S0), .S1(RA_S1), .CLK(C4), .BUS_IN(DBUS), .NOT_OE(NOT_RA_OUT), .NOT_ENABLE(PHI1),
    .ASYNC_OUT(RA_VAL), .BUS_OUT(DBUS));
  Hex_Digit_Display hex_digit_display_8 (.value(RA_VAL[7:4]));  // open: dp
  Hex_Digit_Display hex_digit_display_9 (.value(RC_VAL[3:0]));  // open: dp
  Hex_Digit_Display hex_digit_display_10 (.value(RA_VAL[3:0]));  // open: dp
  ALUOperandSelector aluoperandselector_1 (
    .SEL0(X_SEL0), .SEL1(X_SEL1), .SEL2(X_SEL2), .A_ASYNC(RA_VAL), .B_ASYNC(RB_VAL), .C_ASYNC(RC_VAL),
    .D_ASYNC(RD_VAL), .E_ASYNC(ABL_VAL), .F_ASYNC(SP_VAL), .G_ASYNC(BP_VAL), .H_ASYNC(8'h1),
    .OUT_ASYNC(aluoperandselector_1_out_async));
  Joystick joystick_1 (.x(joystick_1_x), .y(joystick_1_y));
  nor nor_5 (nor_5_out, NOT_DEVICE_SEL_3, NOT_DEVICE_OE);
  BufferedRegister RB (
    .BUS_IN(DBUS), .CLK(C4), .NOT_R_IN(NOT_RB_IN), .NOT_R_OUT(NOT_RB_OUT), .NOT_ENABLE(PHI1),
    .ASYNC_OUT(RB_VAL), .BUS_OUT(DBUS));  // open: RESET
  ALUOperandSelector aluoperandselector_2 (
    .SEL0(Y_SEL0), .SEL1(Y_SEL1), .SEL2(Y_SEL2), .A_ASYNC(RA_VAL), .B_ASYNC(RB_VAL), .C_ASYNC(RC_VAL),
    .D_ASYNC(RD_VAL), .E_ASYNC(RT_VAL), .F_ASYNC(SP_VAL), .G_ASYNC(BP_VAL), .H_ASYNC(8'h1),
    .OUT_ASYNC(aluoperandselector_2_out_async));
  Hex_Digit_Display hex_digit_display_11 (.value(joystick_1_y));  // open: dp
  BufferedRegister RD (
    .BUS_IN(DBUS), .CLK(C4), .NOT_R_IN(NOT_RD_IN), .NOT_R_OUT(NOT_RD_OUT), .NOT_ENABLE(PHI1),
    .ASYNC_OUT(RD_VAL), .BUS_OUT(DBUS));  // open: RESET
  Hex_Digit_Display hex_digit_display_12 (.value(RD_VAL[7:4]));  // open: dp
  Hex_Digit_Display hex_digit_display_13 (.value(RD_VAL[3:0]));  // open: dp
  Hex_Digit_Display hex_digit_display_14 (.value(RB_VAL[7:4]));  // open: dp
  Hex_Digit_Display hex_digit_display_15 (.value(RB_VAL[3:0]));  // open: dp
  JoystickAdapter joystickadapter_1 (
    .DBUS_IN(DBUS), .ABUS(ABUS), .NOT_DEVICE_IN(NOT_DEVICE_IN), .NOT_DEVICE_OE(NOT_DEVICE_OE),
    .NOT_DEVICE_SEL(NOT_DEVICE_SEL_3), .CLK(C3), .JX_IN(joystick_1_x), .JY_IN(joystick_1_y),
    .ASYNC_OUT(joystickadapter_1_async_out));
  assign DBUS = nor_5_out ? joystickadapter_1_async_out : 8'bz;  // Controlled_Buffer controlled_buffer_6
  ALUOperatorSelector aluoperatorselector_1 (
    .OP_SEL0(OP_SEL0), .OP_SEL1(OP_SEL1), .OP_SEL2(OP_SEL2), .OP_OUT(aluoperatorselector_1_op_out));
  ALU alu_1 (
    .OPERATORS(aluoperatorselector_1_op_out), .O1(aluoperandselector_1_out_async),
    .O2(aluoperandselector_2_out_async), .NOT_ENABLE(PHI1), .BUS_OUT(DBUS), .FLAGS(alu_1_flags));
  FLAGSRegister FLAGS (
    .MODE2(FLAGS_MODE_SEL2), .MODE1(FLAGS_MODE_SEL1), .MODE0(FLAGS_MODE_SEL0), .BUS_IN(DBUS),
    .ALU_IN(alu_1_flags), .CLK(C4), .FLAGS_OUT(FLAGS_VAL));
  LED led_56 (.in(FLAGS_VAL[3]));
  LED led_57 (.in(FLAGS_VAL[2]));
  LED led_58 (.in(FLAGS_VAL[1]));
  LED led_59 (.in(FLAGS_VAL[0]));
  nor nor_6 (nor_6_out, PHI1, NOT_FLAGS_OUT);
  assign DBUS = nor_6_out ? {4'b0000, FLAGS_VAL} : 8'bz;  // Controlled_Buffer controlled_buffer_7

  // Notes on the sheet:
  //   IR
  //   CS_PC
  //   ABUS
  //   DBUS
  //   DL
  //   RA
  //   RB
  //   RC
  //   RD
  //   RT
  //   DL
  //   SS
  //   SP
  //   INZC
  //   Click here with the poke tool to type into the serial port ->
  //   Write to bus
  //   Data bus
  //   Address bus
  //   Clock
  //   RAM
  //   ROM
  //   DATA LATCH
  //   RT
  //   RC
  //   RA
  //   ALU_OPERAND_SELECTORS
  //   RD
  //   RB
  //   ALU_OPERATOR_SELECTOR
  //   I
  //   N
  //   Z
  //   C
endmodule

module ShiftRegister (
  input  S0,
  input  S1,
  input  CLK,
  input  [7:0] BUS_IN,
  input  NOT_OE,
  input  NOT_ENABLE,
  output [7:0] ASYNC_OUT,
  output [7:0] BUS_OUT
);

  wire nor_1_out;

  nor nor_1 (nor_1_out, NOT_OE, NOT_ENABLE);
  L_4_bit_bidir_univ_shift_register_sn74194 l_4_bit_bidir_univ_shift_register_sn74194_1 (
    .SL_SERIAL(ASYNC_OUT[3]), .DATA_IN(BUS_IN[7:4]), .SR_SERIAL(1'b0), .CLK(CLK), .NOT_CLR(1'b1), .S0(S0),
    .S1(S1), .DATA_OUT(ASYNC_OUT[7:4]));
  L_4_bit_bidir_univ_shift_register_sn74194 l_4_bit_bidir_univ_shift_register_sn74194_2 (
    .SL_SERIAL(1'b0), .DATA_IN(BUS_IN[3:0]), .SR_SERIAL(ASYNC_OUT[4]), .CLK(CLK), .NOT_CLR(1'b1), .S0(S0),
    .S1(S1), .DATA_OUT(ASYNC_OUT[3:0]));
  assign BUS_OUT = nor_1_out ? ASYNC_OUT : 8'bz;  // Controlled_Buffer controlled_buffer_1
endmodule

module BufferedRegister (
  input  [7:0] BUS_IN,
  input  CLK,
  input  NOT_R_IN,
  input  NOT_R_OUT,
  input  NOT_ENABLE,
  input  RESET,
  output [7:0] ASYNC_OUT,
  output [7:0] BUS_OUT
);

  wire nor_1_out, not_1_out;

  Register register_1 (.D(BUS_IN), .en(not_1_out), .clk(CLK), .Q(ASYNC_OUT), .clr(RESET));
  not not_1 (not_1_out, NOT_R_IN);
  nor nor_1 (nor_1_out, NOT_R_OUT, NOT_ENABLE);
  assign BUS_OUT = nor_1_out ? ASYNC_OUT : 8'bz;  // Controlled_Buffer controlled_buffer_1
endmodule

module ALUOperandSelector (
  input  SEL0,
  input  SEL1,
  input  SEL2,
  input  [7:0] A_ASYNC,
  input  [7:0] B_ASYNC,
  input  [7:0] C_ASYNC,
  input  [7:0] D_ASYNC,
  input  [7:0] E_ASYNC,
  input  [7:0] F_ASYNC,
  input  [7:0] G_ASYNC,
  input  [7:0] H_ASYNC,
  output [7:0] OUT_ASYNC
);

  wire decoder_1_out0, decoder_1_out1, decoder_1_out2, decoder_1_out3, decoder_1_out4, decoder_1_out5,
       decoder_1_out6, decoder_1_out7;

  Decoder #(.select(3)) decoder_1 (
    .out0(decoder_1_out0), .out1(decoder_1_out1), .out2(decoder_1_out2), .out3(decoder_1_out3),
    .out4(decoder_1_out4), .out5(decoder_1_out5), .out6(decoder_1_out6), .out7(decoder_1_out7),
    .sel({SEL2, SEL1, SEL0}), .en(1'b1));
  assign OUT_ASYNC = decoder_1_out6 ? G_ASYNC : 8'bz;  // Controlled_Buffer controlled_buffer_1
  assign OUT_ASYNC = decoder_1_out7 ? H_ASYNC : 8'bz;  // Controlled_Buffer controlled_buffer_2
  assign OUT_ASYNC = decoder_1_out0 ? A_ASYNC : 8'bz;  // Controlled_Buffer controlled_buffer_3
  assign OUT_ASYNC = decoder_1_out1 ? B_ASYNC : 8'bz;  // Controlled_Buffer controlled_buffer_4
  assign OUT_ASYNC = decoder_1_out2 ? C_ASYNC : 8'bz;  // Controlled_Buffer controlled_buffer_5
  assign OUT_ASYNC = decoder_1_out3 ? D_ASYNC : 8'bz;  // Controlled_Buffer controlled_buffer_6
  assign OUT_ASYNC = decoder_1_out4 ? E_ASYNC : 8'bz;  // Controlled_Buffer controlled_buffer_7
  assign OUT_ASYNC = decoder_1_out5 ? F_ASYNC : 8'bz;  // Controlled_Buffer controlled_buffer_8
endmodule

module ALUOperatorSelector (
  input  OP_SEL0,
  input  OP_SEL1,
  input  OP_SEL2,
  output [7:0] OP_OUT
);

  Decoder #(.select(3)) decoder_1 (
    .out0(OP_OUT[0]), .out1(OP_OUT[1]), .out2(OP_OUT[2]), .out3(OP_OUT[3]), .out4(OP_OUT[4]),
    .out5(OP_OUT[5]), .out6(OP_OUT[6]), .out7(OP_OUT[7]), .sel({OP_SEL2, OP_SEL1, OP_SEL0}), .en(1'b1));
endmodule

module FLAGSRegister (
  input  MODE2,
  input  MODE1,
  input  MODE0,
  input  [7:0] BUS_IN,
  input  [2:0] ALU_IN,
  input  CLK,
  output [3:0] FLAGS_OUT
);

  wire flagscontroller_v2_1_c_val, flagscontroller_v2_1_i_val, flagscontroller_v2_1_n_val,
       flagscontroller_v2_1_not_c_in, flagscontroller_v2_1_not_i_in, flagscontroller_v2_1_not_n_in,
       flagscontroller_v2_1_not_z_in, flagscontroller_v2_1_z_val, not_1_out, not_2_out, not_3_out, not_4_out;
  wire [3:0] bit_extender_1_out;

  Bit_Extender #(.out_width(4)) bit_extender_1 (.in(BUS_IN), .out(bit_extender_1_out));
  FLAGSController_v2 flagscontroller_v2_1 (
    .MODE2(MODE2), .MODE1(MODE1), .MODE0(MODE0), .BUS_IN(bit_extender_1_out), .ALU_IN(ALU_IN),
    .NOT_C_IN(flagscontroller_v2_1_not_c_in), .NOT_Z_IN(flagscontroller_v2_1_not_z_in),
    .NOT_N_IN(flagscontroller_v2_1_not_n_in), .NOT_I_IN(flagscontroller_v2_1_not_i_in),
    .C_VAL(flagscontroller_v2_1_c_val), .Z_VAL(flagscontroller_v2_1_z_val),
    .N_VAL(flagscontroller_v2_1_n_val), .I_VAL(flagscontroller_v2_1_i_val));
  Register #(.width(1)) C (.D(flagscontroller_v2_1_c_val), .en(not_1_out), .clk(CLK), .Q(FLAGS_OUT[0]));  // open: clr
  not not_1 (not_1_out, flagscontroller_v2_1_not_c_in);
  Register #(.width(1)) Z (.D(flagscontroller_v2_1_z_val), .en(not_2_out), .clk(CLK), .Q(FLAGS_OUT[1]));  // open: clr
  not not_2 (not_2_out, flagscontroller_v2_1_not_z_in);
  Register #(.width(1)) N (.D(flagscontroller_v2_1_n_val), .en(not_3_out), .clk(CLK), .Q(FLAGS_OUT[2]));  // open: clr
  not not_3 (not_3_out, flagscontroller_v2_1_not_n_in);
  Register #(.width(1)) I (.D(flagscontroller_v2_1_i_val), .en(not_4_out), .clk(CLK), .Q(FLAGS_OUT[3]));  // open: clr
  not not_4 (not_4_out, flagscontroller_v2_1_not_i_in);
endmodule

module ALU (
  input  [7:0] OPERATORS,
  input  [7:0] O1,
  input  [7:0] O2,
  input  NOT_ENABLE,
  output [7:0] BUS_OUT,
  output [2:0] FLAGS
);

  wire adder_1_cout, and_2_out, and_3_out, nor_1_out, nor_2_out, nor_3_out, nor_4_out, not_2_out, or_2_out,
       xor_3_out;
  wire [6:0] buffer_1_out;
  wire [7:0] adder_1_out, and_1_out, bit_extender_1_out, controlled_buffer_1_out, not_1_out, or_1_out,
       xor_1_out, xor_2_out;

  assign not_1_out = ~O1;  // NOT_Gate not_1, 8 bits wide
  assign xor_1_out = O1 ^ O2;  // XOR_Gate xor_1, 8 bits wide
  assign controlled_buffer_1_out = OPERATORS[6] ? not_1_out : 8'bz;  // Controlled_Buffer controlled_buffer_1
  assign controlled_buffer_1_out = OPERATORS[5] ? xor_1_out : 8'bz;  // Controlled_Buffer controlled_buffer_2
  assign and_1_out = O1 & O2;  // AND_Gate and_1, 8 bits wide
  assign controlled_buffer_1_out = OPERATORS[4] ? and_1_out : 8'bz;  // Controlled_Buffer controlled_buffer_3
  not not_2 (not_2_out, NOT_ENABLE);
  // NoConnect on OPERATORS[7]
  assign or_1_out = O1 | O2;  // OR_Gate or_1, 8 bits wide
  assign controlled_buffer_1_out = OPERATORS[3] ? or_1_out : 8'bz;  // Controlled_Buffer controlled_buffer_4
  nor nor_1 (nor_1_out, FLAGS[2], buffer_1_out[6]);
  assign bit_extender_1_out = {{7{OPERATORS[2]}}, OPERATORS[2]};  // Bit_Extender bit_extender_1
  assign {FLAGS[2], buffer_1_out} = controlled_buffer_1_out;  // Buffer buffer_1, 8 bits wide
  Pull_Resistor pull_resistor_1 (.node({FLAGS[2], buffer_1_out}));
  nor nor_2 (nor_2_out, buffer_1_out[5], buffer_1_out[4]);
  nor nor_3 (nor_3_out, buffer_1_out[3], buffer_1_out[2]);
  and and_2 (and_2_out, nor_1_out, nor_2_out);
  and and_3 (and_3_out, nor_3_out, nor_4_out);
  and and_4 (FLAGS[1], and_2_out, and_3_out);
  Adder adder_1 (.a(O1), .b(xor_2_out), .out(adder_1_out), .cin(OPERATORS[2]), .cout(adder_1_cout));
  assign xor_2_out = O2 ^ bit_extender_1_out;  // XOR_Gate xor_2, 8 bits wide
  assign controlled_buffer_1_out = or_2_out ? adder_1_out : 8'bz;  // Controlled_Buffer controlled_buffer_5
  xor xor_3 (xor_3_out, OPERATORS[2], adder_1_cout);
  and and_5 (FLAGS[0], xor_3_out, or_2_out);
  nor nor_4 (nor_4_out, buffer_1_out[1], buffer_1_out[0]);
  or or_2 (or_2_out, OPERATORS[2], OPERATORS[1]);
  assign BUS_OUT = not_2_out ? controlled_buffer_1_out : 8'bz;  // Controlled_Buffer controlled_buffer_6

  // Notes on the sheet:
  //   we invert the carry when subtracting, so that the carry flag in a sub operation means "borrow"
endmodule

module ClockModule (
  input  NOT_HLT,
  output C1,
  output C3,
  output C2,
  output C4
);

  wire and_1_out, and_2_out, CLK_GEN_out, nor_1_out, nor_2_out, nor_3_out, nor_4_out, not_1_out, not_2_out,
       not_3_out, not_4_out, not_5_out, not_6_out, not_7_out, not_8_out, not_9_out, not_10_out, not_11_out,
       not_12_out, sysclk_out;

  Clock #(.highDuration(2), .lowDuration(2), .phaseOffset(3)) CLK_GEN (.out(CLK_GEN_out));
  Clock #(.highDuration(2), .lowDuration(2), .phaseOffset(1)) sysclk (.out(sysclk_out));
  and and_1 (and_1_out, CLK_GEN_out, NOT_HLT);
  and and_2 (and_2_out, NOT_HLT, sysclk_out);
  nor nor_1 (nor_1_out, ~and_1_out, C3);  // NOR_Gate
  nor nor_2 (nor_2_out, C1, and_1_out);
  nor nor_3 (nor_3_out, ~and_2_out, C4);  // NOR_Gate
  nor nor_4 (nor_4_out, C2, and_2_out);
  not not_1 (not_1_out, nor_1_out);
  not not_2 (not_2_out, not_1_out);
  not not_3 (not_3_out, not_2_out);
  not not_4 (not_4_out, nor_2_out);
  not not_5 (not_5_out, not_4_out);
  not not_6 (not_6_out, not_5_out);
  not not_7 (not_7_out, nor_3_out);
  not not_8 (not_8_out, not_7_out);
  not not_9 (not_9_out, not_8_out);
  not not_10 (not_10_out, nor_4_out);
  not not_11 (not_11_out, not_10_out);
  not not_12 (not_12_out, not_11_out);
  not not_13 (C1, not_3_out);
  not not_14 (C3, not_6_out);
  not not_15 (C2, not_9_out);
  not not_16 (C4, not_12_out);
endmodule

module InstructionRegister (
);

  Counter counter_1 ();  // open: clr, load, up, count, clk, D, carry, Q
endmodule

module RAMModule (
  input  [15:0] ABUS,
  input  CLK,
  input  [7:0] BUS_IN,
  input  NOT_DEVICE_IN,
  input  NOT_DEVICE_SEL_RAM,
  input  NOT_RAM_OE,
  output [7:0] DBUS_OUT
);

  wire nor_1_out, not_1_out, or_1_out;
  wire [7:0] ram_1_dout;
  wire [12:0] bit_extender_1_out;

  Bit_Extender #(.in_width(16), .out_width(13), .\type ("zero")) bit_extender_1 (.in(ABUS), .out(bit_extender_1_out));
  or or_1 (or_1_out, NOT_DEVICE_IN, NOT_DEVICE_SEL_RAM);
  RAM #(.addrWidth(13), .asyncread("true")) ram_1 (
    .addr(bit_extender_1_out), .we(not_1_out), .oe(1'b1), .clk(CLK), .din(BUS_IN), .dout(ram_1_dout));
  not not_1 (not_1_out, or_1_out);
  assign DBUS_OUT = nor_1_out ? ram_1_dout : 8'bz;  // Controlled_Buffer controlled_buffer_1
  nor nor_1 (nor_1_out, NOT_DEVICE_SEL_RAM, NOT_RAM_OE);
endmodule

module StackPointer (
  input  SP_MODE_SEL0,
  input  SP_MODE_SEL1,
  input  NOT_OUT,
  input  NOT_OE,
  input  CLK,
  input  [7:0] DBUS,
  output [7:0] ASYNC_OUT,
  output [7:0] BUS_OUT
);

  wire and_1_out, nor_1_out, or_1_out;

  or or_1 (or_1_out, SP_MODE_SEL0, SP_MODE_SEL1);
  and and_1 (and_1_out, SP_MODE_SEL1, SP_MODE_SEL0);
  Counter counter_1 (
    .load(and_1_out), .up(SP_MODE_SEL0), .count(or_1_out), .clk(CLK), .D(DBUS), .Q(ASYNC_OUT));  // open: clr, carry
  nor nor_1 (nor_1_out, NOT_OUT, NOT_OE);
  assign BUS_OUT = nor_1_out ? ASYNC_OUT : 8'bz;  // Controlled_Buffer controlled_buffer_1

  // Notes on the sheet:
  //   SP_MODE_SEL
  //   00 - inactive
  //   01 - count up
  //   10 - count down
  //   11 - load
endmodule

module ROMModule (
  input  [15:0] ABUS,
  input  NOT_DEVICE_SEL_ROM,
  input  NOT_ROM_OE,
  output [7:0] DBUS
);

  wire nor_1_out;
  wire [7:0] STORAGE_ROM_data;
  wire [12:0] bit_extender_1_out;

  Bit_Extender #(.in_width(16), .out_width(13), .\type ("zero")) bit_extender_1 (.in(ABUS), .out(bit_extender_1_out));
  ROM #(.addrWidth(13)) STORAGE_ROM (.addr(bit_extender_1_out), .data(STORAGE_ROM_data));
  assign DBUS = nor_1_out ? STORAGE_ROM_data : 8'bz;  // Controlled_Buffer controlled_buffer_1
  nor nor_1 (nor_1_out, NOT_DEVICE_SEL_ROM, NOT_ROM_OE);

  // Notes on the sheet:
  //   contents of STORAGE_ROM (hex, n*v repeats v):
  //   fc 9 21 8 0 a 20 f4 9 0 1 4e 4f 40 20 16 90 ed 17 ef 17 f0 22 4*eb 6 22 7 0 6f f0 24 d5 da 5a 59 f8
  //   42 6f 6f 74 20 66 61 69 6c 65 64 20 66 6f 72 20 64 65 76 69 63 65 20 77 69 74 68 20 63 6f 64 65 20
  //   30 78 25 78 20 28 72 65 66 65 72 20 74 6f 20 62 69 6f 73 5f 75 74 69 6c 73 2e 6c 6e 61 73 6d 29 2e a
  //   0 50 51 41 20 1a 7 2 32 5c 5b f8 4e 4f 50 51 36 9f 0 ef 91 50 51 41 20 1a 7 2 32 5c 5b e6 ed 8e f0
  //   7a e5 f0 7a 5c 5b 5a 59 f8 4e 51 36 9f 0 ef a2 e6 36 f6 3 cf 5c 59 f8 50 6c 65 61 73 65 20 73 65 6c
  //   65 63 74 20 61 20 62 6f 6f 74 20 64 65 76 69 63 65 20 62 79 20 65 6e 74 65 72 69 6e 67 20 69 74 73
  //   20 6e 75 6d 62 65 72 3a 20 a 0 5b 45 52 52 20 5d 20 0 53 52 41 4d 0 45 6e 74 65 72 69 6e 67 20 72 65
  //   73 63 75 65 20 6d 6f 64 65 2e a 0 0 52 4f 4d 2d 38 4b 20 0 52 41 4d 2d 38 4b 20 49*0 54 54 59 2d 45
  //   20 20 57*0 41 53 4d 2d 33 31 20 0 41 53 4d 2d 31 35 20 0 41 53 4d 2d 37 20 20 0 4e 4f 50 51 57 e 77
  //   3 26 1 27 2 12 26 0 6c e9 7 f0 4 4 56 2 56 e1 f6 6 59 a0 0 ef ba f0 f5 58 a 22 3f 20 16 4*eb 4e 73 8
  //   51 13 4b e6 59 49 e6 21 0 4a e6 21 1 4a e6 21 2 4a e6 13 5a 76 5 36 eb eb eb 56 22 4f 6 1 13 4 8 f6
  //   c 2d 62 3f 20 16 e3 3b 20 16 8d 3 61 5c 5b 5a 59 f8 6b f8 0 57 4e 4f 8d 6 e 77 6 36 9f 0 ef 6b 9f 25
  //   ef 17 f6 3 a4 e6 f0 8 e6 36 9f 0 ef 6b 9f 73 ef 36 9f 78 ef 4a 9f 25 ef 30 4 25 f6 3 a4 f0 8 f6 3 a4
  //   e6 f0 8 50 51 22 ff 23 0 f6 3 b7 d f 8d 2 e 1e 5c 5b e6 f0 8 20 0 4*ec f6 2 6f 14 f6 3 a4 20 0 f6 2
  //   6f 14 f6 3 a4 51 d f 8d 1 e 1e 5c e6 f0 8 5a 59 61 f8 11 c8 f a0 a ee 7b 8a a 74 41 f8 74 30 f8 4e
  //   4f 3f 20 1e 40 20 1f 90 ef 8b fe f8 fd f8 f6 2 7e ed 94 f0 8d 50 51 6 23 42 20 1f 37 e6 3e 20 1f 5c
  //   5b f8 4e 4f 50 51 a0 0 ef bc 4f f6 2 8d 95 ef bc 33 5a e6 ed b9 f0 a7 e5 f0 a7 3a 0 5c 5b 5a 59 f8
  //   42 6f 6f 74 61 62 6c 65 20 64 65 76 69 63 65 73 20 66 6f 75 6e 64 3a a 0 4c 4e 46 53 0 4c 4e 44 49 1
  //   1 1 20 7*0 a5 25 73 7c 20 25 78 2e 25 78 20 7c 20 0 0 0 4e 4f 50 51 f6 3 59 a1 0 ef 34 76 a 36 3b 20
  //   1a e6 36 3b 20 17 e6 36 3b 20 18 8c 4 36 e6 37 12 16 3d 20 1b 3e 20 1c 76 5 36 3b 20 19 43 20 1d 0
  //   f0 4c 43 20 19 0 43 20 1b 0 43 20 1c 0 43 20 1a 0 43 20 17 0 43 20 18 0 43 20 1e 0 43 20 1f 0 5c 5b
  //   5a 59 f8 4e 4f 4 2 40 20 16 90 ef 72 f6 0 b a1 0 ef 72 f6 3 77 ed 74 e3 f0 60 d5 da 5a 59 f8 4e 4f
  //   50 51 76 8 36 e6 37 9f 0 ef 8d 12 16 76 5 36 9f 8 ef 90 fd f0 91 fe 5c 5b 5a 59 f8 4e 3f 20 19 9f 0
  //   ef a1 fe f0 a2 fd 59 f8 4f 40 20 19 a0 0 ef b5 a0 8 ef b2 f0 b5 f6 0 6b 5a f8 4f 37 a0 0 ef cd 40 20
  //   19 a0 0 ef cd a0 8 ef ca f0 cd f6 0 76 5a f8 50 51 6 23 42 20 1e 32 e6 3e 20 1e 41 20 1d c9 1 ef e5
  //   f6 3 a4 5c 5b f8 3b 20 1d f8 53 52 4f 4d 0 58 49 50 0 e6 ed f9 f8 e5 f8 4c 4e 58 45 0 4e 50 51 57 e
  //   77 6 26 0 27 1 4 6 f6 9 f5 36 c7 1 b7 ef 1e 43 20 14 5 5 1 f0 79 4 9 22 0 23 1 f6 9 f5 4 4 56 3 56
  //   fb f6 6 59 bc ef 3b 43 20 14 5 5 1 f0 79 4 6 f6 9 f5 26 4 27 5 22 0 23 1 4 7 f6 9 f5 54 f6 3 f5 39
  //   5b 26 2 27 3 4 6 f6 5 e7 26 2 27 3 22 4 23 5 20 2 21 3 4e 4f 20 f9 21 1 4e 4f 20 2 21 3 f6 6 0 5 1 f
  //   61 5c 5b 59 f9 2 50 51 4e 57 e 77 7 26 5 27 6 43 20 14 0 22 5 23 6 26 3 27 4 28 1 a 20 1 24 2 22 3
  //   23 4 f6 9 f5 26 3 27 4 36 24 0 22 5 23 6 4 a f6 9 f5 38 7 0 4 4 56 8 56 d0 f6 6 59 bc ef cc 43 20 14
  //   1 5 12 f0 f9 20 0 f6 8 41 4 0 f6 8 c4 ed ec 4 9 f6 9 f5 54 f6 3 f5 39 5b 56 24 56 0 f6 4 0 f0 f0 5
  //   12 f0 f9 bc ef f7 5 13 f0 f9 5 0 f 61 59 5c 5b f8 0 f6 7 8f 6 8 7 a5 f6 3 b7 f6 b 0 3f 20 3 9f 0 ef
  //   32 9f 1 ef 1c f4 5 3e 1 4 0 f6 5 46 f6 7 9b 43 20 2 10 4f 6 0 7 27 f6 2 0 8d 1 43 20 2 11 6 a 7 b0
  //   f6 3 b7 1 6 2 7 c3 f6 3 b7 1 4e 50 51 57 e 77 3 4*eb 6 20 7 4 6f e6 36 b7 ef 64 28 2 1 56 2 56 dc f0
  //   6b 28 2 0 56 3 56 f1 ea 36 f6 0 b 26 0 27 1 50 51 76 c 54 ea 54 f6 7 8f 6 6 7 b2 f6 2 0 8d 6 22 0 23
  //   1 20 2 9f 0 ef a8 f6 4 80 3c 20 2 55 20 14 f6 7 9b 6 8 7 0 f6 2 0 8d 1 f0 bb 76 a 36 8c 2 54 e6 39
  //   5b 76 8 54 e6 39 5b 6b 8 0 f5 f 61 5c 5b 59 f8 43 20 15 1 43 20 16 0 6 2 7 e1 56 3f 56 f0 4 10 f6 c
  //   2d f8 5b 57 41 52 4e 5d 20 0 5b 43 52 49 54 5d 20 0 85 ed eb f8 e9 f8 5b 49 4e 46 4f 5d 20 0 91 ed
  //   fa 96 f8 fe f8 4*0 4e 4f 50 51 57 e 77 5 27 2 26 3 21 f8 25 0 21 f7 25 1 20 f6 21 f5 25 4 9f 0 ef 20
  //   f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
endmodule

module CodeSegment_ProgramCounter (
  input  [3:0] FLAGS,
  input  J,
  input  JC,
  input  JZ,
  input  JN,
  input  NOT_PC_IN,
  input  NOT_CS_IN,
  input  NOT_PC_INC,
  input  RESET,
  input  [15:0] ABUS,
  input  CLK,
  input  CSPC_UP,
  input  NOT_PC_OUT,
  input  NOT_CS_OUT,
  input  NOT_OE,
  output [15:0] CS_PC,
  output [7:0] BUS_OUT
);

  wire and_1_out, and_2_out, and_3_out, and_4_out, and_5_out, nor_1_out, nor_2_out, nor_3_out, not_1_out,
       not_2_out, not_3_out, or_1_out, or_2_out, or_3_out, or_4_out, PC_carry;

  and and_1 (and_1_out, JC, FLAGS[0]);
  or or_1 (or_1_out, and_1_out, and_2_out);
  and and_2 (and_2_out, JZ, FLAGS[1]);
  and and_3 (and_3_out, JN, FLAGS[2]);
  or or_2 (or_2_out, or_1_out, and_3_out);
  nor nor_1 (nor_1_out, J, or_2_out);
  nor nor_2 (nor_2_out, NOT_CS_IN, nor_1_out);
  and and_4 (and_4_out, CLK, RESET);
  Counter CS (
    .clr(and_4_out), .load(nor_2_out), .up(CSPC_UP), .count(and_5_out), .clk(CLK), .D(ABUS[15:8]),
    .Q(CS_PC[15:8]));  // open: carry
  and and_5 (and_5_out, not_1_out, PC_carry);
  not not_1 (not_1_out, NOT_PC_INC);
  nor nor_3 (nor_3_out, nor_1_out, NOT_PC_IN);
  Counter PC (
    .clr(and_4_out), .load(nor_3_out), .up(CSPC_UP), .count(not_1_out), .clk(CLK), .D(ABUS[7:0]),
    .carry(PC_carry), .Q(CS_PC[7:0]));
  assign BUS_OUT = not_3_out ? CS_PC[15:8] : 8'bz;  // Controlled_Buffer controlled_buffer_1
  assign BUS_OUT = not_2_out ? CS_PC[7:0] : 8'bz;  // Controlled_Buffer controlled_buffer_2
  not not_2 (not_2_out, or_3_out);
  not not_3 (not_3_out, or_4_out);
  or or_3 (or_3_out, NOT_OE, NOT_PC_OUT);
  or or_4 (or_4_out, NOT_OE, NOT_CS_OUT);
endmodule

module LCD_emulator (
  input  RS,
  input  R_NW,
  input  LCD_EN,
  input  [7:0] BUS_IN
);
endmodule

module Interface_emulator (
  input  POLL,
  input  TRANSMIT,
  input  CLK,
  input  [7:0] BUS_IN,
  output [7:0] BUS_OUT,
  output A_OUT
);

  wire [7:0] register_1_q;

  Register register_1 (.D(BUS_IN), .en(TRANSMIT), .clk(CLK), .Q(register_1_q));  // open: clr
  assign BUS_OUT = POLL ? register_1_q : 8'bz;  // Controlled_Buffer controlled_buffer_1

  assign A_OUT = POLL;
endmodule

module ControlUnit (
  input  [7:0] IR_IN,
  input  NOT_IRQ,
  input  RESET,
  input  CLK,
  input  I,
  output [3:0] MICROINSTR_CT_OUT,
  output [7:0] IR_OUT,
  output RA_S0,
  output RA_S1,
  output NOT_RA_OUT,
  output NOT_DEVICE_IN,
  output NOT_DEVICE_OUT,
  output NOT_SS_IN,
  output NOT_SS_OUT,
  output SP_MODE_SEL0,
  output NOT_RB_IN,
  output NOT_RC_IN,
  output NOT_RD_IN,
  output SP_MODE_SEL1,
  output NOT_SP_OUT,
  output NOT_ABH_IN,
  output NOT_ABL_IN,
  output NOT_RB_OUT,
  output NOT_RC_OUT,
  output NOT_RD_OUT,
  output NOT_RT_IN,
  output NOT_RT_OUT,
  output X_SEL0,
  output X_SEL1,
  output X_SEL2,
  output Y_SEL0,
  output Y_SEL1,
  output Y_SEL2,
  output OP_SEL0,
  output OP_SEL1,
  output OP_SEL2,
  output NOT_CS_IN,
  output NOT_PC_IN,
  output NOT_PC_INC,
  output NOT_CS_OUT,
  output NOT_PC_OUT,
  output NOT_BP_IN,
  output NOT_BP_OUT,
  output J,
  output JC,
  output JZ,
  output JN,
  output NOT_PASS,
  output NOT_HLT,
  output ADDR_SEL0,
  output ADDR_SEL1,
  output NOT_FETCH,
  output NOT_DATA_LATCH_OUT,
  output NOT_IVH_OUT,
  output NOT_IVL_OUT,
  output FLAGS_MODE_SEL0,
  output FLAGS_MODE_SEL1,
  output FLAGS_MODE_SEL2,
  output NOT_FLAGS_OUT,
  output CSPC_UP,
  output NOT_DS_IN,
  output NOT_DS_OUT
);

  wire and_1_out, decoder_1_out1, decoder_1_out2, decoder_1_out3, decoder_2_out1, decoder_2_out2,
       decoder_2_out3, n74163_1_pin3, n74163_1_pin10, not_1_out, not_2_out, or_1_out;
  wire [7:0] multiplexer_1_out;
  wire [7:4] EEPROM1_data;
  wire [7:5] EEPROM6_data;

  Multiplexer #(.width(8)) multiplexer_1 (.in0(8'h2), .in1(IR_IN), .out(multiplexer_1_out), .sel(or_1_out));
  or or_1 (or_1_out, NOT_IRQ, I);
  not not_1 (not_1_out, RESET);
  Register IR (.D(multiplexer_1_out), .en(not_2_out), .clk(CLK), .Q(IR_OUT), .clr(RESET));
  not not_2 (not_2_out, NOT_PASS);
  and and_1 (and_1_out, NOT_PASS, not_1_out);
  _74163 #(.ShowInternalStructure("true")) u_74163_1 (
    .pin1(and_1_out), .pin2(CLK), .pin3(n74163_1_pin3), .pin4(n74163_1_pin3), .pin5(n74163_1_pin3),
    .pin6(n74163_1_pin3), .pin7(n74163_1_pin3), .pin14(MICROINSTR_CT_OUT[0]), .pin13(MICROINSTR_CT_OUT[1]),
    .pin12(MICROINSTR_CT_OUT[2]), .pin11(MICROINSTR_CT_OUT[3]), .pin10(n74163_1_pin10), .pin9(n74163_1_pin10));  // open: pin15
  ROM #(.addrWidth(13)) EEPROM0 (
    .addr({1'b0, IR_OUT, MICROINSTR_CT_OUT}),
    .data({SP_MODE_SEL0, NOT_SS_OUT, NOT_SS_IN, NOT_DEVICE_OUT, NOT_DEVICE_IN, NOT_RA_OUT, RA_S1, RA_S0}));
  ROM #(.addrWidth(13)) EEPROM1 (
    .addr({1'b0, IR_OUT, MICROINSTR_CT_OUT}),
    .data({EEPROM1_data, NOT_ABL_IN, NOT_ABH_IN, NOT_SP_OUT, SP_MODE_SEL1}));
  ROM #(.addrWidth(13)) EEPROM2 (
    .addr({1'b0, IR_OUT, MICROINSTR_CT_OUT}),
    .data({Y_SEL2, Y_SEL1, Y_SEL0, X_SEL2, X_SEL1, X_SEL0, NOT_RT_OUT, NOT_RT_IN}));
  ROM #(.addrWidth(13)) EEPROM3 (
    .addr({1'b0, IR_OUT, MICROINSTR_CT_OUT}),
    .data({NOT_PC_OUT, NOT_CS_OUT, NOT_PC_INC, NOT_PC_IN, NOT_CS_IN, OP_SEL2, OP_SEL1, OP_SEL0}));
  ROM #(.addrWidth(13)) EEPROM4 (
    .addr({1'b0, IR_OUT, MICROINSTR_CT_OUT}), .data({NOT_HLT, NOT_PASS, JN, JZ, JC, J, NOT_BP_OUT, NOT_BP_IN}));
  ROM #(.addrWidth(13)) EEPROM5 (
    .addr({1'b0, IR_OUT, MICROINSTR_CT_OUT}),
    .data({FLAGS_MODE_SEL1, FLAGS_MODE_SEL0, NOT_IVL_OUT, NOT_IVH_OUT, NOT_DATA_LATCH_OUT, NOT_FETCH, ADDR_SEL1, ADDR_SEL0}));
  ROM #(.addrWidth(13)) EEPROM6 (
    .addr({1'b0, IR_OUT, MICROINSTR_CT_OUT}),
    .data({EEPROM6_data, NOT_DS_OUT, NOT_DS_IN, CSPC_UP, NOT_FLAGS_OUT, FLAGS_MODE_SEL2}));
  Decoder #(.select(2)) decoder_1 (
    .out1(decoder_1_out1), .out2(decoder_1_out2), .out3(decoder_1_out3), .sel(EEPROM1_data[5:4]));  // open: out0, en
  Decoder #(.select(2)) decoder_2 (
    .out1(decoder_2_out1), .out2(decoder_2_out2), .out3(decoder_2_out3), .sel(EEPROM1_data[7:6]));  // open: out0, en
  not not_3 (NOT_RB_IN, decoder_1_out1);
  not not_4 (NOT_RC_IN, decoder_1_out2);
  not not_5 (NOT_RD_IN, decoder_1_out3);
  not not_6 (NOT_RB_OUT, decoder_2_out1);
  not not_7 (NOT_RC_OUT, decoder_2_out2);
  not not_8 (NOT_RD_OUT, decoder_2_out3);
  // also tied to VCC on the sheet: {n74163_1_pin3, n74163_1_pin10}

  // Notes on the sheet:
  //   Get the 163! Synchronous reset
  //   contents of EEPROM0 (hex, n*v repeats v):
  //   34*7c 74 f4 f4 fc 12*7c 74 f4 f4 fc 10*7c 7f 63*7c fc 15*7c 5c 47*7c 3c 47*7c fc 31*7c 78 15*7c 78
  //   15*7c 78 15*7c 7f 47*7c 7f 47*7c 7f 47*7c 5c 15*7c fc 33*7c 3c 6f 14*7c 3c 6c 14*7c 3c 6c 14*7c 3c
  //   6c 13*7c 3c 7c 70 13*7c 3c 7c 74 13*7c 3c 7c 74 13*7c 3c 7c 74 13*7c 3c 7c 74 13*7c 70 15*7c 74
  //   15*7c 74 15*7c 74 15*7c 6f 15*7c 6c 15*7c 6c 15*7c 6c 15*7c 74 16*7c 70 15*7c 74 15*7c 74 15*7c 74
  //   15*7c 6f 15*7c 6c 15*7c 6c 15*7c 6c 15*7c 74 15*7c 70 15*7c 74 15*7c 74 15*7c 74 15*7c 6f 15*7c 6c
  //   15*7c 6c 15*7c 6c 15*7c 74 14*7c 6c 7c 74 13*7c 6f 15*7c 6c 15*7c 6c 15*7c 6c 15*7c 70 15*7c 74
  //   15*7c 74 15*7c 74 15*7c 74 14*7c 70 fc 14*7c 74 fc 14*7c 74 fc 14*7c 74 fc 15*7c 6c 74 fc 13*7c 6c
  //   74 fc 14*7c 6c 74 fc 13*7c 6c 74 fc 11*7c 74 fc 14*7c 74 fc 14*7c 74 fc 14*7c 6f 15*7c 6c 15*7c 6c
  //   15*7c 6c 16*7c 6c 74 14*7c 6c 74 13*7c 6c 7c 7c 74 12*7c 6c 7c 7c 74 12*7c 6c 15*7c 6c 15*7c 7f
  //   15*7c 7f 15*7c 7f 15*7c 7f 208*7c 7f 63*7c fc 30*7c 7f 15*7c 7f 15*7c 7f 15*7c 7f 208*7c 7f 63*7c fc
  //   350*7c 7f 15*7c 7f 15*7c 7f 15*7c 7f 208*7c 7f 62*7c 7f 15*7c 7f 15*7c 7f 15*7c 7f 208*7c 7f 62*7c
  //   7f 15*7c 7f 15*7c 7f 15*7c 7f 208*7c 7f 62*7c 7f 63*7c 7f 63*7c 7f 63*7c 7e 15*7c 7d 161*7c 74 f4 fc
  //   13*7c 74 f4 fc 11*7c 6c 6c 14*7c 6c 6c 7c fc 12*7c 6c 6c 6c 4189*7c
  //   contents of EEPROM1 (hex, n*v repeats v):
  //   32*e a 6 14*e a 6 30*e 1e 15*e 2e 15*e 3e 15*e f 63*e 3e 15*e 3c 15*e c 15*e f 15*e 3e 15*e 1e 15*e
  //   2e 15*e 3e 15*e 4e 15*e 6e 15*e 7e 15*e 8e 15*e 9e 15*e be 15*e ce 15*e de 15*e ee 15*e ce 15*e cf
  //   15*e ce 15*e 6 6 a 13*e 6 6 a 1e 12*e 6 6 a 2e 12*e 6 6 a 3e 12*e 6 a 6 13*e 6 a 6 4e 12*e 6 a 6 8e
  //   12*e 6 a 6 ce 12*e 6 a 6 13*e 6 15*e 6 4e 14*e 6 8e 14*e 6 ce 14*e 6 15*e 6 1e 14*e 6 2e 14*e 6 3e
  //   14*e 6 15*e 8a c6 14*e 8a c6 4e 13*e 8a c6 8e 13*e 8a c6 ce 13*e 8a c6 14*e 8a c6 1e 13*e 8a c6 2e
  //   13*e 8a c6 3e 13*e 8a c6 14*e a 6 14*e a 6 4e 13*e a 6 8e 13*e a 6 ce 13*e a 6 14*e a 6 1e 13*e a 6
  //   2e 13*e a 6 3e 13*e a 6 14*e 6 e 6 13*e c6 15*e c6 1e 14*e c6 2e 14*e c6 3e 14*e c6 15*e c6 4e 14*e
  //   c6 8e 14*e c6 ce 14*e c6 31*e 4e 15*e 8e 15*e ce 15*e 6 15*e c6 15*e 8a c6 14*e a 6 62*e f 15*e 1f
  //   15*e 2f 15*e 3f 15*e 6 f 14*e c6 f 14*e f 8a c6 13*e f a 6 13*e f 15*e f 79*e 1e 15*e 1e 15*e 1e
  //   15*e 1e 15*e 2e 15*e 2e 15*e 2e 15*e 2e 15*e 3e 15*e 3e 15*e 3e 15*e 3e 32*e 1e 15*e 2e 15*e 3e 15*e
  //   f 94*e 1e 15*e 1e 15*e 1e 15*e 1e 15*e 2e 15*e 2e 15*e 2e 15*e 2e 15*e 3e 15*e 3e 15*e 3e 15*e 3e
  //   32*e 1e 15*e 2e 15*e 3e 15*e f 414*e 1e 15*e 1e 15*e 1e 15*e 1e 15*e 2e 15*e 2e 15*e 2e 15*e 2e 15*e
  //   3e 15*e 3e 15*e 3e 15*e 3e 32*e 1e 15*e 2e 15*e 3e 78*e 1e 15*e 1e 15*e 1e 15*e 1e 15*e 2e 15*e 2e
  //   15*e 2e 15*e 2e 15*e 3e 15*e 3e 15*e 3e 15*e 3e 32*e 1e 15*e 2e 15*e 3e 78*e 1e 15*e 1e 15*e 1e 15*e
  //   1e 15*e 2e 15*e 2e 15*e 2e 15*e 2e 15*e 3e 15*e 3e 15*e 3e 15*e 3e 32*e 1e 15*e 2e 15*e 3e 30*e 1e
  //   15*e 2e 15*e 3e 31*e 1e 15*e 2e 15*e 3e 31*e 1e 15*e 2e 15*e 3e 47*e 6 15*e 6 15*e 6 15*e 6 15*e a 6
  //   14*e a 6 14*e a 6 14*e a 6 14*e 8a c6 14*e a 6 14*e 8a c6 14*e 7 b 14*e 7 b e f 12*e f 7 b 4189*e
  //   contents of EEPROM2 (hex, n*v repeats v):
  //   513*3 d3 15*3 d3 15*3 d3 15*3 d3 16*3 d3 15*3 d3 15*3 d3 15*3 d3 15*3 d3 446*3 2 3 1 221*3 2 1 14*3
  //   2 1 15*3 2 1 14*3 2 1 125*3 2 1 14*3 2 1 13*3 2 3 3 1 12*3 2 3 3 1 60*3 23 15*3 43 15*3 63 15*3 7
  //   15*3 27 15*3 47 15*3 67 15*3 b 15*3 2b 15*3 4b 15*3 6b 15*3 f 15*3 2f 15*3 4f 15*3 6f 15*3 2 83 14*3
  //   2 87 14*3 2 8b 14*3 2 8f 14*3 2 97 14*3 2 9b 30*3 23 15*3 43 15*3 63 15*3 7 15*3 27 15*3 47 15*3 67
  //   15*3 b 15*3 2b 15*3 4b 15*3 6b 15*3 f 15*3 2f 15*3 4f 15*3 6f 15*3 2 83 14*3 2 87 14*3 2 8b 14*3 2
  //   8f 14*3 2 97 14*3 2 9b 30*3 23 15*3 43 15*3 63 15*3 7 15*3 27 15*3 47 15*3 67 15*3 b 15*3 2b 15*3 4b
  //   15*3 6b 15*3 f 15*3 2f 15*3 4f 15*3 6f 15*3 2 83 14*3 2 87 14*3 2 8b 14*3 2 8f 30*3 23 15*3 43 15*3
  //   63 15*3 7 15*3 27 15*3 47 15*3 67 15*3 b 15*3 2b 15*3 4b 15*3 6b 15*3 f 15*3 2f 15*3 4f 15*3 6f 15*3
  //   2 83 14*3 2 87 14*3 2 8b 14*3 2 8f 30*3 23 15*3 43 15*3 63 15*3 7 15*3 27 15*3 47 15*3 67 15*3 b
  //   15*3 2b 15*3 4b 15*3 6b 15*3 f 15*3 2f 15*3 4f 15*3 6f 15*3 2 83 14*3 2 87 14*3 2 8b 14*3 2 8f 30*3
  //   23 15*3 43 15*3 63 15*3 7 15*3 27 15*3 47 15*3 67 15*3 b 15*3 2b 15*3 4b 15*3 6b 15*3 f 15*3 2f 15*3
  //   4f 15*3 6f 15*3 2 83 14*3 2 87 14*3 2 8b 14*3 2 8f 30*3 7 15*3 b 15*3 f 15*3 e3 15*3 e7 15*3 eb 15*3
  //   ef 15*3 e3 15*3 e7 15*3 eb 15*3 ef 241*3 2 97 4204*3
  //   contents of EEPROM3 (hex, n*v repeats v):
  //   d8 15*f8 d8 15*f8 d8 f8 b8 78 f8 e0 d8 11*f8 b8 78 f8 e0 d8 9*f8 d8 d8 14*f8 d8 d8 14*f8 d8 d8 14*f8
  //   d8 d8 14*f8 d8 d8 14*f8 d8 d8 14*f8 d8 d8 14*f8 d8 d8 14*f8 d8 15*f8 d8 15*f8 d8 15*f8 d8 15*f8 d8
  //   15*f8 d8 15*f8 d8 15*f8 d8 15*f8 d8 15*f8 d8 15*f8 d8 15*f8 d8 15*f8 d8 15*f8 d8 15*f8 d8 15*f8 d8
  //   15*f8 d8 15*f8 d8 15*f8 d8 15*f8 d8 15*f8 d8 f9 f8 d8 12*f8 d8 f9 f8 d8 12*f8 d8 f9 f8 d8 12*f8 d8
  //   f9 f8 d8 12*f8 d8 f8 f9 d8 12*f8 d8 f8 f9 d8 12*f8 d8 f8 f9 d8 12*f8 d8 f8 f9 d8 12*f8 d8 f8 f9 d8
  //   d8 11*f8 d8 d8 14*f8 d8 d8 14*f8 d8 d8 14*f8 d8 d8 14*f8 d8 d8 14*f8 d8 d8 14*f8 d8 d8 14*f8 d8 d8
  //   14*f8 d8 d8 d8 15*f8 d8 15*f8 d8 15*f8 d8 15*f8 d8 15*f8 d8 15*f8 d8 15*f8 d8 15*f8 d8 15*f8 d8 d8
  //   12*f8 d8 d8 d8 13*f8 d8 d8 d8 13*f8 d8 d8 d8 13*f8 d8 d8 d8 13*f8 d8 d8 d8 13*f8 d8 d8 d8 13*f8 d8
  //   d8 d8 13*f8 d8 d8 d8 13*f8 4*d8 12*f8 d8 f8 d8 d8 13*f8 d8 15*f8 d8 15*f8 d8 15*f8 d8 15*f8 d8 15*f8
  //   d8 15*f8 d8 15*f8 d8 15*f8 d8 d8 14*f8 d8 15*f8 d8 15*f8 d8 15*f8 d8 14*f8 d8 f8 f8 d8 15*f8 d8
  //   16*f8 d8 11*f8 d8 d8 f8 f8 d8 11*f8 d8 d8 15*f8 d8 15*f8 d8 14*f8 d8 15*f8 d8 15*f8 d8 15*f8 d8
  //   15*f8 d8 f8 d8 15*f8 d8 16*f8 d8 13*f8 d8 d8 d8 12*f8 d8 15*f8 d8 15*f8 d9 15*f8 d9 15*f8 d9 15*f8
  //   d9 15*f8 d9 15*f8 d9 15*f8 d9 15*f8 d9 15*f8 d9 15*f8 d9 15*f8 d9 15*f8 d9 15*f8 d9 15*f8 d9 15*f8
  //   d9 15*f8 d9 15*f8 d8 d9 14*f8 d8 d9 14*f8 d8 d9 14*f8 d8 d9 14*f8 d8 d9 14*f8 d8 d9 14*f8 da 15*f8
  //   da 15*f8 da 15*f8 da 15*f8 da 15*f8 da 15*f8 da 15*f8 da 15*f8 da 15*f8 da 15*f8 da 15*f8 da 15*f8
  //   da 15*f8 da 15*f8 da 15*f8 da 15*f8 d8 da 14*f8 d8 da 14*f8 d8 da 14*f8 d8 da 14*f8 d8 da 14*f8 d8
  //   da 14*f8 da 15*f8 da 15*f8 da 15*f8 da 15*f8 da 15*f8 da 15*f8 da 15*f8 da 15*f8 da 15*f8 da 15*f8
  //   da 15*f8 da 15*f8 da 15*f8 da 15*f8 da 15*f8 da 15*f8 d8 da 14*f8 d8 da 14*f8 d8 da 14*f8 d8 da
  //   14*f8 db 15*f8 db 15*f8 db 15*f8 db 15*f8 db 15*f8 db 15*f8 db 15*f8 db 15*f8 db 15*f8 db 15*f8 db
  //   15*f8 db 15*f8 db 15*f8 db 15*f8 db 15*f8 db 15*f8 d8 db 14*f8 d8 db 14*f8 d8 db 14*f8 d8 db 14*f8
  //   dc 15*f8 dc 15*f8 dc 15*f8 dc 15*f8 dc 15*f8 dc 15*f8 dc 15*f8 dc 15*f8 dc 15*f8 dc 15*f8 dc 15*f8
  //   dc 15*f8 dc 15*f8 dc 15*f8 dc 15*f8 dc 15*f8 d8 dc 14*f8 d8 dc 14*f8 d8 dc 14*f8 d8 dc 14*f8 dd
  //   15*f8 dd 15*f8 dd 15*f8 dd 15*f8 dd 15*f8 dd 15*f8 dd 15*f8 dd 15*f8 dd 15*f8 dd 15*f8 dd 15*f8 dd
  //   15*f8 dd 15*f8 dd 15*f8 dd 15*f8 dd 15*f8 d8 dd 14*f8 d8 dd 14*f8 d8 dd 14*f8 d8 dd 14*f8 de 15*f8
  //   de 15*f8 de 15*f8 de 15*f8 d9 15*f8 d9 15*f8 d9 15*f8 d9 15*f8 da 15*f8 da 15*f8 da 15*f8 da 15*f8
  //   d8 15*f8 d8 15*f8 d8 e8 d8 13*f8 d8 e8 d8 13*f8 d8 e8 d8 13*f8 d8 e8 d8 13*f8 d8 d8 e0 d8 12*f8 d8
  //   d8 e0 d8 12*f8 d8 d8 e0 d8 12*f8 d8 d8 e0 d8 14*f8 e0 d8 12*f8 d8 d8 b8 78 e0 d8 12*f8 b8 78 e0 d8
  //   12*f8 e0 d8 14*f8 d8 fa e0 d8 13*f8 e0 d8 11*f8 d8 15*f8 d8 15*f8 d8 15*f8 d8 4127*f8
  //   contents of EEPROM4 (hex, n*v repeats v):
  //   83 15*c3 3 20*c3 c7 83 14*c3 c7 83 10*c3 83 15*c3 83 15*c3 83 15*c3 83 15*c3 83 15*c3 83 15*c3 83
  //   14*c3 c2 83 14*c3 83 15*c3 83 15*c3 82 15*c3 81 15*c3 83 15*c3 83 15*c3 83 15*c3 83 15*c3 83 15*c3
  //   83 15*c3 83 15*c3 83 15*c3 83 15*c3 83 15*c3 83 15*c3 83 15*c3 83 15*c3 83 15*c3 83 15*c3 83 18*c3
  //   83 15*c3 83 15*c3 83 15*c3 83 15*c3 83 15*c3 83 15*c3 83 15*c3 83 16*c3 83 12*c3 83 15*c3 83 15*c3
  //   83 15*c3 83 15*c3 83 15*c3 83 15*c3 83 15*c3 83 16*c3 83 15*c3 83 15*c3 83 15*c3 83 15*c3 83 15*c3
  //   83 15*c3 83 15*c3 83 15*c3 83 16*c3 83 14*c3 83 15*c3 83 15*c3 83 15*c3 83 15*c3 83 15*c3 83 15*c3
  //   83 15*c3 83 16*c3 83 15*c3 83 13*c3 83 15*c3 83 15*c3 83 15*c3 83 15*c3 83 15*c3 83 15*c3 83 15*c3
  //   83 16*c3 83 14*c3 83 15*c3 83 15*c3 83 15*c3 83 17*c3 83 15*c3 83 16*c3 83 15*c3 83 12*c3 83 14*c3
  //   c1 83 15*c3 83 14*c3 83 15*c3 83 15*c3 83 15*c3 83 17*c3 83 15*c3 83 16*c3 83 15*c3 83 12*c3 82
  //   15*c3 83 15*c3 83 15*c3 83 15*c3 83 15*c3 83 15*c3 83 15*c3 83 15*c3 83 15*c3 83 15*c3 83 15*c3 83
  //   15*c3 83 15*c3 83 15*c3 83 15*c3 83 15*c3 83 15*c3 83 16*c3 83 15*c3 83 15*c3 83 15*c3 83 15*c3 83
  //   15*c3 82 14*c3 83 15*c3 83 15*c3 83 15*c3 83 15*c3 83 15*c3 83 15*c3 83 15*c3 83 15*c3 83 15*c3 83
  //   15*c3 83 15*c3 83 15*c3 83 15*c3 83 15*c3 83 15*c3 83 16*c3 83 15*c3 83 15*c3 83 15*c3 83 15*c3 83
  //   15*c3 82 14*c3 83 15*c3 83 15*c3 83 15*c3 83 15*c3 83 15*c3 83 15*c3 83 15*c3 83 15*c3 83 15*c3 83
  //   15*c3 83 15*c3 83 15*c3 83 15*c3 83 15*c3 83 15*c3 83 16*c3 83 15*c3 83 15*c3 83 15*c3 83 14*c3 83
  //   15*c3 83 15*c3 83 15*c3 83 15*c3 83 15*c3 83 15*c3 83 15*c3 83 15*c3 83 15*c3 83 15*c3 83 15*c3 83
  //   15*c3 83 15*c3 83 15*c3 83 15*c3 83 16*c3 83 15*c3 83 15*c3 83 15*c3 83 14*c3 83 15*c3 83 15*c3 83
  //   15*c3 83 15*c3 83 15*c3 83 15*c3 83 15*c3 83 15*c3 83 15*c3 83 15*c3 83 15*c3 83 15*c3 83 15*c3 83
  //   15*c3 83 15*c3 83 16*c3 83 15*c3 83 15*c3 83 15*c3 83 14*c3 83 15*c3 83 15*c3 83 15*c3 83 15*c3 83
  //   15*c3 83 15*c3 83 15*c3 83 15*c3 83 15*c3 83 15*c3 83 15*c3 83 15*c3 83 15*c3 83 15*c3 83 15*c3 83
  //   16*c3 83 15*c3 83 15*c3 83 15*c3 83 14*c3 83 15*c3 83 15*c3 83 15*c3 83 15*c3 83 15*c3 83 15*c3 83
  //   15*c3 83 15*c3 83 15*c3 83 15*c3 83 15*c3 83 15*c3 83 15*c3 83 16*c3 cb 83 14*c3 e3 83 14*c3 d3 83
  //   14*c3 c7 83 15*c3 cb 83 14*c3 e3 83 14*c3 d3 83 14*c3 c7 83 14*c3 c7 83 16*c3 c7 83 14*c3 c7 83
  //   12*c3 c7 83 16*c3 c7 83 13*c3 c7 83 11*c3 83 15*c3 83 15*c3 83 15*c3 83 4127*c3
  //   contents of EEPROM5 (hex, n*v repeats v):
  //   38 15*3c 38 15*3c 2c 1c 3e 3e 3e 7c 38 9*3c 2c 1c 3e 3e 3e 7c 38 9*3c 30 38 14*3c 30 38 14*3c 30 38
  //   14*3c 30 38 14*3c 30 38 14*3c 30 38 14*3c 30 38 14*3c 30 38 14*3c 38 15*3c 38 15*3c 38 15*3c 38
  //   15*3c 38 15*3c 38 15*3c 38 15*3c 38 15*3c 38 15*3c 38 15*3c 38 15*3c 38 15*3c 38 15*3c 38 15*3c 38
  //   15*3c 38 15*3c 38 15*3c 38 15*3c 38 15*3c 38 15*3c 30 3c 3c 38 12*3c 30 3c 3c 38 12*3c 30 3c 3c 38
  //   12*3c 30 3c 3c 38 12*3c 30 3c 3c 38 12*3c 30 3c 3c 38 12*3c 30 3c 3c 38 12*3c 30 3c 3c 38 12*3c 30
  //   3c 3c 30 38 11*3c 30 39 14*3c 30 39 14*3c 30 39 14*3c 30 39 14*3c 30 39 14*3c 30 39 14*3c 30 39
  //   14*3c 30 39 14*3c 30 31 38 15*3c 38 15*3c 38 15*3c 38 15*3c 38 15*3c 38 15*3c 38 15*3c 38 15*3c 38
  //   15*3c 30 38 12*3c 30 30 38 13*3c 30 30 38 13*3c 30 30 38 13*3c 30 30 38 13*3c 30 30 38 13*3c 30 30
  //   38 13*3c 30 30 38 13*3c 30 30 38 13*3c 30 30 30 38 12*3c 30 3d 30 39 13*3c 39 15*3c 39 15*3c 39
  //   15*3c 39 15*3c 39 15*3c 39 15*3c 39 15*3c 39 15*3c 31 38 13*3c 3e 38 14*3c 3e 38 14*3c 3e 38 14*3c
  //   3e 38 14*3c 30 3d 3e 38 13*3c 3d 3e 38 15*3c 3e 38 11*3c 30 30 3c 3e 38 11*3c 32 38 14*3c 3e 38
  //   14*3c 3e 38 14*3c 3a 15*3c 3a 15*3c 3a 15*3c 3a 15*3c 30 3e 39 14*3c 3e 39 13*3c 3e 3c 3c 38 12*3c
  //   3e 30 30 38 12*3c 3a 15*3c 3a 15*3c f8 15*3c f8 15*3c f8 15*3c f8 15*3c f8 15*3c f8 15*3c f8 15*3c
  //   f8 15*3c f8 15*3c f8 15*3c f8 15*3c f8 15*3c f8 15*3c f8 15*3c f8 15*3c f8 15*3c 30 f8 14*3c 30 f8
  //   14*3c 30 f8 14*3c 30 f8 14*3c 30 f8 14*3c 30 f8 14*3c f8 15*3c f8 15*3c f8 15*3c f8 15*3c f8 15*3c
  //   f8 15*3c f8 15*3c f8 15*3c f8 15*3c f8 15*3c f8 15*3c f8 15*3c f8 15*3c f8 15*3c f8 15*3c f8 15*3c
  //   30 f8 14*3c 30 f8 14*3c 30 f8 14*3c 30 f8 14*3c 30 f8 14*3c 30 f8 14*3c f8 15*3c f8 15*3c f8 15*3c
  //   f8 15*3c f8 15*3c f8 15*3c f8 15*3c f8 15*3c f8 15*3c f8 15*3c f8 15*3c f8 15*3c f8 15*3c f8 15*3c
  //   f8 15*3c f8 15*3c 30 f8 14*3c 30 f8 14*3c 30 f8 14*3c 30 f8 14*3c f8 15*3c f8 15*3c f8 15*3c f8
  //   15*3c f8 15*3c f8 15*3c f8 15*3c f8 15*3c f8 15*3c f8 15*3c f8 15*3c f8 15*3c f8 15*3c f8 15*3c f8
  //   15*3c f8 15*3c 30 f8 14*3c 30 f8 14*3c 30 f8 14*3c 30 f8 14*3c f8 15*3c f8 15*3c f8 15*3c f8 15*3c
  //   f8 15*3c f8 15*3c f8 15*3c f8 15*3c f8 15*3c f8 15*3c f8 15*3c f8 15*3c f8 15*3c f8 15*3c f8 15*3c
  //   f8 15*3c 30 f8 14*3c 30 f8 14*3c 30 f8 14*3c 30 f8 14*3c f8 15*3c f8 15*3c f8 15*3c f8 15*3c f8
  //   15*3c f8 15*3c f8 15*3c f8 15*3c f8 15*3c f8 15*3c f8 15*3c f8 15*3c f8 15*3c f8 15*3c f8 15*3c f8
  //   15*3c 30 f8 14*3c 30 f8 14*3c 30 f8 14*3c 30 f8 14*3c f8 15*3c f8 15*3c f8 15*3c f8 15*3c f8 15*3c
  //   f8 15*3c f8 15*3c f8 15*3c f8 15*3c f8 15*3c f8 15*3c f8 15*3c 38 15*3c 38 15*3c 30 3c 38 13*3c 30
  //   3c 38 13*3c 30 3c 38 13*3c 30 3c 38 13*3c 30 30 3c 38 12*3c 30 30 3c 38 12*3c 30 30 3c 38 12*3c 30
  //   30 3c 38 15*3c 38 12*3c 30 30 3e 3e 3c 38 12*3c 3e 3e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
  //   contents of EEPROM6 (hex, n*v repeats v):
  //   32*1e 1a 1e 1e 1e 1c 1f 14*1e 1c 1f 106*1e 16 95*1e e 239*1e 16 911*1e e 159*1e 16 2447*1e 1f 15*1e
  //   1f 15*1e 1f 15*1e 1f 4127*1e
endmodule

module AddrDecoder (
  input  [15:0] ABUS,
  output NOT_DEVICE_SEL_ROM,
  output NOT_DEVICE_SEL_RAM,
  output NOT_DEVICE_SEL_0,
  output NOT_DEVICE_SEL_1,
  output NOT_DEVICE_SEL_2,
  output NOT_DEVICE_SEL_3,
  output NOT_DEVICE_SEL_4,
  output NOT_DEVICE_SEL_5
);

  wire decoder_1_out0, decoder_1_out1, decoder_1_out2, decoder_1_out3, decoder_1_out4, decoder_1_out5,
       decoder_1_out6, decoder_1_out7;

  Decoder #(.select(3)) decoder_1 (
    .out0(decoder_1_out0), .out1(decoder_1_out1), .out2(decoder_1_out2), .out3(decoder_1_out3),
    .out4(decoder_1_out4), .out5(decoder_1_out5), .out6(decoder_1_out6), .out7(decoder_1_out7),
    .sel(ABUS[15:13]), .en(1'b1));
  not not_1 (NOT_DEVICE_SEL_ROM, decoder_1_out0);
  not not_2 (NOT_DEVICE_SEL_RAM, decoder_1_out1);
  not not_3 (NOT_DEVICE_SEL_0, decoder_1_out2);
  not not_4 (NOT_DEVICE_SEL_1, decoder_1_out3);
  not not_5 (NOT_DEVICE_SEL_2, decoder_1_out4);
  not not_6 (NOT_DEVICE_SEL_3, decoder_1_out5);
  not not_7 (NOT_DEVICE_SEL_4, decoder_1_out6);
  not not_8 (NOT_DEVICE_SEL_5, decoder_1_out7);
endmodule

module AddressSelector (
  input  [7:0] ABL_in,
  input  [7:0] ABH_in,
  input  [7:0] DS_IN,
  input  [15:0] SS_SP_in,
  input  [15:0] CS_PC_in,
  input  ADDR_SEL0,
  input  ADDR_SEL1,
  input  CSPC_override,
  output [15:0] ADDR_OUT
);

  wire [1:0] or_1_out;

  or or_1 (or_1_out[0], ADDR_SEL0, CSPC_override);
  or or_2 (or_1_out[1], ADDR_SEL1, CSPC_override);
  Multiplexer #(.select(2), .width(16)) multiplexer_1 (
    .in0({ABH_in, ABL_in}), .in1({DS_IN, ABL_in}), .in2(SS_SP_in), .in3(CS_PC_in), .out(ADDR_OUT),
    .sel(or_1_out));

  // Notes on the sheet:
  //   01: DS:ABL
  //   10: SS:SP
  //   11: CS:PC
  //   00: ABH:ABL
endmodule

module FLAGSController (
  input  MODE2,
  input  MODE1,
  input  MODE0,
  input  [3:0] BUS_IN,
  input  [2:0] ALU_IN,
  output NOT_C_IN,
  output NOT_Z_IN,
  output NOT_N_IN,
  output NOT_I_IN,
  output C_VAL,
  output Z_VAL,
  output N_VAL,
  output I_VAL
);

  wire and_1_out, not_1_out, not_3_out, or_3_out, or_4_out, or_5_out, or_6_out, or_7_out, or_8_out, or_9_out,
       or_10_out, or_11_out, or_12_out, or_13_out, or_14_out, or_15_out;

  not not_1 (not_1_out, MODE2);
  not not_2 (NOT_C_IN, MODE1);
  not not_3 (not_3_out, MODE0);
  or or_1 (NOT_Z_IN, MODE2, NOT_C_IN);
  or or_2 (NOT_N_IN, MODE2, NOT_C_IN);
  or or_3 (or_3_out, not_1_out, MODE1);
  or or_4 (or_4_out, MODE2, NOT_C_IN);
  or or_5 (or_5_out, or_4_out, MODE0);
  or or_6 (or_6_out, MODE0, BUS_IN[0]);
  and and_1 (and_1_out, or_6_out, or_7_out);
  or or_7 (or_7_out, not_1_out, MODE0);
  or or_8 (or_8_out, MODE2, not_3_out);
  or or_9 (or_9_out, or_8_out, ALU_IN[0]);
  or or_10 (or_10_out, MODE0, BUS_IN[1]);
  and and_2 (Z_VAL, or_10_out, or_11_out);
  or or_11 (or_11_out, not_3_out, ALU_IN[1]);
  or or_12 (or_12_out, MODE0, BUS_IN[2]);
  and and_3 (N_VAL, or_12_out, or_13_out);
  or or_13 (or_13_out, not_3_out, ALU_IN[2]);
  or or_14 (or_14_out, MODE0, BUS_IN[3]);
  and and_4 (I_VAL, or_14_out, or_15_out);
  or or_15 (or_15_out, MODE1, MODE0);
  and and_5 (NOT_I_IN, or_3_out, or_5_out);
  and and_6 (C_VAL, and_1_out, or_9_out);
endmodule

module TwoPhaseClock (
  input  NOT_HLT,
  output BASE_CLK,
  output PHI1,
  output PHI2,
  output C1,
  output C2,
  output C3,
  output C4
);

  wire and_1_out, j_k_ff_1_q, j_k_ff_2_q, nor_1_out, nor_2_out, not_1_out, not_2_out, not_3_out, not_4_out,
       not_6_out;

  Clock clock_1 (.out(BASE_CLK));
  and and_1 (and_1_out, BASE_CLK, NOT_HLT);
  J_K_Flip_Flop j_k_ff_1 (.J(1'b1), .K(1'b1), .clk(and_1_out), .Q(j_k_ff_1_q));  // open: Qn, preset, reset
  not not_1 (not_1_out, j_k_ff_1_q);
  not not_2 (not_2_out, and_1_out);
  J_K_Flip_Flop j_k_ff_2 (.J(not_1_out), .K(not_1_out), .clk(not_2_out), .Q(j_k_ff_2_q));  // open: Qn, preset, reset
  not not_3 (not_3_out, j_k_ff_2_q);
  and and_2 (C1, j_k_ff_1_q, PHI1);
  and and_3 (C3, j_k_ff_1_q, PHI2);
  nor nor_1 (nor_1_out, not_3_out, PHI2);
  not not_4 (not_4_out, nor_1_out);
  not not_5 (PHI1, not_4_out);
  nor nor_2 (nor_2_out, PHI1, j_k_ff_2_q);
  not not_6 (not_6_out, nor_2_out);
  not not_7 (PHI2, not_6_out);
  not not_8 (C2, C1);
  not not_9 (C4, C3);
endmodule

module DeviceOutputController (
  input  NOT_DEVICE_SEL,
  output NOT_DEVICE_OE
);

  wire undriven;

  or or_1 (NOT_DEVICE_OE, undriven, NOT_DEVICE_SEL);
endmodule

module DeviceOEPhaseSelector (
  input  NOT_DEVICE_OUT,
  input  NOT_FETCH,
  input  PHI1,
  input  PHI2,
  output NOT_DEVICE_OE
);

  wire or_1_out, or_2_out;

  or or_1 (or_1_out, NOT_DEVICE_OUT, PHI1);
  and and_1 (NOT_DEVICE_OE, or_1_out, or_2_out);
  or or_2 (or_2_out, NOT_FETCH, PHI2);
endmodule

module ResetCircuit (
  input  RESET_BTN,
  input  PHASE,
  output RESET_OUT
);

  D_Flip_Flop d_ff_1 (.D(1'b0), .clk(PHASE), .Q(RESET_OUT), .preset(RESET_BTN));  // open: Qn, reset
endmodule

module FLAGSController_v2 (
  input  MODE2,
  input  MODE1,
  input  MODE0,
  input  [3:0] BUS_IN,
  input  [2:0] ALU_IN,
  output NOT_C_IN,
  output NOT_Z_IN,
  output NOT_N_IN,
  output NOT_I_IN,
  output C_VAL,
  output Z_VAL,
  output N_VAL,
  output I_VAL
);

  wire multiplexer_1_out, not_1_out, or_1_out, or_3_out, or_4_out;

  not not_1 (not_1_out, MODE2);
  not not_2 (NOT_C_IN, MODE1);
  // NOT_Gate not_3 has open pins: in=MODE0, out=open
  or or_1 (or_1_out, MODE2, MODE0);
  Multiplexer multiplexer_1 (.in0(BUS_IN[0]), .in1(ALU_IN[0]), .out(multiplexer_1_out), .sel(MODE0));
  Multiplexer multiplexer_2 (.in0(BUS_IN[1]), .in1(ALU_IN[1]), .out(Z_VAL), .sel(MODE0));
  Multiplexer multiplexer_3 (.in0(BUS_IN[2]), .in1(ALU_IN[2]), .out(N_VAL), .sel(MODE0));
  or or_2 (NOT_N_IN, MODE2, NOT_C_IN);
  or or_3 (or_3_out, not_1_out, MODE1);
  or or_4 (or_4_out, or_1_out, NOT_C_IN);
  Multiplexer multiplexer_4 (.in0(multiplexer_1_out), .in1(MODE0), .out(C_VAL), .sel(MODE2));
  and and_1 (NOT_I_IN, or_3_out, or_4_out);
  Multiplexer multiplexer_5 (.in0(BUS_IN[3]), .in1(MODE0), .out(I_VAL), .sel(MODE2));

  assign NOT_Z_IN = NOT_N_IN;
endmodule
