// Logisim project Devices.circ as structural Verilog: 6 circuits, main circuit ButtonAdapter
module ButtonAdapter (
  input  BUTTON_IN,
  input  [7:0] DBUS_IN,
  input  [15:0] ABUS,
  input  NOT_DEVICE_IN,
  input  NOT_DEVICE_OE,
  input  NOT_DEVICE_SEL,
  input  CLK,
  output NOT_IRQ,
  output [7:0] D_BUS_OUT
);

  wire nor_1_out, s_r_ff_1_q;

  nor nor_1 (nor_1_out, NOT_DEVICE_IN, NOT_DEVICE_SEL);
  S_R_Flip_Flop s_r_ff_1 (.S(BUTTON_IN), .R(nor_1_out), .clk(CLK), .Q(s_r_ff_1_q));  // open: reset, Qn, preset
  assign NOT_IRQ = s_r_ff_1_q ? 1'b0 : 1'bz;  // Controlled_Buffer controlled_buffer_1
  assign D_BUS_OUT = {{7{1'b0}}, s_r_ff_1_q};  // Bit_Extender bit_extender_1
endmodule

module HexDisplayAdapter (
  input  [7:0] DBUS_IN,
  input  [15:0] ABUS,
  input  NOT_DEVICE_IN,
  input  NOT_DEVICE_OE,
  input  NOT_DEVICE_SEL,
  input  CLK,
  output [3:0] LSB,
  output [3:0] MSB
);

  wire nor_1_out;

  nor nor_1 (nor_1_out, NOT_DEVICE_IN, NOT_DEVICE_SEL);
  Register register_1 (.D(DBUS_IN), .en(nor_1_out), .clk(CLK), .Q({MSB, LSB}));  // open: clr
endmodule

module TTYAdapter (
  input  K_AVAIL,
  input  [6:0] K_DATA,
  input  [7:0] BUS_IN,
  input  [15:0] ABUS,
  input  NOT_DEVICE_IN,
  input  NOT_DEVICE_OE,
  input  NOT_DEVICE_SEL,
  input  CLK,
  output NOT_IRQ,
  output [7:0] ASYNC_OUT,
  output K_READ_EN,
  output [6:0] TTY_DATA,
  output K_CLEAR,
  output K_CLK,
  output TTY_WE,
  output TTY_CLR
);

  wire and_2_out, and_5_out, comparator_1_eq, comparator_2_eq, comparator_3_eq, comparator_4_lt,
       comparator_5_eq, nor_1_out, not_1_out, or_1_out;
  wire [3:0] bit_extender_4_out;
  wire [7:0] bit_extender_2_out, bit_extender_3_out, rom_1_data;
  wire [12:0] bit_extender_1_out;

  Bit_Extender #(.in_width(16), .out_width(13), .\type ("zero")) bit_extender_1 (.in(ABUS), .out(bit_extender_1_out));
  and and_1 (K_READ_EN, nor_1_out, comparator_2_eq);
  Comparator #(.width(13)) comparator_1 (.a({13{1'b0}}), .b(bit_extender_1_out), .eq(comparator_1_eq));  // open: gt, lt
  Comparator #(.width(13)) comparator_2 (.a(13'h1), .b(bit_extender_1_out), .eq(comparator_2_eq));  // open: gt, lt
  and and_2 (and_2_out, comparator_1_eq, nor_1_out);
  assign bit_extender_2_out = {{1{1'b0}}, K_DATA};  // Bit_Extender bit_extender_2
  or or_1 (or_1_out, NOT_DEVICE_SEL, NOT_DEVICE_IN);
  not not_1 (not_1_out, or_1_out);
  nor nor_1 (nor_1_out, NOT_DEVICE_SEL, NOT_DEVICE_OE);
  assign bit_extender_3_out = {{7{1'b0}}, K_AVAIL};  // Bit_Extender bit_extender_3
  assign ASYNC_OUT = K_READ_EN ? bit_extender_2_out : 8'bz;  // Controlled_Buffer controlled_buffer_1
  assign ASYNC_OUT = and_2_out ? bit_extender_3_out : 8'bz;  // Controlled_Buffer controlled_buffer_2
  and and_3 (K_CLEAR, comparator_3_eq, not_1_out);
  Comparator #(.width(13)) comparator_3 (.a(bit_extender_1_out), .b({13{1'b0}}), .eq(comparator_3_eq));  // open: gt, lt
  Transistor #(.\type ("n")) transistor_1 (.in(1'b0), .out(NOT_IRQ), .gate(K_AVAIL));
  Bit_Extender #(.in_width(13), .out_width(4), .\type ("zero")) bit_extender_4 (
    .in(bit_extender_1_out), .out(bit_extender_4_out));
  Comparator #(.mode("unsigned"), .width(13)) comparator_4 (
    .a(13'h1dff), .b(bit_extender_1_out), .lt(comparator_4_lt));  // open: gt, eq
  Bit_Extender #(.out_width(7), .\type ("zero")) bit_extender_5 (.in(BUS_IN), .out(TTY_DATA));
  Comparator #(.width(13)) comparator_5 (.a(13'h2), .b(bit_extender_1_out), .eq(comparator_5_eq));  // open: gt, lt
  ROM #(.addrWidth(4)) rom_1 (.addr(bit_extender_4_out), .data(rom_1_data));
  and and_4 (TTY_WE, not_1_out, comparator_5_eq);
  assign ASYNC_OUT = and_5_out ? rom_1_data : 8'bz;  // Controlled_Buffer controlled_buffer_3
  and and_5 (and_5_out, nor_1_out, comparator_4_lt);

  assign K_CLK = CLK;
  assign TTY_CLR = 1'b0;

  // Notes on the sheet:
  //   contents of rom_1 (hex, n*v repeats v):
  //   4c 4e 44 49 1 8 0 20 7*0 a5
endmodule

module TTYAdapterOLD (
  input  [7:0] DBUS_IN,
  input  [15:0] ABUS,
  input  NOT_DEVICE_IN,
  input  NOT_DEVICE_OE,
  input  NOT_DEVICE_SEL,
  input  CLK,
  output [6:0] TTY_DATA,
  output TTY_WE,
  output TTY_CLR
);

  wire bit_extender_1_out, nor_1_out, not_1_out;

  Bit_Extender #(.in_width(16), .out_width(1)) bit_extender_1 (.in(ABUS), .out(bit_extender_1_out));
  nor nor_1 (nor_1_out, NOT_DEVICE_IN, NOT_DEVICE_SEL);
  Bit_Extender #(.out_width(7)) bit_extender_2 (.in(DBUS_IN), .out(TTY_DATA));
  and and_1 (TTY_WE, nor_1_out, not_1_out);
  not not_1 (not_1_out, bit_extender_1_out);
  and and_2 (TTY_CLR, bit_extender_1_out, CLK, nor_1_out);
endmodule

module RGBScreenAdapter (
  input  [7:0] DBUS_IN,
  input  [15:0] ABUS,
  input  NOT_DEVICE_IN,
  input  NOT_DEVICE_OE,
  input  NOT_DEVICE_SEL,
  input  CLK,
  output DEVICE_RESET,
  output DEVICE_CLK,
  output DEVICE_WE,
  output [5:0] DEVICE_X,
  output [4:0] DEVICE_Y,
  output [7:0] DEVICE_DATA
);

  wire and_2_out;
  wire [12:0] bit_extender_1_out;

  nor nor_1 (DEVICE_WE, NOT_DEVICE_SEL, NOT_DEVICE_IN);
  and and_1 (DEVICE_RESET, DEVICE_WE, and_2_out);
  and and_2 (and_2_out, DBUS_IN[7], DBUS_IN[6], DBUS_IN[5], DBUS_IN[4], DBUS_IN[3], DBUS_IN[2], DBUS_IN[1], DBUS_IN[0], bit_extender_1_out[12], bit_extender_1_out[11], bit_extender_1_out[10], bit_extender_1_out[9], bit_extender_1_out[8], bit_extender_1_out[7], bit_extender_1_out[6], bit_extender_1_out[5], bit_extender_1_out[4], bit_extender_1_out[3], bit_extender_1_out[2], bit_extender_1_out[1], bit_extender_1_out[0]);
  Bit_Extender #(.in_width(16), .out_width(13)) bit_extender_1 (.in(ABUS), .out(bit_extender_1_out));

  assign DEVICE_CLK = CLK;
  assign DEVICE_DATA = DBUS_IN;
  assign DEVICE_X = ABUS[5:0];
  assign DEVICE_Y = ABUS[12:8];
endmodule

module JoystickAdapter (
  input  [7:0] DBUS_IN,
  input  [15:0] ABUS,
  input  NOT_DEVICE_IN,
  input  NOT_DEVICE_OE,
  input  NOT_DEVICE_SEL,
  input  CLK,
  input  [3:0] JX_IN,
  input  [3:0] JY_IN,
  output [7:0] ASYNC_OUT
);


  assign ASYNC_OUT = {JY_IN, JX_IN};
endmodule
